// Logisim project ITC.circ as structural Verilog
// Carry out
module main (
  input  Carry_in,
  input  [3:0] A,
  input  [3:0] B,
  output [3:0] Sum,
  output Carry_out
);

  wire fulladder_2_bits_1_carry_out, fulladder_2_bits_2_carry_out, fulladder_2_bits_3_carry_out;

  FullAdder_2_bits fulladder_2_bits_1 (
    .A(A[0]), .B(B[0]), .Carry_in(Carry_in), .Sum(Sum[0]), .Carry_out(fulladder_2_bits_1_carry_out));
  FullAdder_2_bits fulladder_2_bits_2 (
    .A(A[1]), .B(B[1]), .Carry_in(fulladder_2_bits_1_carry_out), .Sum(Sum[1]),
    .Carry_out(fulladder_2_bits_2_carry_out));
  FullAdder_2_bits fulladder_2_bits_3 (
    .A(A[2]), .B(B[2]), .Carry_in(fulladder_2_bits_2_carry_out), .Sum(Sum[2]),
    .Carry_out(fulladder_2_bits_3_carry_out));
  FullAdder_2_bits fulladder_2_bits_4 (
    .A(A[3]), .B(B[3]), .Carry_in(fulladder_2_bits_3_carry_out), .Sum(Sum[3]), .Carry_out(Carry_out));
endmodule

module FullAdder_2_bits (
  input  A,
  input  B,
  input  Carry_in,
  output Sum,
  output Carry_out
);

  wire and_1_out, and_2_out, xor_1_out;

  xor xor_1 (xor_1_out, A, B);
  and and_1 (and_1_out, A, B);
  xor xor_2 (Sum, xor_1_out, Carry_in);
  and and_2 (and_2_out, xor_1_out, Carry_in);
  LED led_1 (.in(xor_1_out));
  LED led_2 (.in(and_1_out));
  or or_1 (Carry_out, and_1_out, and_2_out);
  LED led_3 (.in(Sum));
  LED led_4 (.in(Carry_out));
  // Probe on Sum

  // Notes on the sheet:
  //   Intermediate_sum
  //   Carry_one
endmodule

module FullAdder_4_bits (
  input  Carry_in,
  input  [3:0] A,
  input  [3:0] B,
  output [3:0] Sum,
  output [4:0] out_5,
  output Carry_out
);

  wire fulladder_2_bits_1_carry_out, fulladder_2_bits_2_carry_out, fulladder_2_bits_3_carry_out;

  FullAdder_2_bits fulladder_2_bits_1 (
    .A(A[0]), .B(B[0]), .Carry_in(Carry_in), .Sum(out_5[0]), .Carry_out(fulladder_2_bits_1_carry_out));
  FullAdder_2_bits fulladder_2_bits_2 (
    .A(A[1]), .B(B[1]), .Carry_in(fulladder_2_bits_1_carry_out), .Sum(out_5[1]),
    .Carry_out(fulladder_2_bits_2_carry_out));
  FullAdder_2_bits fulladder_2_bits_3 (
    .A(A[2]), .B(B[2]), .Carry_in(fulladder_2_bits_2_carry_out), .Sum(out_5[2]),
    .Carry_out(fulladder_2_bits_3_carry_out));
  FullAdder_2_bits fulladder_2_bits_4 (
    .A(A[3]), .B(B[3]), .Carry_in(fulladder_2_bits_3_carry_out), .Sum(out_5[3]), .Carry_out(Carry_out));

  assign out_5[4] = Carry_out;
  assign Sum = out_5[3:0];
endmodule

module FullAdder_8_bits (
  input  Carry_in,
  input  [7:0] A,
  input  [7:0] B,
  output [7:0] Sum,
  output Carry_out
);

  wire fulladder_4_bits_1_carry_out;

  FullAdder_4_bits fulladder_4_bits_1 (
    .Carry_in(Carry_in), .A(A[3:0]), .B(B[3:0]), .Sum(Sum[3:0]), .Carry_out(fulladder_4_bits_1_carry_out));  // open: out_5
  FullAdder_4_bits fulladder_4_bits_2 (
    .Carry_in(fulladder_4_bits_1_carry_out), .A(A[7:4]), .B(B[7:4]), .Sum(Sum[7:4]), .Carry_out(Carry_out));  // open: out_5
endmodule

module FullAdder_16_bits (
  input  Carry_in,
  input  [15:0] A,
  input  [15:0] B,
  output [15:0] out_4,
  output out_5
);

  wire fulladder_8_bits_1_carry_out;

  // Probe on A
  // Probe on B
  FullAdder_8_bits fulladder_8_bits_1 (
    .Carry_in(Carry_in), .A(A[7:0]), .B(B[7:0]), .Sum(out_4[7:0]), .Carry_out(fulladder_8_bits_1_carry_out));
  FullAdder_8_bits fulladder_8_bits_2 (
    .Carry_in(fulladder_8_bits_1_carry_out), .A(A[15:8]), .B(B[15:8]), .Sum(out_4[15:8]), .Carry_out(out_5));
  // Probe on out_4
endmodule

module FullAdder_32_bits (
  input  in_1,
  input  [31:0] in_2,
  input  [31:0] in_3,
  output [31:0] out_4,
  output out_5
);

  wire fulladder_16_bits_1_out_5;

  FullAdder_16_bits fulladder_16_bits_1 (
    .Carry_in(in_1), .A(in_2[15:0]), .B(in_3[15:0]), .out_4(out_4[15:0]), .out_5(fulladder_16_bits_1_out_5));
  FullAdder_16_bits fulladder_16_bits_2 (
    .Carry_in(fulladder_16_bits_1_out_5), .A(in_2[31:16]), .B(in_3[31:16]), .out_4(out_4[31:16]),
    .out_5(out_5));
endmodule

module FullAdder_64_bits (
  input  in_1,
  input  [63:0] in_2,
  input  [63:0] in_3,
  output [63:0] out_4,
  output out_5
);

  wire fulladder_32_bits_1_out_5;

  FullAdder_32_bits fulladder_32_bits_1 (
    .in_1(in_1), .in_2(in_2[31:0]), .in_3(in_3[31:0]), .out_4(out_4[31:0]), .out_5(fulladder_32_bits_1_out_5));
  FullAdder_32_bits fulladder_32_bits_2 (
    .in_1(fulladder_32_bits_1_out_5), .in_2(in_2[63:32]), .in_3(in_3[63:32]), .out_4(out_4[63:32]),
    .out_5(out_5));
endmodule

module haider_the_genious (
  input  in_1,
  input  in_2,
  input  [7:0] in_3,
  input  [15:0] in_4,
  output [15:0] out_5
);

  wire clock_1_out, counter_1_carry;
  wire [1:0] rom_1_data;
  wire [7:0] counter_1_q, counter_2_q, counter_3_q;
  wire [15:0] adder_1_out, controlled_buffer_1_out, register_1_q, register_2_q;

  Adder #(.width(16)) adder_1 (.a(in_4), .b(controlled_buffer_1_out), .out(adder_1_out));  // open: cin, cout
  Counter counter_1 (
    .load(in_1), .D(in_3), .count(in_2), .Q(counter_1_q), .carry(counter_1_carry), .clk(clock_1_out));  // open: up, clr
  Clock clock_1 (.out(clock_1_out));
  Register #(.width(16)) register_1 (
    .D(adder_1_out), .en(rom_1_data[0]), .clk(clock_1_out), .Q(register_1_q));  // open: clr
  assign controlled_buffer_1_out = rom_1_data[0] ? register_1_q : 16'bz;  // Controlled_Buffer controlled_buffer_1
  Counter counter_2 (.Q(counter_2_q), .clk(clock_1_out));  // open: load, D, count, carry, up, clr
  Register #(.width(16)) register_2 (
    .D(adder_1_out), .en(rom_1_data[1]), .clk(clock_1_out), .Q(register_2_q));  // open: clr
  ROM #(.dataWidth(2)) rom_1 (.addr(counter_2_q), .data(rom_1_data));
  RAM #(.dataWidth(16), .\type ("nonvolatile")) ram_1 (
    .addr(counter_3_q), .clk(clock_1_out), .dout(out_5));  // open: we, oe, din
  Counter counter_3 (.Q(counter_3_q), .clk(clock_1_out));  // open: load, D, count, carry, up, clr
  assign controlled_buffer_1_out = rom_1_data[1] ? register_2_q : 16'bz;  // Controlled_Buffer controlled_buffer_2

  // Notes on the sheet:
  //   contents of rom_1 (hex, n*v repeats v):
  //   1 2 1 2 1 2 1 2
endmodule

module step_A (
  input  in_1,
  output [15:0] out_2,
  output out_3
);

  wire clock_1_out, clock_2_out;
  wire [7:0] counter_1_q;
  wire [15:0] controlled_buffer_1_out, ram_1_dout, ram_2_dout, register_1_q, register_2_q, register_3_q;

  Counter counter_1 (.Q(counter_1_q), .up(in_1), .clk(clock_2_out));  // open: load, D, count, carry, clr
  RAM #(.dataWidth(16), .\type ("nonvolatile")) ram_1 (
    .addr(counter_1_q), .oe(in_1), .clk(clock_2_out), .dout(ram_1_dout));  // open: we, din
  Register #(.width(16)) register_1 (.D(ram_1_dout), .en(in_1), .clk(clock_2_out), .Q(register_1_q));  // open: clr
  Counter counter_2 (.clk(clock_1_out));  // open: load, D, count, Q, carry, up, clr
  Clock clock_1 (.out(clock_1_out));
  Clock clock_2 (.out(clock_2_out));
  FullAdder_16_bits fulladder_16_bits_1 (
    .A(register_1_q), .B(register_2_q), .out_4(out_2), .out_5(out_3));  // open: Carry_in
  RAM #(.dataWidth(16), .\type ("nonvolatile")) ram_2 (
    .addr(counter_1_q), .oe(in_1), .clk(clock_2_out), .dout(ram_2_dout));  // open: we, din
  Register #(.width(16)) register_2 (.D(ram_2_dout), .en(in_1), .clk(clock_2_out), .Q(register_2_q));  // open: clr
  // Probe on out_2
  RAM #(.dataWidth(16)) ram_3 (
    .addr(counter_1_q), .we(in_1), .clk(clock_2_out), .din(controlled_buffer_1_out));  // open: oe, dout
  // Probe on controlled_buffer_1_out
  Register #(.width(16)) register_3 (.D(out_2), .en(in_1), .clk(clock_2_out), .Q(register_3_q));  // open: clr
  // Probe on register_3_q
  assign controlled_buffer_1_out = 1'b1 ? register_3_q : 16'bz;  // Controlled_Buffer controlled_buffer_1

  // Notes on the sheet:
  //   in_1: initial=0x1
endmodule

module step_B (
  input  in_1,
  input  in_2,
  input  in_3,
  input  in_4,
  input  in_5,
  input  in_6,
  input  in_7,
  input  in_8,
  input  in_9,
  input  in_10,
  input  in_11,
  input  in_12
);

  wire clock_1_out, multi_core_adder_1_c1;
  wire [7:0] counter_1_q, counter_2_q;
  wire [15:0] controlled_buffer_1_out, multi_core_adder_1_cl1, multi_core_adder_1_cl2,
       multi_core_adder_1_cl3, multi_core_adder_1_cl4, Ram_A_dout, Ram_B_dout, register_1_q, register_2_q,
       register_3_q, register_4_q, register_5_q, register_6_q, register_7_q, register_8_q, register_9_q,
       register_10_q, register_11_q, register_12_q;

  Counter counter_1 (.Q(counter_1_q), .up(1'b1), .clk(clock_1_out));  // open: load, D, count, carry, clr
  RAM #(.dataWidth(16), .\type ("nonvolatile")) Ram_A (
    .addr(counter_1_q), .clk(clock_1_out), .dout(Ram_A_dout));  // open: we, oe, din
  RAM #(.dataWidth(16), .\type ("nonvolatile")) Ram_B (
    .addr(counter_1_q), .clk(clock_1_out), .dout(Ram_B_dout));  // open: we, oe, din
  Register #(.width(16)) register_1 (.D(Ram_A_dout), .en(in_4), .clk(clock_1_out), .Q(register_1_q));  // open: clr
  Register #(.width(16)) register_2 (.D(Ram_A_dout), .en(in_3), .clk(clock_1_out), .Q(register_2_q));  // open: clr
  Register #(.width(16)) register_3 (.D(Ram_A_dout), .en(in_2), .clk(clock_1_out), .Q(register_3_q));  // open: clr
  Register #(.width(16)) register_4 (.D(Ram_A_dout), .en(in_1), .clk(clock_1_out), .Q(register_4_q));  // open: clr
  Register #(.width(16)) register_5 (.D(Ram_B_dout), .en(in_4), .clk(clock_1_out), .Q(register_5_q));  // open: clr
  Register #(.width(16)) register_6 (.D(Ram_B_dout), .en(in_3), .clk(clock_1_out), .Q(register_6_q));  // open: clr
  Register #(.width(16)) register_7 (.D(Ram_B_dout), .en(in_2), .clk(clock_1_out), .Q(register_7_q));  // open: clr
  Register #(.width(16)) register_8 (.D(Ram_B_dout), .en(in_1), .clk(clock_1_out), .Q(register_8_q));  // open: clr
  Counter counter_2 (.Q(counter_2_q), .up(1'b1), .clk(clock_1_out));  // open: load, D, count, carry, clr
  Clock clock_1 (.out(clock_1_out));
  Multi_core_adder multi_core_adder_1 (
    .A1(register_1_q), .A2(register_2_q), .A3(register_3_q), .A4(register_4_q), .B1(register_5_q),
    .B2(register_6_q), .B3(register_7_q), .B4(register_8_q), .Cl1(multi_core_adder_1_cl1),
    .Cl2(multi_core_adder_1_cl2), .Cl3(multi_core_adder_1_cl3), .Cl4(multi_core_adder_1_cl4),
    .C1(multi_core_adder_1_c1), .C2(multi_core_adder_1_c1), .C4(multi_core_adder_1_c1),
    .C3(multi_core_adder_1_c1));
  Register #(.width(16)) register_9 (
    .D(multi_core_adder_1_cl1), .en(in_8), .clk(clock_1_out), .Q(register_9_q));  // open: clr
  Register #(.width(16)) register_10 (
    .D(multi_core_adder_1_cl2), .en(in_7), .clk(clock_1_out), .Q(register_10_q));  // open: clr
  Register #(.width(16)) register_11 (
    .D(multi_core_adder_1_cl3), .en(in_6), .clk(clock_1_out), .Q(register_11_q));  // open: clr
  Register #(.width(16)) register_12 (
    .D(multi_core_adder_1_cl4), .en(in_5), .clk(clock_1_out), .Q(register_12_q));  // open: clr
  RAM #(.dataWidth(16)) ram_1 (
    .addr(counter_2_q), .we(1'b1), .clk(clock_1_out), .din(controlled_buffer_1_out));  // open: oe, dout
  assign controlled_buffer_1_out = in_12 ? register_9_q : 16'bz;  // Controlled_Buffer controlled_buffer_1
  assign controlled_buffer_1_out = in_11 ? register_10_q : 16'bz;  // Controlled_Buffer controlled_buffer_2
  assign controlled_buffer_1_out = in_10 ? register_11_q : 16'bz;  // Controlled_Buffer controlled_buffer_3
  assign controlled_buffer_1_out = in_9 ? register_12_q : 16'bz;  // Controlled_Buffer controlled_buffer_4
endmodule

module Multi_core_adder (
  input  [15:0] A1,
  input  [15:0] A2,
  input  [15:0] A3,
  input  [15:0] A4,
  input  [15:0] B1,
  input  [15:0] B2,
  input  [15:0] B3,
  input  [15:0] B4,
  output [15:0] Cl1,
  output [15:0] Cl2,
  output [15:0] Cl3,
  output [15:0] Cl4,
  output C1,
  output C2,
  output C4,
  output C3
);

  FullAdder_16_bits fulladder_16_bits_1 (.A(A1), .B(B1), .out_4(Cl1), .out_5(C1));  // open: Carry_in
  FullAdder_16_bits fulladder_16_bits_2 (.A(A2), .B(B2), .out_4(Cl2), .out_5(C2));  // open: Carry_in
  FullAdder_16_bits fulladder_16_bits_3 (.A(A3), .B(B3), .out_4(Cl3), .out_5(C4));  // open: Carry_in
  FullAdder_16_bits fulladder_16_bits_4 (.A(A4), .B(B4), .out_4(Cl4), .out_5(C3));  // open: Carry_in
endmodule

module step_C (
);

  wire clock_1_out, multi_core_adder_1_c1, or_1_out;
  wire [7:0] counter_1_q, counter_2_q;
  wire [15:0] controlled_buffer_1_out, multi_core_adder_1_cl1, multi_core_adder_1_cl2,
       multi_core_adder_1_cl3, multi_core_adder_1_cl4, Ram_A_dout, Ram_B_dout, register_1_q, register_2_q,
       register_3_q, register_4_q, register_5_q, register_6_q, register_7_q, register_8_q, register_9_q,
       register_10_q, register_11_q, register_12_q, rom_1_data;

  Counter counter_1 (.Q(counter_1_q), .up(1'b1), .clk(clock_1_out));  // open: load, D, count, carry, clr
  RAM #(.dataWidth(16), .\type ("nonvolatile")) Ram_A (
    .addr(counter_1_q), .clk(clock_1_out), .dout(Ram_A_dout));  // open: we, oe, din
  RAM #(.dataWidth(16), .\type ("nonvolatile")) Ram_B (
    .addr(counter_1_q), .clk(clock_1_out), .dout(Ram_B_dout));  // open: we, oe, din
  _7_Segment_Display u_7_segment_display_1 ();  // open: g, f, a, b, e, d, c, dp
  _7_Segment_Display u_7_segment_display_2 ();  // open: g, f, a, b, e, d, c, dp
  Register #(.width(16)) register_1 (
    .D(Ram_A_dout), .en(rom_1_data[0]), .clk(clock_1_out), .Q(register_1_q));  // open: clr
  Register #(.width(16)) register_2 (
    .D(Ram_A_dout), .en(rom_1_data[1]), .clk(clock_1_out), .Q(register_2_q));  // open: clr
  Register #(.width(16)) register_3 (
    .D(Ram_A_dout), .en(rom_1_data[2]), .clk(clock_1_out), .Q(register_3_q));  // open: clr
  Register #(.width(16)) register_4 (
    .D(Ram_A_dout), .en(rom_1_data[3]), .clk(clock_1_out), .Q(register_4_q));  // open: clr
  Register #(.width(16)) register_5 (
    .D(Ram_B_dout), .en(rom_1_data[0]), .clk(clock_1_out), .Q(register_5_q));  // open: clr
  Register #(.width(16)) register_6 (
    .D(Ram_B_dout), .en(rom_1_data[1]), .clk(clock_1_out), .Q(register_6_q));  // open: clr
  Register #(.width(16)) register_7 (
    .D(Ram_B_dout), .en(rom_1_data[2]), .clk(clock_1_out), .Q(register_7_q));  // open: clr
  Register #(.width(16)) register_8 (
    .D(Ram_B_dout), .en(rom_1_data[3]), .clk(clock_1_out), .Q(register_8_q));  // open: clr
  ROM #(.dataWidth(16)) rom_1 (.addr(counter_1_q), .data(rom_1_data));
  Clock clock_1 (.out(clock_1_out));
  Multi_core_adder multi_core_adder_1 (
    .A1(register_1_q), .A2(register_2_q), .A3(register_3_q), .A4(register_4_q), .B1(register_5_q),
    .B2(register_6_q), .B3(register_7_q), .B4(register_8_q), .Cl1(multi_core_adder_1_cl1),
    .Cl2(multi_core_adder_1_cl2), .Cl3(multi_core_adder_1_cl3), .Cl4(multi_core_adder_1_cl4),
    .C1(multi_core_adder_1_c1), .C2(multi_core_adder_1_c1), .C4(multi_core_adder_1_c1),
    .C3(multi_core_adder_1_c1));
  Register #(.width(16)) register_9 (
    .D(multi_core_adder_1_cl1), .en(rom_1_data[1]), .clk(clock_1_out), .Q(register_9_q));  // open: clr
  Register #(.width(16)) register_10 (
    .D(multi_core_adder_1_cl2), .en(rom_1_data[2]), .clk(clock_1_out), .Q(register_10_q));  // open: clr
  Register #(.width(16)) register_11 (
    .D(multi_core_adder_1_cl3), .en(rom_1_data[3]), .clk(clock_1_out), .Q(register_11_q));  // open: clr
  Register #(.width(16)) register_12 (
    .D(multi_core_adder_1_cl4), .en(rom_1_data[0]), .clk(clock_1_out), .Q(register_12_q));  // open: clr
  or or_1 (or_1_out, rom_1_data[7], rom_1_data[6], rom_1_data[5], rom_1_data[4]);
  RAM #(.dataWidth(16)) ram_1 (
    .addr(counter_2_q), .we(1'b1), .clk(clock_1_out), .din(controlled_buffer_1_out));  // open: oe, dout
  Counter counter_2 (.count(or_1_out), .Q(counter_2_q), .up(1'b1), .clk(clock_1_out));  // open: load, D, carry, clr
  assign controlled_buffer_1_out = rom_1_data[4] ? register_9_q : 16'bz;  // Controlled_Buffer controlled_buffer_1
  assign controlled_buffer_1_out = rom_1_data[5] ? register_10_q : 16'bz;  // Controlled_Buffer controlled_buffer_2
  assign controlled_buffer_1_out = rom_1_data[6] ? register_11_q : 16'bz;  // Controlled_Buffer controlled_buffer_3
  assign controlled_buffer_1_out = rom_1_data[7] ? register_12_q : 16'bz;  // Controlled_Buffer controlled_buffer_4

  // Notes on the sheet:
  //   contents of rom_1 (hex, n*v repeats v):
  //   0 1 2 14 28 41 82 14 28 41 82 14 28 41 82 14 28 41 82 14 28 41 82 14 28 41 82 14 28 41 82
endmodule

module step_4 (
);

  wire clock_1_out, or_1_out, or_2_out, or_3_out;
  wire [3:0] counter_3_q, counter_3_q_2;
  wire [7:0] counter_1_q, counter_2_q, counter_4_q;
  wire [15:0] matrix_multiplier_1_cl1, ram_1_dout, Ram_A_dout, register_1_q, register_2_q, register_3_q,
       register_4_q, register_5_q, register_6_q, register_7_q, register_8_q, register_9_q, rom_1_data;

  Counter counter_1 (.count(or_2_out), .Q(counter_1_q), .up(1'b1), .clk(clock_1_out));  // open: load, D, carry, clr
  Counter #(.max('h10)) counter_2 (
    .count(or_1_out), .Q(counter_2_q), .up(1'b1), .clk(clock_1_out));  // open: load, D, carry, clr
  or or_1 (or_1_out, rom_1_data[0], rom_1_data[9], rom_1_data[10], rom_1_data[11]);
  or or_2 (or_2_out, rom_1_data[15], rom_1_data[13], rom_1_data[14]);
  RAM #(.dataWidth(16), .\type ("nonvolatile")) Ram_A (
    .addr(counter_1_q), .oe(or_2_out), .clk(clock_1_out), .dout(Ram_A_dout));  // open: we, din
  RAM #(.dataWidth(16), .\type ("nonvolatile")) ram_1 (
    .addr(counter_2_q), .clk(clock_1_out), .dout(ram_1_dout));  // open: we, oe, din
  or or_3 (or_3_out, rom_1_data[0], rom_1_data[1], rom_1_data[2], rom_1_data[3], rom_1_data[4], rom_1_data[5], rom_1_data[6], rom_1_data[7], rom_1_data[9], rom_1_data[10], rom_1_data[11], rom_1_data[12], rom_1_data[13], rom_1_data[14], rom_1_data[15], rom_1_data[8]);
  Register #(.width(16)) register_1 (
    .D(Ram_A_dout), .en(rom_1_data[15]), .clk(clock_1_out), .Q(register_1_q));  // open: clr
  Register #(.width(16)) register_2 (
    .D(Ram_A_dout), .en(rom_1_data[14]), .clk(clock_1_out), .Q(register_2_q));  // open: clr
  Register #(.width(16)) register_3 (
    .D(Ram_A_dout), .en(rom_1_data[13]), .clk(clock_1_out), .Q(register_3_q));  // open: clr
  Register #(.width(16)) register_4 (
    .D(Ram_A_dout), .en(rom_1_data[12]), .clk(clock_1_out), .Q(register_4_q));  // open: clr
  Register #(.width(16)) register_5 (
    .D(ram_1_dout), .en(rom_1_data[11]), .clk(clock_1_out), .Q(register_5_q));  // open: clr
  Register #(.width(16)) register_6 (
    .D(ram_1_dout), .en(rom_1_data[10]), .clk(clock_1_out), .Q(register_6_q));  // open: clr
  Register #(.width(16)) register_7 (
    .D(ram_1_dout), .en(rom_1_data[9]), .clk(clock_1_out), .Q(register_7_q));  // open: clr
  Register #(.width(16)) register_8 (
    .D(ram_1_dout), .en(rom_1_data[8]), .clk(clock_1_out), .Q(register_8_q));  // open: clr
  Counter counter_3 (
    .count(or_3_out), .Q({counter_3_q_2, counter_3_q}), .up(1'b1), .clk(clock_1_out));  // open: load, D, carry, clr
  ROM #(.dataWidth(16)) rom_1 (.addr({counter_3_q_2, counter_3_q}), .data(rom_1_data));
  Clock clock_1 (.out(clock_1_out));
  matrix_multiplier matrix_multiplier_1 (
    .A1(register_1_q), .A2(register_2_q), .A3(register_3_q), .A4(register_4_q), .B1(register_5_q),
    .B2(register_6_q), .B3(register_7_q), .B4(register_8_q), .Cl1(matrix_multiplier_1_cl1));
  Register #(.width(16)) register_9 (
    .D(matrix_multiplier_1_cl1), .en(rom_1_data[7]), .clk(clock_1_out), .Q(register_9_q));  // open: clr
  Hex_Digit_Display hex_digit_display_1 (.value(counter_3_q_2));  // open: dp
  RAM #(.dataWidth(16)) ram_2 (
    .addr(counter_4_q), .we(rom_1_data[3]), .clk(clock_1_out), .din(register_9_q));  // open: oe, dout
  Counter counter_4 (
    .count(rom_1_data[3]), .Q(counter_4_q), .up(1'b1), .clk(clock_1_out));  // open: load, D, carry, clr
  RAM #(.dataWidth(16), .\type ("nonvolatile")) ram_3 (.addr(counter_4_q));  // open: we, oe, clk, din, dout
  Hex_Digit_Display hex_digit_display_2 (.value(counter_3_q));  // open: dp
  // Probe on {counter_3_q_2, counter_3_q}

  // Notes on the sheet:
  //   contents of rom_1 (hex, n*v repeats v):
  //   8800 8800 4400 2200 1101 880 408 200 101 880 408 200 101 880 408 200 101 880 808 8400 8200 4100 2000
  //   1000 80 808 800 400 200 100 880 808 400 200 100 880 808 400 200 101 8880 8808 4400 2200 1100 880 808
  //   400 200 100 880 808 400 200 100 880 808 400 200 101 8880 8808 4400 2200 1100 880 808 400 200 100 880
  //   808 400 200 100 880 808 400 200 100 80 8
endmodule

module multicore_adder2 (
  input  Ci1,
  input  Ci2,
  input  Ci3,
  input  Ci4,
  input  [15:0] A1,
  input  [15:0] A2,
  input  [15:0] A3,
  input  [15:0] A4,
  input  [15:0] B1,
  input  [15:0] B2,
  input  [15:0] B3,
  input  [15:0] B4,
  output [15:0] S1,
  output [15:0] S2,
  output [15:0] S3,
  output [15:0] S4,
  output Co1,
  output Co2,
  output Co3,
  output Co4
);

  FullAdder_16_bits fulladder_16_bits_1 (.Carry_in(Ci1), .A(A1), .B(B1), .out_4(S1), .out_5(Co1));
  FullAdder_16_bits fulladder_16_bits_2 (.Carry_in(Ci2), .A(A2), .B(B2), .out_4(S2), .out_5(Co2));
  FullAdder_16_bits fulladder_16_bits_3 (.Carry_in(Ci3), .A(A3), .B(B3), .out_4(S3), .out_5(Co3));
  FullAdder_16_bits fulladder_16_bits_4 (.Carry_in(Ci4), .A(A4), .B(B4), .out_4(S4), .out_5(Co4));
endmodule

module Multi_core_64_adder (
  input  Ci1,
  input  Ci2,
  input  Ci3,
  input  Ci4,
  input  [63:0] A1,
  input  [63:0] A2,
  input  [63:0] A3,
  input  [63:0] A4,
  input  [63:0] B1,
  input  [63:0] B2,
  input  [63:0] B3,
  input  [63:0] B4,
  output [63:0] S1,
  output [63:0] S2,
  output [63:0] S3,
  output [63:0] S4,
  output Co1,
  output Co2,
  output Co3,
  output Co4
);

  FullAdder_64_bits fulladder_64_bits_1 (.in_1(Ci1), .in_2(A1), .in_3(B1), .out_4(S1), .out_5(Co1));
  FullAdder_64_bits fulladder_64_bits_2 (.in_1(Ci2), .in_2(A2), .in_3(B2), .out_4(S2), .out_5(Co2));
  FullAdder_64_bits fulladder_64_bits_3 (.in_1(Ci3), .in_2(A3), .in_3(B3), .out_4(S3), .out_5(Co3));
  FullAdder_64_bits fulladder_64_bits_4 (.in_1(Ci4), .in_2(A4), .in_3(B4), .out_4(S4), .out_5(Co4));
endmodule

module matrix_multiplier (
  input  [15:0] A1,
  input  [15:0] A2,
  input  [15:0] A3,
  input  [15:0] A4,
  input  [15:0] B1,
  input  [15:0] B2,
  input  [15:0] B3,
  input  [15:0] B4,
  output [15:0] Cl1
);

  wire [15:0] adder_1_out, adder_2_out, multiplier_1_out, multiplier_2_out, multiplier_3_out,
       multiplier_4_out;

  Multiplier #(.width(16)) multiplier_1 (.a(A1), .b(B1), .out(multiplier_1_out));  // open: cin, cout
  Multiplier #(.width(16)) multiplier_2 (.a(A2), .b(B2), .out(multiplier_2_out));  // open: cin, cout
  Multiplier #(.width(16)) multiplier_3 (.a(A3), .b(B3), .out(multiplier_3_out));  // open: cin, cout
  Multiplier #(.width(16)) multiplier_4 (.a(A4), .b(B4), .out(multiplier_4_out));  // open: cin, cout
  Adder #(.width(16)) adder_1 (.a(multiplier_1_out), .b(multiplier_2_out), .out(adder_1_out));  // open: cin, cout
  Adder #(.width(16)) adder_2 (.a(multiplier_3_out), .b(multiplier_4_out), .out(adder_2_out));  // open: cin, cout
  Adder #(.width(16)) adder_3 (.a(adder_1_out), .b(adder_2_out), .out(Cl1));  // open: cin, cout
endmodule

module efficent_MMuld (
);

  wire clock_1_out, or_1_out, or_2_out, or_3_out;
  wire [3:0] counter_3_q, counter_3_q_2;
  wire [7:0] counter_1_q, counter_2_q, counter_4_q;
  wire [15:0] matrix_multiplier_1_cl1, ram_1_dout, Ram_A_dout, register_1_q, register_2_q, register_3_q,
       register_4_q, register_5_q, register_6_q, register_7_q, register_8_q, register_9_q, rom_1_data;

  Counter counter_1 (.count(or_2_out), .Q(counter_1_q), .up(1'b1), .clk(clock_1_out));  // open: load, D, carry, clr
  Counter #(.max('hf)) counter_2 (
    .count(or_1_out), .Q(counter_2_q), .up(1'b1), .clk(clock_1_out));  // open: load, D, carry, clr
  or or_1 (or_1_out, rom_1_data[8], rom_1_data[9], rom_1_data[10], rom_1_data[11]);
  or or_2 (or_2_out, rom_1_data[12], rom_1_data[15], rom_1_data[13], rom_1_data[14]);
  RAM #(.dataWidth(16), .\type ("nonvolatile")) Ram_A (
    .addr(counter_1_q), .oe(or_2_out), .clk(clock_1_out), .dout(Ram_A_dout));  // open: we, din
  RAM #(.dataWidth(16), .\type ("nonvolatile")) ram_1 (
    .addr(counter_2_q), .oe(or_1_out), .clk(clock_1_out), .dout(ram_1_dout));  // open: we, din
  or or_3 (or_3_out, rom_1_data[0], rom_1_data[1], rom_1_data[2], rom_1_data[3], rom_1_data[4], rom_1_data[5], rom_1_data[6], rom_1_data[7], rom_1_data[9], rom_1_data[10], rom_1_data[11], rom_1_data[12], rom_1_data[13], rom_1_data[14], rom_1_data[15], rom_1_data[8]);
  Register #(.width(16)) register_1 (
    .D(Ram_A_dout), .en(rom_1_data[15]), .clk(clock_1_out), .Q(register_1_q));  // open: clr
  Register #(.width(16)) register_2 (
    .D(Ram_A_dout), .en(rom_1_data[14]), .clk(clock_1_out), .Q(register_2_q));  // open: clr
  Register #(.width(16)) register_3 (
    .D(Ram_A_dout), .en(rom_1_data[13]), .clk(clock_1_out), .Q(register_3_q));  // open: clr
  Register #(.width(16)) register_4 (
    .D(Ram_A_dout), .en(rom_1_data[12]), .clk(clock_1_out), .Q(register_4_q));  // open: clr
  Register #(.width(16)) register_5 (
    .D(ram_1_dout), .en(rom_1_data[11]), .clk(clock_1_out), .Q(register_5_q));  // open: clr
  Register #(.width(16)) register_6 (
    .D(ram_1_dout), .en(rom_1_data[10]), .clk(clock_1_out), .Q(register_6_q));  // open: clr
  Register #(.width(16)) register_7 (
    .D(ram_1_dout), .en(rom_1_data[9]), .clk(clock_1_out), .Q(register_7_q));  // open: clr
  Register #(.width(16)) register_8 (
    .D(ram_1_dout), .en(rom_1_data[8]), .clk(clock_1_out), .Q(register_8_q));  // open: clr
  Counter counter_3 (
    .count(or_3_out), .Q({counter_3_q_2, counter_3_q}), .up(1'b1), .clk(clock_1_out));  // open: load, D, carry, clr
  ROM #(.dataWidth(16)) rom_1 (.addr({counter_3_q_2, counter_3_q}), .data(rom_1_data));
  Clock clock_1 (.out(clock_1_out));
  matrix_multiplier matrix_multiplier_1 (
    .A1(register_1_q), .A2(register_2_q), .A3(register_3_q), .A4(register_4_q), .B1(register_5_q),
    .B2(register_6_q), .B3(register_7_q), .B4(register_8_q), .Cl1(matrix_multiplier_1_cl1));
  Register #(.width(16)) register_9 (
    .D(matrix_multiplier_1_cl1), .en(rom_1_data[7]), .clk(clock_1_out), .Q(register_9_q));  // open: clr
  Hex_Digit_Display hex_digit_display_1 (.value(counter_3_q_2));  // open: dp
  RAM #(.dataWidth(16)) ram_2 (
    .addr(counter_4_q), .we(rom_1_data[3]), .clk(clock_1_out), .din(register_9_q));  // open: oe, dout
  Counter counter_4 (
    .count(rom_1_data[3]), .Q(counter_4_q), .up(1'b1), .clk(clock_1_out));  // open: load, D, carry, clr
  RAM #(.dataWidth(16), .\type ("nonvolatile")) ram_3 (.addr(counter_4_q));  // open: we, oe, clk, din, dout
  Hex_Digit_Display hex_digit_display_2 (.value(counter_3_q));  // open: dp
  // Probe on {counter_3_q_2, counter_3_q}

  // Notes on the sheet:
  //   contents of rom_1 (hex, n*v repeats v):
  //   8800 8800 4400 2200 1100 880 408 200 100 880 408 200 100 880 408 200 100 8880 4408 2200 1100 880 408
  //   200 100 880 408 200 100 880 408 200 100 8880 4408 2200 1100 880 408 200 100 880 408 200 100 880 408
  //   200 100 8880 4408 2200 1100 880 408 200 100 880 408 200 100 880 408 200 100 80 8
endmodule

module more_efficent_MMult (
);

  wire clock_1_out, undriven, undriven_2, undriven_3, undriven_4, undriven_5, undriven_6, undriven_7,
       undriven_8, undriven_9, undriven_10, undriven_11, undriven_12, undriven_13, undriven_14, undriven_15,
       undriven_16, undriven_17, undriven_18, undriven_19, undriven_20, undriven_21, undriven_22,
       undriven_23, undriven_24, undriven_25, undriven_26, undriven_27, undriven_28, undriven_29,
       undriven_30, undriven_31, undriven_32, undriven_33, undriven_34, undriven_35, undriven_36,
       undriven_37, undriven_38, undriven_39, undriven_40, undriven_41, undriven_42, undriven_43,
       undriven_44, undriven_45, undriven_46, undriven_48;
  wire [7:0] counter_1_q, counter_2_q, counter_3_q, counter_4_q;
  wire [15:0] ram_1_dout, ram_2_dout, ram_3_dout, ram_4_dout, ram_5_dout, ram_6_dout, ram_7_dout, ram_8_dout,
       register_1_q, register_5_q, register_9_q, register_33_q, rom_1_data, undriven_47;

  Counter #(.max('h3)) counter_1 (
    .count(undriven), .Q(counter_1_q), .up(1'b1), .clk(undriven_2));  // open: load, D, carry, clr
  Counter #(.max('h3)) counter_2 (
    .count(undriven_3), .Q(counter_2_q), .up(1'b1), .clk(undriven_2));  // open: load, D, carry, clr
  RAM #(.dataWidth(16), .\type ("nonvolatile")) ram_1 (
    .addr(counter_1_q), .oe(undriven), .clk(undriven_2), .dout(ram_1_dout));  // open: we, din
  RAM #(.dataWidth(16), .\type ("nonvolatile")) ram_2 (
    .addr(counter_1_q), .oe(undriven), .clk(undriven_2), .dout(ram_2_dout));  // open: we, din
  RAM #(.dataWidth(16), .\type ("nonvolatile")) ram_3 (
    .addr(counter_1_q), .oe(undriven), .clk(undriven_2), .dout(ram_3_dout));  // open: we, din
  RAM #(.dataWidth(16), .\type ("nonvolatile")) ram_4 (
    .addr(counter_1_q), .oe(undriven), .clk(undriven_2), .dout(ram_4_dout));  // open: we, din
  RAM #(.dataWidth(16), .\type ("nonvolatile")) ram_5 (
    .addr(counter_2_q), .oe(undriven_3), .clk(undriven_2), .dout(ram_5_dout));  // open: we, din
  RAM #(.dataWidth(16), .\type ("nonvolatile")) ram_6 (
    .addr(counter_2_q), .oe(undriven_3), .clk(undriven_2), .dout(ram_6_dout));  // open: we, din
  RAM #(.dataWidth(16), .\type ("nonvolatile")) ram_7 (
    .addr(counter_2_q), .oe(undriven_3), .clk(undriven_2), .dout(ram_7_dout));  // open: we, din
  RAM #(.dataWidth(16), .\type ("nonvolatile")) ram_8 (
    .addr(counter_2_q), .oe(undriven_3), .clk(undriven_2), .dout(ram_8_dout));  // open: we, din
  Register #(.width(16)) register_1 (.D(ram_1_dout), .en(undriven_4), .clk(undriven_5), .Q(register_1_q));  // open: clr
  Register #(.width(16)) register_2 (.D(ram_2_dout), .en(undriven_4), .clk(undriven_6));  // open: Q, clr
  Register #(.width(16)) register_3 (.D(ram_3_dout), .en(undriven_4), .clk(undriven_7));  // open: Q, clr
  Register #(.width(16)) register_4 (.D(ram_4_dout), .en(undriven_4), .clk(undriven_8));  // open: Q, clr
  Register #(.width(16)) register_5 (
    .D(ram_1_dout), .en(undriven_9), .clk(undriven_10), .Q(register_5_q));  // open: clr
  Register #(.width(16)) register_6 (.D(ram_2_dout), .en(undriven_9), .clk(undriven_11));  // open: Q, clr
  Register #(.width(16)) register_7 (.D(ram_3_dout), .en(undriven_9), .clk(undriven_12));  // open: Q, clr
  Register #(.width(16)) register_8 (.D(ram_4_dout), .en(undriven_9), .clk(undriven_13));  // open: Q, clr
  Register #(.width(16)) register_9 (
    .D(ram_1_dout), .en(undriven_14), .clk(undriven_15), .Q(register_9_q));  // open: clr
  Register #(.width(16)) register_10 (.D(ram_2_dout), .en(undriven_14), .clk(undriven_16));  // open: Q, clr
  Register #(.width(16)) register_11 (.D(ram_3_dout), .en(undriven_14), .clk(undriven_17));  // open: Q, clr
  Register #(.width(16)) register_12 (.D(ram_4_dout), .en(undriven_14), .clk(undriven_18));  // open: Q, clr
  Register #(.width(16)) register_13 (.D(ram_1_dout), .en(undriven_19), .clk(undriven_20));  // open: Q, clr
  Register #(.width(16)) register_14 (.D(ram_2_dout), .en(undriven_19), .clk(undriven_21));  // open: Q, clr
  Register #(.width(16)) register_15 (.D(ram_3_dout), .en(undriven_19), .clk(undriven_22));  // open: Q, clr
  Register #(.width(16)) register_16 (.D(ram_4_dout), .en(undriven_19), .clk(undriven_23));  // open: Q, clr
  Register #(.width(16)) register_17 (.D(ram_5_dout), .en(undriven_24), .clk(undriven_25));  // open: Q, clr
  Register #(.width(16)) register_18 (.D(ram_6_dout), .en(undriven_24), .clk(undriven_26));  // open: Q, clr
  Register #(.width(16)) register_19 (.D(ram_7_dout), .en(undriven_24), .clk(undriven_27));  // open: Q, clr
  Register #(.width(16)) register_20 (.D(ram_8_dout), .en(undriven_24), .clk(undriven_28));  // open: Q, clr
  Register #(.width(16)) register_21 (.D(ram_5_dout), .en(undriven_29), .clk(undriven_30));  // open: Q, clr
  Register #(.width(16)) register_22 (.D(ram_6_dout), .en(undriven_29), .clk(undriven_31));  // open: Q, clr
  Register #(.width(16)) register_23 (.D(ram_7_dout), .en(undriven_29), .clk(undriven_32));  // open: Q, clr
  Register #(.width(16)) register_24 (.D(ram_8_dout), .en(undriven_29), .clk(undriven_33));  // open: Q, clr
  Register #(.width(16)) register_25 (.D(ram_5_dout), .en(undriven_34), .clk(undriven_35));  // open: Q, clr
  Register #(.width(16)) register_26 (.D(ram_6_dout), .en(undriven_34), .clk(undriven_36));  // open: Q, clr
  Register #(.width(16)) register_27 (.D(ram_7_dout), .en(undriven_34), .clk(undriven_37));  // open: Q, clr
  Register #(.width(16)) register_28 (.D(ram_8_dout), .en(undriven_34), .clk(undriven_38));  // open: Q, clr
  matrix_multiplier matrix_multiplier_1 (.A1(register_1_q), .A2(register_5_q));  // open: A3, A4, B1, B2, B3, B4, Cl1
  Register #(.width(16)) register_29 (.D(ram_5_dout), .en(undriven_39), .clk(undriven_40));  // open: Q, clr
  Register #(.width(16)) register_30 (.D(ram_6_dout), .en(undriven_39), .clk(undriven_41));  // open: Q, clr
  Register #(.width(16)) register_31 (.D(ram_7_dout), .en(undriven_39), .clk(undriven_42));  // open: Q, clr
  Register #(.width(16)) register_32 (.D(ram_8_dout), .en(undriven_39), .clk(undriven_43));  // open: Q, clr
  RAM #(.dataWidth(16), .\type ("nonvolatile")) ram_9 ();  // open: addr, we, oe, clk, din, dout
  RAM #(.dataWidth(16), .\type ("nonvolatile")) ram_10 ();  // open: addr, we, oe, clk, din, dout
  // OR_Gate or_1 has open pins: in0=rom_1_data[0], in1=rom_1_data[1], in2=rom_1_data[2], in3=rom_1_data[3], in4=rom_1_data[4], in5=rom_1_data[5], in6=rom_1_data[6], in7=rom_1_data[7], in8=rom_1_data[9], in9=rom_1_data[10], in10=rom_1_data[11], in11=rom_1_data[12], in12=rom_1_data[13], in13=rom_1_data[14], in14=rom_1_data[15], in15=rom_1_data[8], out=open
  Counter counter_3 (.count(undriven_44), .Q(counter_3_q), .clk(undriven_46));  // open: load, D, carry, up, clr
  Clock clock_1 (.out(clock_1_out));
  ROM #(.dataWidth(16)) rom_1 (.addr(counter_3_q), .data(rom_1_data));
  Register #(.width(16)) register_33 (
    .D(undriven_47), .en(undriven_45), .clk(clock_1_out), .Q(register_33_q));  // open: clr
  Hex_Digit_Display hex_digit_display_1 (.value(counter_3_q[7:4]));  // open: dp
  Counter counter_4 (.count(undriven_48), .Q(counter_4_q), .up(1'b1), .clk(clock_1_out));  // open: load, D, carry, clr
  Hex_Digit_Display hex_digit_display_2 (.value(counter_3_q[3:0]));  // open: dp
  RAM #(.dataWidth(16)) ram_11 (
    .addr(counter_4_q), .we(undriven_48), .clk(clock_1_out), .din(register_33_q));  // open: oe, dout
  RAM #(.dataWidth(16), .\type ("nonvolatile")) ram_12 (.addr(counter_4_q));  // open: we, oe, clk, din, dout
  // Probe on counter_3_q

  // Notes on the sheet:
  //   contents of rom_1 (hex, n*v repeats v):
  //   8800 800 880 888 8888 888 888 888 8888 888 888 888 8888 4*888 88 8 0 1100 880 408 200 100 880 408
  //   200 100 880 408 200 100 8880 4408 2200 1100 880 408 200 100 880 408 200 100 880 408 200 100 8880
  //   4408 2200 1100 880 408 200 100 880 408 200 100 880 408 200 100 80 8
endmodule

module MMult_Tiling (
  input  in_1,
  input  in_2,
  input  in_3,
  input  in_4,
  input  in_5,
  input  in_6,
  input  in_7
);

  wire clock_1_out, or_1_out, or_2_out, or_3_out, or_4_out, or_5_out, or_6_out, or_7_out;
  wire [7:0] counter_1_q, counter_2_q, counter_3_q, counter_4_q, counter_5_q, counter_6_q;
  wire [15:0] adder_1_out, adder_2_out, adder_3_out, adder_4_out, adder_5_out, adder_6_out, adder_7_out,
       adder_8_out, adder_9_out, adder_10_out, adder_11_out, adder_12_out, controlled_buffer_1_out,
       controlled_buffer_2_out, controlled_buffer_3_out, controlled_buffer_5_out, controlled_buffer_9_out,
       controlled_buffer_10_out, mmult_tiling_core_1_out_17, mmult_tiling_core_1_out_18,
       mmult_tiling_core_1_out_19, mmult_tiling_core_1_out_20, multiplier_1_out, multiplier_2_out,
       multiplier_3_out, multiplier_4_out, multiplier_5_out, multiplier_6_out, multiplier_7_out,
       multiplier_8_out, multiplier_9_out, multiplier_10_out, multiplier_11_out, multiplier_12_out,
       multiplier_13_out, multiplier_14_out, multiplier_15_out, multiplier_16_out, ram_1_dout, ram_2_dout,
       ram_3_dout, ram_4_dout, register_1_q, register_2_q, register_3_q, register_4_q, register_5_q,
       register_6_q, register_7_q, register_8_q, register_9_q, register_10_q, register_11_q, register_12_q,
       register_13_q, register_14_q, register_15_q, register_16_q, register_17_q, register_18_q,
       register_19_q, register_20_q, register_21_q, register_22_q, register_23_q, register_24_q,
       register_26_q, register_27_q, register_29_q, register_30_q, register_31_q, register_32_q, rom_1_data;

  or or_1 (or_1_out, rom_1_data[13], rom_1_data[12], rom_1_data[14], rom_1_data[15]);
  Counter counter_1 (.count(or_1_out), .Q(counter_1_q), .clk(clock_1_out));  // open: load, D, carry, up, clr
  or or_2 (or_2_out, rom_1_data[9], rom_1_data[8], rom_1_data[10], rom_1_data[11]);
  Counter #(.max('h7)) counter_2 (
    .count(or_2_out), .Q(counter_2_q), .clk(clock_1_out));  // open: load, D, carry, up, clr
  RAM #(.dataWidth(16), .\type ("nonvolatile")) ram_1 (
    .addr(counter_1_q), .oe(or_1_out), .clk(clock_1_out), .dout(ram_1_dout));  // open: we, din
  RAM #(.dataWidth(16), .\type ("nonvolatile")) ram_2 (
    .addr(counter_1_q), .oe(or_1_out), .clk(clock_1_out), .dout(ram_2_dout));  // open: we, din
  RAM #(.dataWidth(16), .\type ("nonvolatile")) ram_3 (
    .addr(counter_2_q), .oe(or_2_out), .clk(clock_1_out), .dout(ram_3_dout));  // open: we, din
  RAM #(.dataWidth(16), .\type ("nonvolatile")) ram_4 (
    .addr(counter_2_q), .oe(or_2_out), .clk(clock_1_out), .dout(ram_4_dout));  // open: we, din
  Register #(.width(16)) register_1 (
    .D(ram_1_dout), .en(rom_1_data[13]), .clk(clock_1_out), .Q(register_1_q));  // open: clr
  Register #(.width(16)) register_2 (
    .D(ram_2_dout), .en(rom_1_data[13]), .clk(clock_1_out), .Q(register_2_q));  // open: clr
  Register #(.width(16)) register_3 (
    .D(ram_1_dout), .en(rom_1_data[15]), .clk(clock_1_out), .Q(register_3_q));  // open: clr
  Register #(.width(16)) register_4 (
    .D(ram_2_dout), .en(rom_1_data[15]), .clk(clock_1_out), .Q(register_4_q));  // open: clr
  Register #(.width(16)) register_5 (
    .D(ram_1_dout), .en(rom_1_data[12]), .clk(clock_1_out), .Q(register_5_q));  // open: clr
  Register #(.width(16)) register_6 (
    .D(ram_1_dout), .en(rom_1_data[14]), .clk(clock_1_out), .Q(register_6_q));  // open: clr
  Register #(.width(16)) register_7 (
    .D(ram_2_dout), .en(rom_1_data[14]), .clk(clock_1_out), .Q(register_7_q));  // open: clr
  Register #(.width(16)) register_8 (
    .D(ram_2_dout), .en(rom_1_data[12]), .clk(clock_1_out), .Q(register_8_q));  // open: clr
  Register #(.width(16)) register_9 (
    .D(ram_3_dout), .en(rom_1_data[11]), .clk(clock_1_out), .Q(register_9_q));  // open: clr
  Register #(.width(16)) register_10 (
    .D(ram_3_dout), .en(rom_1_data[9]), .clk(clock_1_out), .Q(register_10_q));  // open: clr
  Register #(.width(16)) register_11 (
    .D(ram_3_dout), .en(rom_1_data[8]), .clk(clock_1_out), .Q(register_11_q));  // open: clr
  Register #(.width(16)) register_12 (
    .D(ram_3_dout), .en(rom_1_data[10]), .clk(clock_1_out), .Q(register_12_q));  // open: clr
  Clock clock_1 (.out(clock_1_out));
  Register #(.width(16)) register_13 (
    .D(ram_4_dout), .en(rom_1_data[9]), .clk(clock_1_out), .Q(register_13_q));  // open: clr
  Register #(.width(16)) register_14 (
    .D(ram_4_dout), .en(rom_1_data[8]), .clk(clock_1_out), .Q(register_14_q));  // open: clr
  Register #(.width(16)) register_15 (
    .D(ram_4_dout), .en(rom_1_data[11]), .clk(clock_1_out), .Q(register_15_q));  // open: clr
  Register #(.width(16)) register_16 (
    .D(ram_4_dout), .en(rom_1_data[10]), .clk(clock_1_out), .Q(register_16_q));  // open: clr
  Multiplier #(.width(16)) multiplier_1 (
    .a(register_9_q), .b(register_3_q), .out(multiplier_1_out));  // open: cin, cout
  Multiplier #(.width(16)) multiplier_2 (
    .a(register_6_q), .b(register_12_q), .out(multiplier_2_out));  // open: cin, cout
  Multiplier #(.width(16)) multiplier_3 (
    .a(register_3_q), .b(register_15_q), .out(multiplier_3_out));  // open: cin, cout
  Multiplier #(.width(16)) multiplier_4 (
    .a(register_6_q), .b(register_16_q), .out(multiplier_4_out));  // open: cin, cout
  Multiplier #(.width(16)) multiplier_5 (
    .a(register_4_q), .b(register_9_q), .out(multiplier_5_out));  // open: cin, cout
  Multiplier #(.width(16)) multiplier_6 (
    .a(register_7_q), .b(register_12_q), .out(multiplier_6_out));  // open: cin, cout
  Multiplier #(.width(16)) multiplier_7 (
    .a(register_4_q), .b(register_15_q), .out(multiplier_7_out));  // open: cin, cout
  Multiplier #(.width(16)) multiplier_8 (
    .a(register_7_q), .b(register_16_q), .out(multiplier_8_out));  // open: cin, cout
  Multiplier #(.width(16)) multiplier_9 (
    .a(register_10_q), .b(register_1_q), .out(multiplier_9_out));  // open: cin, cout
  Multiplier #(.width(16)) multiplier_10 (
    .a(register_5_q), .b(register_11_q), .out(multiplier_10_out));  // open: cin, cout
  Multiplier #(.width(16)) multiplier_11 (
    .a(register_1_q), .b(register_13_q), .out(multiplier_11_out));  // open: cin, cout
  Multiplier #(.width(16)) multiplier_12 (
    .a(register_5_q), .b(register_14_q), .out(multiplier_12_out));  // open: cin, cout
  Multiplier #(.width(16)) multiplier_13 (
    .a(register_2_q), .b(register_10_q), .out(multiplier_13_out));  // open: cin, cout
  Multiplier #(.width(16)) multiplier_14 (
    .a(register_8_q), .b(register_11_q), .out(multiplier_14_out));  // open: cin, cout
  Multiplier #(.width(16)) multiplier_15 (
    .a(register_2_q), .b(register_13_q), .out(multiplier_15_out));  // open: cin, cout
  Multiplier #(.width(16)) multiplier_16 (
    .a(register_8_q), .b(register_14_q), .out(multiplier_16_out));  // open: cin, cout
  Adder #(.width(16)) adder_1 (.a(multiplier_9_out), .b(multiplier_10_out), .out(adder_1_out));  // open: cin, cout
  Adder #(.width(16)) adder_2 (.a(multiplier_11_out), .b(multiplier_12_out), .out(adder_2_out));  // open: cin, cout
  Adder #(.width(16)) adder_3 (.a(multiplier_13_out), .b(multiplier_14_out), .out(adder_3_out));  // open: cin, cout
  Adder #(.width(16)) adder_4 (.a(multiplier_15_out), .b(multiplier_16_out), .out(adder_4_out));  // open: cin, cout
  Adder #(.width(16)) adder_5 (.a(multiplier_1_out), .b(multiplier_2_out), .out(adder_5_out));  // open: cin, cout
  Adder #(.width(16)) adder_6 (.a(multiplier_3_out), .b(multiplier_4_out), .out(adder_6_out));  // open: cin, cout
  Adder #(.width(16)) adder_7 (.a(multiplier_5_out), .b(multiplier_6_out), .out(adder_7_out));  // open: cin, cout
  Adder #(.width(16)) adder_8 (.a(multiplier_7_out), .b(multiplier_8_out), .out(adder_8_out));  // open: cin, cout
  Register #(.width(16)) register_17 (.D(adder_5_out), .en(in_1), .clk(clock_1_out), .Q(register_17_q));  // open: clr
  Register #(.width(16)) register_18 (.D(adder_7_out), .en(in_1), .clk(clock_1_out), .Q(register_18_q));  // open: clr
  Register #(.width(16)) register_19 (.D(adder_1_out), .en(in_5), .clk(clock_1_out), .Q(register_19_q));  // open: clr
  Register #(.width(16)) register_20 (.D(adder_3_out), .en(in_5), .clk(clock_1_out), .Q(register_20_q));  // open: clr
  Register #(.width(16)) register_21 (.D(adder_2_out), .en(in_5), .clk(clock_1_out), .Q(register_21_q));  // open: clr
  Register #(.width(16)) register_22 (.D(adder_6_out), .en(in_1), .clk(clock_1_out), .Q(register_22_q));  // open: clr
  Register #(.width(16)) register_23 (.D(adder_8_out), .en(in_1), .clk(clock_1_out), .Q(register_23_q));  // open: clr
  Register #(.width(16)) register_24 (.D(adder_4_out), .en(in_5), .clk(clock_1_out), .Q(register_24_q));  // open: clr
  or or_3 (or_3_out, in_2, in_3);
  assign controlled_buffer_1_out = in_2 ? register_17_q : 16'bz;  // Controlled_Buffer controlled_buffer_1
  or or_4 (or_4_out, in_2, in_3);
  assign controlled_buffer_2_out = in_2 ? register_18_q : 16'bz;  // Controlled_Buffer controlled_buffer_2
  Counter counter_3 (.Q(counter_3_q), .clk(clock_1_out));  // open: load, D, count, carry, up, clr
  or or_5 (or_5_out, in_6, in_7);
  assign controlled_buffer_3_out = in_6 ? register_19_q : 16'bz;  // Controlled_Buffer controlled_buffer_3
  assign controlled_buffer_3_out = in_7 ? register_21_q : 16'bz;  // Controlled_Buffer controlled_buffer_4
  or or_6 (or_6_out, in_6, in_7);
  assign controlled_buffer_5_out = in_6 ? register_20_q : 16'bz;  // Controlled_Buffer controlled_buffer_5
  assign controlled_buffer_5_out = in_7 ? register_24_q : 16'bz;  // Controlled_Buffer controlled_buffer_6
  Counter counter_4 (.Q(counter_4_q), .clk(clock_1_out));  // open: load, D, count, carry, up, clr
  RAM #(.dataWidth(16), .\type ("nonvolatile")) ram_5 (
    .addr(counter_4_q), .we(or_3_out), .clk(clock_1_out), .din(controlled_buffer_1_out));  // open: oe, dout
  assign controlled_buffer_1_out = in_3 ? register_22_q : 16'bz;  // Controlled_Buffer controlled_buffer_7
  RAM #(.dataWidth(16), .\type ("nonvolatile")) ram_6 (
    .addr(counter_4_q), .we(or_4_out), .clk(clock_1_out), .din(controlled_buffer_2_out));  // open: oe, dout
  assign controlled_buffer_2_out = in_3 ? register_23_q : 16'bz;  // Controlled_Buffer controlled_buffer_8
  RAM #(.dataWidth(16), .\type ("nonvolatile")) ram_7 (
    .addr(counter_3_q), .we(or_5_out), .clk(clock_1_out), .din(controlled_buffer_3_out));  // open: oe, dout
  RAM #(.dataWidth(16), .\type ("nonvolatile")) ram_8 (
    .addr(counter_3_q), .we(or_6_out), .clk(clock_1_out), .din(controlled_buffer_5_out));  // open: oe, dout
  Counter counter_5 (.Q(counter_5_q), .clk(clock_1_out));  // open: load, D, count, carry, up, clr
  ROM #(.dataWidth(16)) rom_1 (.addr(counter_5_q), .data(rom_1_data));
  Adder #(.width(16)) adder_9 (.a(adder_5_out), .b(adder_1_out), .out(adder_9_out));  // open: cin, cout
  Adder #(.width(16)) adder_10 (.a(adder_6_out), .b(adder_2_out), .out(adder_10_out));  // open: cin, cout
  Adder #(.width(16)) adder_11 (.a(adder_7_out), .b(adder_3_out), .out(adder_11_out));  // open: cin, cout
  Adder #(.width(16)) adder_12 (.a(adder_8_out), .b(adder_4_out), .out(adder_12_out));  // open: cin, cout
  MMult_Tiling_Core mmult_tiling_core_1 (
    .in_1(register_3_q), .in_2(register_6_q), .in_3(register_4_q), .in_4(register_7_q), .in_5(register_1_q),
    .in_6(register_5_q), .in_7(register_2_q), .in_8(register_8_q), .in_9(register_9_q),
    .in_10(register_15_q), .in_11(register_12_q), .in_12(register_16_q), .in_13(register_10_q),
    .in_14(register_13_q), .in_15(register_11_q), .in_16(register_14_q), .out_17(mmult_tiling_core_1_out_17),
    .out_18(mmult_tiling_core_1_out_18), .out_19(mmult_tiling_core_1_out_19),
    .out_20(mmult_tiling_core_1_out_20));
  Register #(.width(16)) register_25 (.D(adder_9_out), .en(in_4), .clk(clock_1_out));  // open: Q, clr
  Register #(.width(16)) register_26 (.D(adder_11_out), .en(in_4), .clk(clock_1_out), .Q(register_26_q));  // open: clr
  Hex_Digit_Display hex_digit_display_1 (.value(counter_5_q[7:4]));  // open: dp
  Register #(.width(16)) register_27 (.D(adder_10_out), .en(in_4), .clk(clock_1_out), .Q(register_27_q));  // open: clr
  Register #(.width(16)) register_28 (.D(adder_12_out), .en(in_4), .clk(clock_1_out));  // open: Q, clr
  Hex_Digit_Display hex_digit_display_2 (.value(counter_5_q[3:0]));  // open: dp
  Register #(.width(16)) register_29 (
    .D(mmult_tiling_core_1_out_17), .en(rom_1_data[7]), .clk(clock_1_out), .Q(register_29_q));  // open: clr
  Register #(.width(16)) register_30 (
    .D(mmult_tiling_core_1_out_19), .en(rom_1_data[7]), .clk(clock_1_out), .Q(register_30_q));  // open: clr
  // Probe on counter_5_q
  Register #(.width(16)) register_31 (
    .D(mmult_tiling_core_1_out_18), .en(rom_1_data[7]), .clk(clock_1_out), .Q(register_31_q));  // open: clr
  Register #(.width(16)) register_32 (
    .D(mmult_tiling_core_1_out_20), .en(rom_1_data[7]), .clk(clock_1_out), .Q(register_32_q));  // open: clr
  assign controlled_buffer_9_out = rom_1_data[3] ? register_29_q : 16'bz;  // Controlled_Buffer controlled_buffer_9
  assign controlled_buffer_10_out = rom_1_data[3] ? register_30_q : 16'bz;  // Controlled_Buffer controlled_buffer_10
  assign controlled_buffer_9_out = rom_1_data[2] ? register_31_q : 16'bz;  // Controlled_Buffer controlled_buffer_11
  assign controlled_buffer_10_out = rom_1_data[2] ? register_32_q : 16'bz;  // Controlled_Buffer controlled_buffer_12
  or or_7 (or_7_out, rom_1_data[3], rom_1_data[2]);
  Counter counter_6 (.count(or_7_out), .Q(counter_6_q), .clk(clock_1_out));  // open: load, D, carry, up, clr
  RAM #(.dataWidth(16)) ram_9 (
    .addr(counter_6_q), .we(or_7_out), .clk(clock_1_out), .din(controlled_buffer_9_out));  // open: oe, dout
  RAM #(.dataWidth(16)) ram_10 (
    .addr(counter_6_q), .we(or_7_out), .clk(clock_1_out), .din(controlled_buffer_10_out));  // open: oe, dout

  // Notes on the sheet:
  //   contents of rom_1 (hex, n*v repeats v):
  //   8800 8800 4400 2200 1100 80 808 404 200 100 80 8808 4404 2200 1100 80 808 404 200 100 80 8 4
endmodule

module MMult_Tiling_Core (
  input  [15:0] in_1,
  input  [15:0] in_2,
  input  [15:0] in_3,
  input  [15:0] in_4,
  input  [15:0] in_5,
  input  [15:0] in_6,
  input  [15:0] in_7,
  input  [15:0] in_8,
  input  [15:0] in_9,
  input  [15:0] in_10,
  input  [15:0] in_11,
  input  [15:0] in_12,
  input  [15:0] in_13,
  input  [15:0] in_14,
  input  [15:0] in_15,
  input  [15:0] in_16,
  output [15:0] out_17,
  output [15:0] out_18,
  output [15:0] out_19,
  output [15:0] out_20
);

  wire [15:0] adder_1_out, adder_2_out, adder_3_out, adder_4_out, adder_5_out, adder_6_out, adder_7_out,
       adder_8_out, multiplier_1_out, multiplier_2_out, multiplier_3_out, multiplier_4_out, multiplier_5_out,
       multiplier_6_out, multiplier_7_out, multiplier_8_out, multiplier_9_out, multiplier_10_out,
       multiplier_11_out, multiplier_12_out, multiplier_13_out, multiplier_14_out, multiplier_15_out,
       multiplier_16_out;

  Multiplier #(.width(16)) multiplier_1 (.a(in_1), .b(in_9), .out(multiplier_1_out));  // open: cin, cout
  Multiplier #(.width(16)) multiplier_2 (.a(in_2), .b(in_11), .out(multiplier_2_out));  // open: cin, cout
  Multiplier #(.width(16)) multiplier_3 (.a(in_1), .b(in_10), .out(multiplier_3_out));  // open: cin, cout
  Multiplier #(.width(16)) multiplier_4 (.a(in_2), .b(in_12), .out(multiplier_4_out));  // open: cin, cout
  Multiplier #(.width(16)) multiplier_5 (.a(in_3), .b(in_9), .out(multiplier_5_out));  // open: cin, cout
  Multiplier #(.width(16)) multiplier_6 (.a(in_4), .b(in_11), .out(multiplier_6_out));  // open: cin, cout
  Multiplier #(.width(16)) multiplier_7 (.a(in_3), .b(in_10), .out(multiplier_7_out));  // open: cin, cout
  Multiplier #(.width(16)) multiplier_8 (.a(in_4), .b(in_12), .out(multiplier_8_out));  // open: cin, cout
  Multiplier #(.width(16)) multiplier_9 (.a(in_5), .b(in_13), .out(multiplier_9_out));  // open: cin, cout
  Multiplier #(.width(16)) multiplier_10 (.a(in_6), .b(in_15), .out(multiplier_10_out));  // open: cin, cout
  Multiplier #(.width(16)) multiplier_11 (.a(in_5), .b(in_14), .out(multiplier_11_out));  // open: cin, cout
  Multiplier #(.width(16)) multiplier_12 (.a(in_6), .b(in_16), .out(multiplier_12_out));  // open: cin, cout
  Multiplier #(.width(16)) multiplier_13 (.a(in_7), .b(in_13), .out(multiplier_13_out));  // open: cin, cout
  Multiplier #(.width(16)) multiplier_14 (.a(in_8), .b(in_15), .out(multiplier_14_out));  // open: cin, cout
  Multiplier #(.width(16)) multiplier_15 (.a(in_7), .b(in_14), .out(multiplier_15_out));  // open: cin, cout
  Multiplier #(.width(16)) multiplier_16 (.a(in_8), .b(in_16), .out(multiplier_16_out));  // open: cin, cout
  Adder #(.width(16)) adder_1 (.a(multiplier_1_out), .b(multiplier_2_out), .out(adder_1_out));  // open: cin, cout
  Adder #(.width(16)) adder_2 (.a(multiplier_3_out), .b(multiplier_4_out), .out(adder_2_out));  // open: cin, cout
  Adder #(.width(16)) adder_3 (.a(multiplier_5_out), .b(multiplier_6_out), .out(adder_3_out));  // open: cin, cout
  Adder #(.width(16)) adder_4 (.a(multiplier_7_out), .b(multiplier_8_out), .out(adder_4_out));  // open: cin, cout
  Adder #(.width(16)) adder_5 (.a(multiplier_9_out), .b(multiplier_10_out), .out(adder_5_out));  // open: cin, cout
  Adder #(.width(16)) adder_6 (.a(multiplier_11_out), .b(multiplier_12_out), .out(adder_6_out));  // open: cin, cout
  Adder #(.width(16)) adder_7 (.a(multiplier_13_out), .b(multiplier_14_out), .out(adder_7_out));  // open: cin, cout
  Adder #(.width(16)) adder_8 (.a(multiplier_15_out), .b(multiplier_16_out), .out(adder_8_out));  // open: cin, cout
  Adder #(.width(16)) adder_9 (.a(adder_1_out), .b(adder_5_out), .out(out_17));  // open: cin, cout
  Adder #(.width(16)) adder_10 (.a(adder_2_out), .b(adder_6_out), .out(out_18));  // open: cin, cout
  Adder #(.width(16)) adder_11 (.a(adder_3_out), .b(adder_7_out), .out(out_19));  // open: cin, cout
  Adder #(.width(16)) adder_12 (.a(adder_4_out), .b(adder_8_out), .out(out_20));  // open: cin, cout
endmodule

module Systolic_core (
  input  [15:0] col,
  input  [15:0] row,
  input  R,
  output [15:0] row_out,
  output [15:0] out_5,
  output [15:0] col_out
);

  wire [15:0] adder_1_out, multiplier_1_out;

  Multiplier #(.width(16)) multiplier_1 (.a(col), .b(row), .out(multiplier_1_out));  // open: cin, cout
  Adder #(.width(16)) adder_1 (.a(multiplier_1_out), .b(out_5), .out(adder_1_out));  // open: cin, cout
  Register #(.width(16)) register_1 (.D(adder_1_out), .en(1'b1), .clk(R), .Q(out_5));  // open: clr

  assign col_out = col;
  assign row_out = row;
endmodule

module MMult_Systolic_2x2 (
);

  wire clock_1_out, or_1_out, systolic_core_2_p5, systolic_core_3_p6;
  wire [7:0] counter_1_q, counter_2_q, counter_3_q;
  wire [15:0] controlled_buffer_1_out, controlled_buffer_3_out, ram_1_dout, ram_2_dout, ram_3_dout,
       ram_4_dout, register_1_q, register_2_q, register_3_q, register_4_q, register_5_q, register_6_q,
       register_7_q, register_8_q, rom_1_data, systolic_core_1_col_out, systolic_core_1_out_5,
       systolic_core_1_row_out, systolic_core_2_p6, systolic_core_3_p5, systolic_core_4_p5;

  Counter counter_1 (.Q(counter_1_q), .clk(clock_1_out));  // open: load, D, count, carry, up, clr
  RAM #(.dataWidth(16), .\type ("nonvolatile")) ram_1 (
    .addr(counter_1_q), .oe(1'b1), .clk(clock_1_out), .dout(ram_1_dout));  // open: we, din
  RAM #(.dataWidth(16), .\type ("nonvolatile")) ram_2 (
    .addr(counter_1_q), .oe(1'b1), .clk(clock_1_out), .dout(ram_2_dout));  // open: we, din
  RAM #(.dataWidth(16), .\type ("nonvolatile")) ram_3 (
    .addr(counter_1_q), .oe(1'b1), .clk(clock_1_out), .dout(ram_3_dout));  // open: we, din
  Register #(.width(16)) register_1 (
    .D(ram_2_dout), .en(rom_1_data[15]), .clk(clock_1_out), .Q(register_1_q));  // open: clr
  Register #(.width(16)) register_2 (
    .D(ram_1_dout), .en(rom_1_data[15]), .clk(clock_1_out), .Q(register_2_q));  // open: clr
  Clock clock_1 (.out(clock_1_out));
  Register #(.width(16)) register_3 (
    .D(ram_3_dout), .en(rom_1_data[15]), .clk(clock_1_out), .Q(register_3_q));  // open: clr
  RAM #(.dataWidth(16), .\type ("nonvolatile")) ram_4 (
    .addr(counter_1_q), .oe(1'b1), .clk(clock_1_out), .dout(ram_4_dout));  // open: we, din
  Systolic_core systolic_core_1 (
    .col(register_3_q), .row(register_2_q), .R(rom_1_data[15]), .row_out(systolic_core_1_row_out),
    .out_5(systolic_core_1_out_5), .col_out(systolic_core_1_col_out));
  // Systolic_core systolic_core_2: pin names not known; wires that end beside it: systolic_core_1_col_out, register_1_q, rom_1_data[15], clock_1_out, systolic_core_2_p5, systolic_core_2_p6
  Register #(.width(16)) register_4 (
    .D(ram_4_dout), .en(rom_1_data[15]), .clk(clock_1_out), .Q(register_4_q));  // open: clr
  Register #(.width(16)) register_5 (
    .D(systolic_core_3_p5), .en(rom_1_data[15]), .clk(clock_1_out), .Q(register_5_q));  // open: clr
  // Systolic_core systolic_core_3: pin names not known; wires that end beside it: register_4_q, systolic_core_1_row_out, rom_1_data[15], clock_1_out, systolic_core_3_p5, systolic_core_3_p6
  Register #(.width(16)) register_6 (
    .D(systolic_core_1_out_5), .en(rom_1_data[15]), .clk(clock_1_out), .Q(register_6_q));  // open: clr
  // Systolic_core systolic_core_4: pin names not known; wires that end beside it: systolic_core_3_p6, systolic_core_2_p5, rom_1_data[15], clock_1_out, systolic_core_4_p5
  Register #(.width(16)) register_7 (
    .D(systolic_core_4_p5), .en(rom_1_data[15]), .clk(clock_1_out), .Q(register_7_q));  // open: clr
  Register #(.width(16)) register_8 (
    .D(systolic_core_2_p6), .en(rom_1_data[15]), .clk(clock_1_out), .Q(register_8_q));  // open: clr
  Counter counter_2 (.count(or_1_out), .Q(counter_2_q), .clk(clock_1_out));  // open: load, D, carry, up, clr
  assign controlled_buffer_1_out = rom_1_data[10] ? register_5_q : 16'bz;  // Controlled_Buffer controlled_buffer_1
  assign controlled_buffer_1_out = rom_1_data[11] ? register_6_q : 16'bz;  // Controlled_Buffer controlled_buffer_2
  assign controlled_buffer_3_out = rom_1_data[10] ? register_7_q : 16'bz;  // Controlled_Buffer controlled_buffer_3
  assign controlled_buffer_3_out = rom_1_data[11] ? register_8_q : 16'bz;  // Controlled_Buffer controlled_buffer_4
  RAM #(.dataWidth(16)) ram_5 (
    .addr(counter_2_q), .we(or_1_out), .clk(clock_1_out), .din(controlled_buffer_1_out));  // open: oe, dout
  RAM #(.dataWidth(16)) ram_6 (
    .addr(counter_2_q), .we(or_1_out), .clk(clock_1_out), .din(controlled_buffer_3_out));  // open: oe, dout
  or or_1 (or_1_out, rom_1_data[11], rom_1_data[10]);
  ROM #(.dataWidth(16)) rom_1 (.addr(counter_3_q), .data(rom_1_data));
  Counter counter_3 (.Q(counter_3_q), .clk(clock_1_out));  // open: load, D, count, carry, up, clr

  // Notes on the sheet:
  //   contents of rom_1 (hex, n*v repeats v):
  //   0 4*8000 800 400 200 100
endmodule

module MMult_Systolic_4x4 (
);

  wire clock_1_out, or_1_out, or_2_out, or_3_out;
  wire [7:0] counter_1_q, counter_2_q, counter_3_q, counter_4_q;
  wire [15:0] controlled_buffer_1_out, controlled_buffer_2_out, controlled_buffer_3_out,
       controlled_buffer_4_out, controlled_buffer_17_out, ram_1_dout, ram_2_dout, ram_3_dout, ram_4_dout,
       ram_5_dout, ram_6_dout, ram_7_dout, ram_8_dout, ram_9_dout, ram_10_dout, ram_11_dout, ram_12_dout,
       register_1_q, register_2_q, register_3_q, register_4_q, register_5_q, register_6_q, register_7_q,
       register_8_q, register_9_q, register_10_q, register_11_q, register_12_q, register_13_q, register_14_q,
       register_15_q, register_16_q, register_17_q, register_18_q, register_19_q, register_20_q,
       register_21_q, register_22_q, register_23_q, register_24_q, rom_1_data, systolic_core_1_col_out,
       systolic_core_1_out_5, systolic_core_1_row_out, systolic_core_2_col_out, systolic_core_2_out_5,
       systolic_core_2_row_out, systolic_core_3_col_out, systolic_core_3_out_5, systolic_core_3_row_out,
       systolic_core_4_out_5, systolic_core_4_row_out, systolic_core_5_col_out, systolic_core_5_out_5,
       systolic_core_5_row_out, systolic_core_6_col_out, systolic_core_6_out_5, systolic_core_6_row_out,
       systolic_core_7_col_out, systolic_core_7_out_5, systolic_core_7_row_out, systolic_core_8_out_5,
       systolic_core_8_row_out, systolic_core_9_col_out, systolic_core_9_out_5, systolic_core_9_row_out,
       systolic_core_10_col_out, systolic_core_10_out_5, systolic_core_10_row_out, systolic_core_11_col_out,
       systolic_core_11_out_5, systolic_core_11_row_out, systolic_core_12_out_5, systolic_core_12_row_out,
       systolic_core_13_col_out, systolic_core_13_out_5, systolic_core_14_col_out, systolic_core_14_out_5,
       systolic_core_15_col_out, systolic_core_15_out_5, systolic_core_16_out_5;

  Counter counter_1 (.count(rom_1_data[15]), .Q(counter_1_q), .clk(clock_1_out));  // open: load, D, carry, up, clr
  RAM #(.dataWidth(16), .\type ("nonvolatile")) ram_1 (
    .addr(counter_1_q), .oe(rom_1_data[15]), .clk(clock_1_out), .dout(ram_1_dout));  // open: we, din
  RAM #(.dataWidth(16), .\type ("nonvolatile")) ram_2 (
    .addr(counter_1_q), .oe(rom_1_data[15]), .clk(clock_1_out), .dout(ram_2_dout));  // open: we, din
  RAM #(.dataWidth(16), .\type ("nonvolatile")) ram_3 (
    .addr(counter_1_q), .oe(rom_1_data[15]), .clk(clock_1_out), .dout(ram_3_dout));  // open: we, din
  RAM #(.dataWidth(16), .\type ("nonvolatile")) ram_4 (
    .addr(counter_1_q), .oe(rom_1_data[15]), .clk(clock_1_out), .dout(ram_4_dout));  // open: we, din
  RAM #(.dataWidth(16), .\type ("nonvolatile")) ram_5 (
    .addr(counter_1_q), .oe(rom_1_data[15]), .clk(clock_1_out), .dout(ram_5_dout));  // open: we, din
  Register #(.width(16)) register_1 (
    .D(ram_1_dout), .en(rom_1_data[11]), .clk(clock_1_out), .Q(register_1_q));  // open: clr
  Register #(.width(16)) register_2 (
    .D(ram_2_dout), .en(rom_1_data[11]), .clk(clock_1_out), .Q(register_2_q));  // open: clr
  Register #(.width(16)) register_3 (
    .D(ram_3_dout), .en(rom_1_data[11]), .clk(clock_1_out), .Q(register_3_q));  // open: clr
  Register #(.width(16)) register_4 (
    .D(ram_4_dout), .en(rom_1_data[11]), .clk(clock_1_out), .Q(register_4_q));  // open: clr
  RAM #(.dataWidth(16), .\type ("nonvolatile")) ram_6 (
    .addr(counter_1_q), .oe(rom_1_data[15]), .clk(clock_1_out), .dout(ram_6_dout));  // open: we, din
  Register #(.width(16)) register_5 (
    .D(ram_5_dout), .en(rom_1_data[11]), .clk(clock_1_out), .Q(register_5_q));  // open: clr
  Clock clock_1 (.out(clock_1_out));
  Register #(.width(16)) register_6 (
    .D(ram_6_dout), .en(rom_1_data[11]), .clk(clock_1_out), .Q(register_6_q));  // open: clr
  RAM #(.dataWidth(16), .\type ("nonvolatile")) ram_7 (
    .addr(counter_1_q), .oe(rom_1_data[15]), .clk(clock_1_out), .dout(ram_7_dout));  // open: we, din
  Systolic_core systolic_core_1 (
    .col(register_5_q), .row(register_1_q), .R(clock_1_out), .row_out(systolic_core_1_row_out),
    .out_5(systolic_core_1_out_5), .col_out(systolic_core_1_col_out));
  Systolic_core systolic_core_2 (
    .col(systolic_core_1_col_out), .row(register_2_q), .R(clock_1_out), .row_out(systolic_core_2_row_out),
    .out_5(systolic_core_2_out_5), .col_out(systolic_core_2_col_out));
  Systolic_core systolic_core_3 (
    .col(systolic_core_2_col_out), .row(register_3_q), .R(clock_1_out), .row_out(systolic_core_3_row_out),
    .out_5(systolic_core_3_out_5), .col_out(systolic_core_3_col_out));
  Systolic_core systolic_core_4 (
    .col(systolic_core_3_col_out), .row(register_4_q), .R(clock_1_out), .row_out(systolic_core_4_row_out),
    .out_5(systolic_core_4_out_5));  // open: col_out
  Register #(.width(16)) register_7 (
    .D(systolic_core_1_out_5), .en(rom_1_data[11]), .clk(clock_1_out), .Q(register_7_q));  // open: clr
  Register #(.width(16)) register_8 (
    .D(systolic_core_2_out_5), .en(rom_1_data[11]), .clk(clock_1_out), .Q(register_8_q));  // open: clr
  Register #(.width(16)) register_9 (
    .D(systolic_core_3_out_5), .en(rom_1_data[11]), .clk(clock_1_out), .Q(register_9_q));  // open: clr
  Register #(.width(16)) register_10 (
    .D(systolic_core_4_out_5), .en(rom_1_data[11]), .clk(clock_1_out), .Q(register_10_q));  // open: clr
  assign controlled_buffer_1_out = rom_1_data[7] ? register_7_q : 16'bz;  // Controlled_Buffer controlled_buffer_1
  assign controlled_buffer_2_out = rom_1_data[7] ? register_8_q : 16'bz;  // Controlled_Buffer controlled_buffer_2
  assign controlled_buffer_3_out = rom_1_data[7] ? register_9_q : 16'bz;  // Controlled_Buffer controlled_buffer_3
  assign controlled_buffer_4_out = rom_1_data[7] ? register_10_q : 16'bz;  // Controlled_Buffer controlled_buffer_4
  RAM #(.dataWidth(16), .\type ("nonvolatile")) ram_8 (
    .addr(counter_1_q), .oe(rom_1_data[15]), .clk(clock_1_out), .dout(ram_8_dout));  // open: we, din
  Register #(.width(16)) register_11 (
    .D(ram_7_dout), .en(rom_1_data[11]), .clk(clock_1_out), .Q(register_11_q));  // open: clr
  Systolic_core systolic_core_5 (
    .col(register_6_q), .row(systolic_core_1_row_out), .R(clock_1_out), .row_out(systolic_core_5_row_out),
    .out_5(systolic_core_5_out_5), .col_out(systolic_core_5_col_out));
  Systolic_core systolic_core_6 (
    .col(systolic_core_5_col_out), .row(systolic_core_2_row_out), .R(clock_1_out),
    .row_out(systolic_core_6_row_out), .out_5(systolic_core_6_out_5), .col_out(systolic_core_6_col_out));
  Systolic_core systolic_core_7 (
    .col(systolic_core_6_col_out), .row(systolic_core_3_row_out), .R(clock_1_out),
    .row_out(systolic_core_7_row_out), .out_5(systolic_core_7_out_5), .col_out(systolic_core_7_col_out));
  Systolic_core systolic_core_8 (
    .col(systolic_core_7_col_out), .row(systolic_core_4_row_out), .R(clock_1_out),
    .row_out(systolic_core_8_row_out), .out_5(systolic_core_8_out_5));  // open: col_out
  Register #(.width(16)) register_12 (
    .D(systolic_core_5_out_5), .en(rom_1_data[11]), .clk(clock_1_out), .Q(register_12_q));  // open: clr
  Register #(.width(16)) register_13 (
    .D(systolic_core_6_out_5), .en(rom_1_data[11]), .clk(clock_1_out), .Q(register_13_q));  // open: clr
  Register #(.width(16)) register_14 (
    .D(systolic_core_7_out_5), .en(rom_1_data[11]), .clk(clock_1_out), .Q(register_14_q));  // open: clr
  Register #(.width(16)) register_15 (
    .D(systolic_core_8_out_5), .en(rom_1_data[11]), .clk(clock_1_out), .Q(register_15_q));  // open: clr
  assign controlled_buffer_1_out = rom_1_data[6] ? register_12_q : 16'bz;  // Controlled_Buffer controlled_buffer_5
  assign controlled_buffer_2_out = rom_1_data[6] ? register_13_q : 16'bz;  // Controlled_Buffer controlled_buffer_6
  assign controlled_buffer_3_out = rom_1_data[6] ? register_14_q : 16'bz;  // Controlled_Buffer controlled_buffer_7
  assign controlled_buffer_4_out = rom_1_data[6] ? register_15_q : 16'bz;  // Controlled_Buffer controlled_buffer_8
  Register #(.width(16)) register_16 (
    .D(ram_8_dout), .en(rom_1_data[11]), .clk(clock_1_out), .Q(register_16_q));  // open: clr
  Systolic_core systolic_core_9 (
    .col(register_11_q), .row(systolic_core_5_row_out), .R(clock_1_out), .row_out(systolic_core_9_row_out),
    .out_5(systolic_core_9_out_5), .col_out(systolic_core_9_col_out));
  Systolic_core systolic_core_10 (
    .col(systolic_core_9_col_out), .row(systolic_core_6_row_out), .R(clock_1_out),
    .row_out(systolic_core_10_row_out), .out_5(systolic_core_10_out_5), .col_out(systolic_core_10_col_out));
  Systolic_core systolic_core_11 (
    .col(systolic_core_10_col_out), .row(systolic_core_7_row_out), .R(clock_1_out),
    .row_out(systolic_core_11_row_out), .out_5(systolic_core_11_out_5), .col_out(systolic_core_11_col_out));
  Systolic_core systolic_core_12 (
    .col(systolic_core_11_col_out), .row(systolic_core_8_row_out), .R(clock_1_out),
    .row_out(systolic_core_12_row_out), .out_5(systolic_core_12_out_5));  // open: col_out
  Register #(.width(16)) register_17 (
    .D(systolic_core_9_out_5), .en(rom_1_data[11]), .clk(clock_1_out), .Q(register_17_q));  // open: clr
  Register #(.width(16)) register_18 (
    .D(systolic_core_10_out_5), .en(rom_1_data[11]), .clk(clock_1_out), .Q(register_18_q));  // open: clr
  Register #(.width(16)) register_19 (
    .D(systolic_core_11_out_5), .en(rom_1_data[11]), .clk(clock_1_out), .Q(register_19_q));  // open: clr
  Register #(.width(16)) register_20 (
    .D(systolic_core_12_out_5), .en(rom_1_data[11]), .clk(clock_1_out), .Q(register_20_q));  // open: clr
  assign controlled_buffer_1_out = rom_1_data[5] ? register_17_q : 16'bz;  // Controlled_Buffer controlled_buffer_9
  assign controlled_buffer_2_out = rom_1_data[5] ? register_18_q : 16'bz;  // Controlled_Buffer controlled_buffer_10
  assign controlled_buffer_3_out = rom_1_data[5] ? register_19_q : 16'bz;  // Controlled_Buffer controlled_buffer_11
  assign controlled_buffer_4_out = rom_1_data[5] ? register_20_q : 16'bz;  // Controlled_Buffer controlled_buffer_12
  Systolic_core systolic_core_13 (
    .col(register_16_q), .row(systolic_core_9_row_out), .R(clock_1_out), .out_5(systolic_core_13_out_5),
    .col_out(systolic_core_13_col_out));  // open: row_out
  Systolic_core systolic_core_14 (
    .col(systolic_core_13_col_out), .row(systolic_core_10_row_out), .R(clock_1_out),
    .out_5(systolic_core_14_out_5), .col_out(systolic_core_14_col_out));  // open: row_out
  Systolic_core systolic_core_15 (
    .col(systolic_core_14_col_out), .row(systolic_core_11_row_out), .R(clock_1_out),
    .out_5(systolic_core_15_out_5), .col_out(systolic_core_15_col_out));  // open: row_out
  Systolic_core systolic_core_16 (
    .col(systolic_core_15_col_out), .row(systolic_core_12_row_out), .R(clock_1_out),
    .out_5(systolic_core_16_out_5));  // open: row_out, col_out
  Register #(.width(16)) register_21 (
    .D(systolic_core_13_out_5), .en(rom_1_data[11]), .clk(clock_1_out), .Q(register_21_q));  // open: clr
  Register #(.width(16)) register_22 (
    .D(systolic_core_14_out_5), .en(rom_1_data[11]), .clk(clock_1_out), .Q(register_22_q));  // open: clr
  Register #(.width(16)) register_23 (
    .D(systolic_core_15_out_5), .en(rom_1_data[11]), .clk(clock_1_out), .Q(register_23_q));  // open: clr
  Register #(.width(16)) register_24 (
    .D(systolic_core_16_out_5), .en(rom_1_data[11]), .clk(clock_1_out), .Q(register_24_q));  // open: clr
  assign controlled_buffer_1_out = rom_1_data[4] ? register_21_q : 16'bz;  // Controlled_Buffer controlled_buffer_13
  assign controlled_buffer_2_out = rom_1_data[4] ? register_22_q : 16'bz;  // Controlled_Buffer controlled_buffer_14
  assign controlled_buffer_3_out = rom_1_data[4] ? register_23_q : 16'bz;  // Controlled_Buffer controlled_buffer_15
  assign controlled_buffer_4_out = rom_1_data[4] ? register_24_q : 16'bz;  // Controlled_Buffer controlled_buffer_16
  Counter counter_2 (
    .count(or_1_out), .Q(counter_2_q), .clk(clock_1_out), .clr(rom_1_data[10]));  // open: load, D, carry, up
  or or_1 (or_1_out, rom_1_data[3], rom_1_data[2], rom_1_data[4], rom_1_data[5], rom_1_data[1], rom_1_data[7], rom_1_data[6], rom_1_data[0]);
  or or_2 (or_2_out, rom_1_data[10], rom_1_data[3], rom_1_data[15], rom_1_data[11], rom_1_data[7], rom_1_data[2], rom_1_data[6], rom_1_data[5], rom_1_data[4], rom_1_data[1], rom_1_data[0]);
  RAM #(.dataWidth(16)) ram_9 (
    .addr(counter_2_q), .we(or_1_out), .clk(clock_1_out), .din(controlled_buffer_1_out), .dout(ram_9_dout));  // open: oe
  RAM #(.dataWidth(16)) ram_10 (
    .addr(counter_2_q), .we(or_1_out), .clk(clock_1_out), .din(controlled_buffer_2_out), .dout(ram_10_dout));  // open: oe
  RAM #(.dataWidth(16)) ram_11 (
    .addr(counter_2_q), .we(or_1_out), .clk(clock_1_out), .din(controlled_buffer_3_out), .dout(ram_11_dout));  // open: oe
  RAM #(.dataWidth(16)) ram_12 (
    .addr(counter_2_q), .we(or_1_out), .clk(clock_1_out), .din(controlled_buffer_4_out), .dout(ram_12_dout));  // open: oe
  ROM #(.dataWidth(16)) rom_1 (.addr(counter_3_q), .data(rom_1_data));
  Counter counter_3 (.count(or_2_out), .Q(counter_3_q), .clk(clock_1_out));  // open: load, D, carry, up, clr
  assign controlled_buffer_17_out = rom_1_data[0] ? ram_12_dout : 16'bz;  // Controlled_Buffer controlled_buffer_17
  assign controlled_buffer_17_out = rom_1_data[2] ? ram_10_dout : 16'bz;  // Controlled_Buffer controlled_buffer_18
  assign controlled_buffer_17_out = rom_1_data[1] ? ram_11_dout : 16'bz;  // Controlled_Buffer controlled_buffer_19
  assign controlled_buffer_17_out = rom_1_data[3] ? ram_9_dout : 16'bz;  // Controlled_Buffer controlled_buffer_20
  or or_3 (or_3_out, rom_1_data[3], rom_1_data[2], rom_1_data[1], rom_1_data[0]);
  Counter counter_4 (.count(or_3_out), .Q(counter_4_q), .clk(clock_1_out));  // open: load, D, carry, up, clr
  RAM #(.dataWidth(16)) ram_13 (
    .addr(counter_4_q), .we(or_3_out), .clk(clock_1_out), .din(controlled_buffer_17_out));  // open: oe, dout

  // Notes on the sheet:
  //   contents of rom_1 (hex, n*v repeats v):
  //   8000 6*8800 80 40 20 10 400 4*8 400 4*4 400 4*2 400 4*1
endmodule

module MMult_tiling_4x4 (
);

  wire clock_1_out, not_1_out, or_1_out;
  wire [7:0] counter_1_q, counter_2_q, counter_3_q, counter_4_q, counter_5_q, counter_6_q, counter_7_q,
       counter_8_q, counter_9_q, register_49_q;
  wire [15:0] controlled_buffer_1_out, controlled_buffer_2_out, controlled_buffer_3_out,
       controlled_buffer_4_out, controlled_buffer_17_out, ram_1_dout, ram_2_dout, ram_3_dout, ram_4_dout,
       ram_5_dout, ram_6_dout, ram_7_dout, register_1_q, register_2_q, register_3_q, register_4_q,
       register_5_q, register_6_q, register_7_q, register_8_q, register_9_q, register_10_q, register_11_q,
       register_12_q, register_13_q, register_14_q, register_15_q, register_16_q, register_17_q,
       register_18_q, register_19_q, register_20_q, register_21_q, register_22_q, register_23_q,
       register_24_q, register_25_q, register_26_q, register_27_q, register_28_q, register_29_q,
       register_30_q, register_31_q, register_32_q, register_33_q, register_34_q, register_35_q,
       register_36_q, register_37_q, register_38_q, register_39_q, register_40_q, register_41_q,
       register_42_q, register_43_q, register_44_q, register_45_q, register_46_q, register_47_q,
       register_48_q, tiling_core_4x4_1_c1, tiling_core_4x4_1_c2, tiling_core_4x4_1_c3, tiling_core_4x4_1_c4,
       tiling_core_4x4_1_c5, tiling_core_4x4_1_c6, tiling_core_4x4_1_c7, tiling_core_4x4_1_c8,
       tiling_core_4x4_1_c9, tiling_core_4x4_1_c10, tiling_core_4x4_1_c11, tiling_core_4x4_1_c12,
       tiling_core_4x4_1_c13, tiling_core_4x4_1_c14, tiling_core_4x4_1_c15, tiling_core_4x4_1_c16;
  wire [15:8] register_49_q_2;
  wire [63:0] rom_1_data;

  Counter counter_1 (.Q(counter_1_q), .clk(clock_1_out));  // open: load, D, count, carry, up, clr
  Counter counter_2 (.Q(counter_2_q), .clk(clock_1_out));  // open: load, D, count, carry, up, clr
  RAM #(.addrWidth(12), .dataWidth(16), .\type ("nonvolatile")) ram_1 (
    .addr({register_49_q[3:0], counter_1_q}), .clk(clock_1_out), .dout(ram_1_dout));  // open: we, oe, din
  RAM #(.addrWidth(12), .dataWidth(16), .\type ("nonvolatile")) ram_2 (
    .addr({register_49_q[7:4], counter_2_q}), .clk(clock_1_out), .dout(ram_2_dout));  // open: we, oe, din
  Register #(.width(16)) register_1 (
    .D(ram_1_dout), .en(rom_1_data[63]), .clk(clock_1_out), .Q(register_1_q), .clr(rom_1_data[31]));
  Register #(.width(16)) register_2 (
    .D(ram_1_dout), .en(rom_1_data[62]), .clk(clock_1_out), .Q(register_2_q), .clr(rom_1_data[31]));
  Register #(.width(16)) register_3 (
    .D(ram_1_dout), .en(rom_1_data[61]), .clk(clock_1_out), .Q(register_3_q), .clr(rom_1_data[31]));
  Register #(.width(16)) register_4 (
    .D(ram_1_dout), .en(rom_1_data[60]), .clk(clock_1_out), .Q(register_4_q), .clr(rom_1_data[31]));
  Register #(.width(16)) register_5 (
    .D(ram_2_dout), .en(rom_1_data[47]), .clk(clock_1_out), .Q(register_5_q), .clr(rom_1_data[31]));
  Register #(.width(16)) register_6 (
    .D(ram_2_dout), .en(rom_1_data[46]), .clk(clock_1_out), .Q(register_6_q), .clr(rom_1_data[31]));
  Register #(.width(16)) register_7 (
    .D(ram_2_dout), .en(rom_1_data[45]), .clk(clock_1_out), .Q(register_7_q), .clr(rom_1_data[31]));
  Register #(.width(16)) register_8 (
    .D(ram_2_dout), .en(rom_1_data[44]), .clk(clock_1_out), .Q(register_8_q), .clr(rom_1_data[31]));
  Register #(.width(16)) register_9 (
    .D(ram_1_dout), .en(rom_1_data[59]), .clk(clock_1_out), .Q(register_9_q), .clr(rom_1_data[31]));
  Register #(.width(16)) register_10 (
    .D(ram_1_dout), .en(rom_1_data[58]), .clk(clock_1_out), .Q(register_10_q), .clr(rom_1_data[31]));
  Register #(.width(16)) register_11 (
    .D(ram_1_dout), .en(rom_1_data[57]), .clk(clock_1_out), .Q(register_11_q), .clr(rom_1_data[31]));
  Register #(.width(16)) register_12 (
    .D(ram_1_dout), .en(rom_1_data[56]), .clk(clock_1_out), .Q(register_12_q), .clr(rom_1_data[31]));
  Register #(.width(16)) register_13 (
    .D(ram_2_dout), .en(rom_1_data[43]), .clk(clock_1_out), .Q(register_13_q), .clr(rom_1_data[31]));
  Register #(.width(16)) register_14 (
    .D(ram_2_dout), .en(rom_1_data[42]), .clk(clock_1_out), .Q(register_14_q), .clr(rom_1_data[31]));
  Register #(.width(16)) register_15 (
    .D(ram_2_dout), .en(rom_1_data[41]), .clk(clock_1_out), .Q(register_15_q), .clr(rom_1_data[31]));
  Register #(.width(16)) register_16 (
    .D(ram_2_dout), .en(rom_1_data[40]), .clk(clock_1_out), .Q(register_16_q), .clr(rom_1_data[31]));
  Register #(.width(16)) register_17 (
    .D(ram_1_dout), .en(rom_1_data[55]), .clk(clock_1_out), .Q(register_17_q), .clr(rom_1_data[31]));
  Register #(.width(16)) register_18 (
    .D(ram_1_dout), .en(rom_1_data[54]), .clk(clock_1_out), .Q(register_18_q), .clr(rom_1_data[31]));
  Register #(.width(16)) register_19 (
    .D(ram_1_dout), .en(rom_1_data[53]), .clk(clock_1_out), .Q(register_19_q), .clr(rom_1_data[31]));
  Register #(.width(16)) register_20 (
    .D(ram_1_dout), .en(rom_1_data[52]), .clk(clock_1_out), .Q(register_20_q), .clr(rom_1_data[31]));
  Register #(.width(16)) register_21 (
    .D(ram_2_dout), .en(rom_1_data[39]), .clk(clock_1_out), .Q(register_21_q), .clr(rom_1_data[31]));
  Register #(.width(16)) register_22 (
    .D(ram_2_dout), .en(rom_1_data[38]), .clk(clock_1_out), .Q(register_22_q), .clr(rom_1_data[31]));
  Register #(.width(16)) register_23 (
    .D(ram_2_dout), .en(rom_1_data[37]), .clk(clock_1_out), .Q(register_23_q), .clr(rom_1_data[31]));
  Register #(.width(16)) register_24 (
    .D(ram_2_dout), .en(rom_1_data[36]), .clk(clock_1_out), .Q(register_24_q), .clr(rom_1_data[31]));
  Register #(.width(16)) register_25 (
    .D(ram_1_dout), .en(rom_1_data[51]), .clk(clock_1_out), .Q(register_25_q), .clr(rom_1_data[31]));
  Register #(.width(16)) register_26 (
    .D(ram_1_dout), .en(rom_1_data[50]), .clk(clock_1_out), .Q(register_26_q), .clr(rom_1_data[31]));
  Register #(.width(16)) register_27 (
    .D(ram_1_dout), .en(rom_1_data[49]), .clk(clock_1_out), .Q(register_27_q), .clr(rom_1_data[31]));
  Register #(.width(16)) register_28 (
    .D(ram_1_dout), .en(rom_1_data[48]), .clk(clock_1_out), .Q(register_28_q), .clr(rom_1_data[31]));
  Clock clock_1 (.out(clock_1_out));
  Register #(.width(16)) register_29 (
    .D(ram_2_dout), .en(rom_1_data[35]), .clk(clock_1_out), .Q(register_29_q), .clr(rom_1_data[31]));
  Register #(.width(16)) register_30 (
    .D(ram_2_dout), .en(rom_1_data[34]), .clk(clock_1_out), .Q(register_30_q), .clr(rom_1_data[31]));
  Register #(.width(16)) register_31 (
    .D(ram_2_dout), .en(rom_1_data[33]), .clk(clock_1_out), .Q(register_31_q), .clr(rom_1_data[31]));
  Register #(.width(16)) register_32 (
    .D(ram_2_dout), .en(rom_1_data[32]), .clk(clock_1_out), .Q(register_32_q), .clr(rom_1_data[31]));
  tiling_core_4x4 tiling_core_4x4_1 (
    .a1(register_1_q), .a2(register_9_q), .a3(register_17_q), .a4(register_25_q), .a5(register_2_q),
    .a6(register_10_q), .a7(register_18_q), .a8(register_26_q), .a9(register_3_q), .a10(register_11_q),
    .a11(register_19_q), .a12(register_27_q), .a13(register_4_q), .a14(register_12_q), .a15(register_20_q),
    .a16(register_28_q), .b1(register_5_q), .b5(register_6_q), .b9(register_7_q), .b13(register_8_q),
    .b2(register_13_q), .b6(register_14_q), .b10(register_15_q), .b14(register_16_q), .b3(register_21_q),
    .b7(register_22_q), .b11(register_23_q), .b15(register_24_q), .b4(register_29_q), .b8(register_30_q),
    .b12(register_31_q), .b16(register_32_q), .s1(register_33_q), .s2(register_37_q), .s3(register_41_q),
    .s4(register_45_q), .s5(register_34_q), .s6(register_38_q), .s7(register_42_q), .s8(register_46_q),
    .s9(register_35_q), .s10(register_39_q), .s11(register_43_q), .s12(register_47_q), .s13(register_36_q),
    .s14(register_40_q), .s15(register_44_q), .s16(register_48_q), .c1(tiling_core_4x4_1_c1),
    .c2(tiling_core_4x4_1_c2), .c3(tiling_core_4x4_1_c3), .c4(tiling_core_4x4_1_c4),
    .c5(tiling_core_4x4_1_c5), .c6(tiling_core_4x4_1_c6), .c7(tiling_core_4x4_1_c7),
    .c8(tiling_core_4x4_1_c8), .c9(tiling_core_4x4_1_c9), .c10(tiling_core_4x4_1_c10),
    .c11(tiling_core_4x4_1_c11), .c12(tiling_core_4x4_1_c12), .c13(tiling_core_4x4_1_c13),
    .c14(tiling_core_4x4_1_c14), .c15(tiling_core_4x4_1_c15), .c16(tiling_core_4x4_1_c16));
  Register #(.width(16)) register_33 (
    .D(tiling_core_4x4_1_c1), .en(rom_1_data[30]), .clk(clock_1_out), .Q(register_33_q), .clr(rom_1_data[29]));
  Register #(.width(16)) register_34 (
    .D(tiling_core_4x4_1_c5), .en(rom_1_data[30]), .clk(clock_1_out), .Q(register_34_q), .clr(rom_1_data[29]));
  Register #(.width(16)) register_35 (
    .D(tiling_core_4x4_1_c9), .en(rom_1_data[30]), .clk(clock_1_out), .Q(register_35_q), .clr(rom_1_data[29]));
  Register #(.width(16)) register_36 (
    .D(tiling_core_4x4_1_c13), .en(rom_1_data[30]), .clk(clock_1_out), .Q(register_36_q), .clr(rom_1_data[29]));
  Register #(.width(16)) register_37 (
    .D(tiling_core_4x4_1_c2), .en(rom_1_data[30]), .clk(clock_1_out), .Q(register_37_q), .clr(rom_1_data[29]));
  assign controlled_buffer_1_out = rom_1_data[27] ? register_33_q : 16'bz;  // Controlled_Buffer controlled_buffer_1
  Register #(.width(16)) register_38 (
    .D(tiling_core_4x4_1_c6), .en(rom_1_data[30]), .clk(clock_1_out), .Q(register_38_q), .clr(rom_1_data[29]));
  assign controlled_buffer_2_out = rom_1_data[27] ? register_34_q : 16'bz;  // Controlled_Buffer controlled_buffer_2
  Register #(.width(16)) register_39 (
    .D(tiling_core_4x4_1_c10), .en(rom_1_data[30]), .clk(clock_1_out), .Q(register_39_q), .clr(rom_1_data[29]));
  assign controlled_buffer_3_out = rom_1_data[27] ? register_35_q : 16'bz;  // Controlled_Buffer controlled_buffer_3
  Register #(.width(16)) register_40 (
    .D(tiling_core_4x4_1_c14), .en(rom_1_data[30]), .clk(clock_1_out), .Q(register_40_q), .clr(rom_1_data[29]));
  assign controlled_buffer_4_out = rom_1_data[27] ? register_36_q : 16'bz;  // Controlled_Buffer controlled_buffer_4
  assign controlled_buffer_1_out = rom_1_data[26] ? register_37_q : 16'bz;  // Controlled_Buffer controlled_buffer_5
  assign controlled_buffer_2_out = rom_1_data[26] ? register_38_q : 16'bz;  // Controlled_Buffer controlled_buffer_6
  assign controlled_buffer_3_out = rom_1_data[26] ? register_39_q : 16'bz;  // Controlled_Buffer controlled_buffer_7
  assign controlled_buffer_4_out = rom_1_data[26] ? register_40_q : 16'bz;  // Controlled_Buffer controlled_buffer_8
  Register #(.width(16)) register_41 (
    .D(tiling_core_4x4_1_c3), .en(rom_1_data[30]), .clk(clock_1_out), .Q(register_41_q), .clr(rom_1_data[29]));
  Register #(.width(16)) register_42 (
    .D(tiling_core_4x4_1_c7), .en(rom_1_data[30]), .clk(clock_1_out), .Q(register_42_q), .clr(rom_1_data[29]));
  Register #(.width(16)) register_43 (
    .D(tiling_core_4x4_1_c11), .en(rom_1_data[30]), .clk(clock_1_out), .Q(register_43_q), .clr(rom_1_data[29]));
  Register #(.width(16)) register_44 (
    .D(tiling_core_4x4_1_c15), .en(rom_1_data[30]), .clk(clock_1_out), .Q(register_44_q), .clr(rom_1_data[29]));
  assign controlled_buffer_1_out = rom_1_data[25] ? register_41_q : 16'bz;  // Controlled_Buffer controlled_buffer_9
  assign controlled_buffer_2_out = rom_1_data[25] ? register_42_q : 16'bz;  // Controlled_Buffer controlled_buffer_10
  assign controlled_buffer_3_out = rom_1_data[25] ? register_43_q : 16'bz;  // Controlled_Buffer controlled_buffer_11
  assign controlled_buffer_4_out = rom_1_data[25] ? register_44_q : 16'bz;  // Controlled_Buffer controlled_buffer_12
  Register #(.width(16)) register_45 (
    .D(tiling_core_4x4_1_c4), .en(rom_1_data[30]), .clk(clock_1_out), .Q(register_45_q), .clr(rom_1_data[29]));
  Register #(.width(16)) register_46 (
    .D(tiling_core_4x4_1_c8), .en(rom_1_data[30]), .clk(clock_1_out), .Q(register_46_q), .clr(rom_1_data[29]));
  Register #(.width(16)) register_47 (
    .D(tiling_core_4x4_1_c12), .en(rom_1_data[30]), .clk(clock_1_out), .Q(register_47_q), .clr(rom_1_data[29]));
  Register #(.width(16)) register_48 (
    .D(tiling_core_4x4_1_c16), .en(rom_1_data[30]), .clk(clock_1_out), .Q(register_48_q), .clr(rom_1_data[29]));
  assign controlled_buffer_1_out = rom_1_data[24] ? register_45_q : 16'bz;  // Controlled_Buffer controlled_buffer_13
  assign controlled_buffer_2_out = rom_1_data[24] ? register_46_q : 16'bz;  // Controlled_Buffer controlled_buffer_14
  assign controlled_buffer_3_out = rom_1_data[24] ? register_47_q : 16'bz;  // Controlled_Buffer controlled_buffer_15
  assign controlled_buffer_4_out = rom_1_data[24] ? register_48_q : 16'bz;  // Controlled_Buffer controlled_buffer_16
  Counter counter_3 (
    .count(rom_1_data[22]), .Q(counter_3_q), .clk(clock_1_out), .clr(rom_1_data[28]));  // open: load, D, carry, up
  Counter counter_4 (
    .count(rom_1_data[21]), .Q(counter_4_q), .clk(clock_1_out), .clr(rom_1_data[28]));  // open: load, D, carry, up
  Counter counter_5 (
    .count(rom_1_data[20]), .Q(counter_5_q), .clk(clock_1_out), .clr(rom_1_data[28]));  // open: load, D, carry, up
  Counter counter_6 (
    .count(rom_1_data[23]), .Q(counter_6_q), .clk(clock_1_out), .clr(rom_1_data[28]));  // open: load, D, carry, up
  RAM #(.dataWidth(16), .\type ("nonvolatile")) ram_3 (
    .addr(counter_6_q), .we(rom_1_data[23]), .oe(rom_1_data[23]), .clk(clock_1_out),
    .din(controlled_buffer_1_out), .dout(ram_3_dout));
  RAM #(.dataWidth(16), .\type ("nonvolatile")) ram_4 (
    .addr(counter_3_q), .we(rom_1_data[22]), .oe(rom_1_data[22]), .clk(clock_1_out),
    .din(controlled_buffer_2_out), .dout(ram_4_dout));
  RAM #(.dataWidth(16), .\type ("nonvolatile")) ram_5 (
    .addr(counter_4_q), .we(rom_1_data[21]), .oe(rom_1_data[21]), .clk(clock_1_out),
    .din(controlled_buffer_3_out), .dout(ram_5_dout));
  RAM #(.dataWidth(16), .\type ("nonvolatile")) ram_6 (
    .addr(counter_5_q), .we(rom_1_data[20]), .oe(rom_1_data[20]), .clk(clock_1_out),
    .din(controlled_buffer_4_out), .dout(ram_6_dout));
  Counter counter_7 (.Q(counter_7_q), .clk(clock_1_out), .clr(rom_1_data[15]));  // open: load, D, count, carry, up
  ROM #(.addrWidth(16), .dataWidth(64)) rom_1 (.addr({register_49_q_2, counter_7_q}), .data(rom_1_data));
  assign controlled_buffer_17_out = rom_1_data[17] ? ram_5_dout : 16'bz;  // Controlled_Buffer controlled_buffer_17
  assign controlled_buffer_17_out = rom_1_data[16] ? ram_6_dout : 16'bz;  // Controlled_Buffer controlled_buffer_18
  assign controlled_buffer_17_out = rom_1_data[19] ? ram_3_dout : 16'bz;  // Controlled_Buffer controlled_buffer_19
  assign controlled_buffer_17_out = rom_1_data[18] ? ram_4_dout : 16'bz;  // Controlled_Buffer controlled_buffer_20
  Counter counter_8 (.count(rom_1_data[11]), .Q(counter_8_q), .clk(clock_1_out));  // open: load, D, carry, up, clr
  RAM #(.dataWidth(16), .\type ("nonvolatile")) ram_7 (
    .addr(counter_8_q), .oe(rom_1_data[11]), .clk(clock_1_out), .dout(ram_7_dout));  // open: we, din
  not not_1 (not_1_out, rom_1_data[11]);
  or or_1 (or_1_out, rom_1_data[19], rom_1_data[18], rom_1_data[17], rom_1_data[16]);
  Counter counter_9 (.count(or_1_out), .Q(counter_9_q), .clk(clock_1_out));  // open: load, D, carry, up, clr
  RAM #(.dataWidth(16)) ram_8 (
    .addr(counter_9_q), .we(or_1_out), .clk(clock_1_out), .din(controlled_buffer_17_out));  // open: oe, dout
  Register #(.width(16)) register_49 (
    .D(ram_7_dout), .en(not_1_out), .clk(clock_1_out),
    .Q({register_49_q_2[11:8], register_49_q_2[15:12], register_49_q}), .clr(rom_1_data[15]));
endmodule
module tiling_core_4x4 (
  input  [15:0] a1,
  input  [15:0] a2,
  input  [15:0] a3,
  input  [15:0] a4,
  input  [15:0] a5,
  input  [15:0] a6,
  input  [15:0] a7,
  input  [15:0] a8,
  input  [15:0] a9,
  input  [15:0] a10,
  input  [15:0] a11,
  input  [15:0] a12,
  input  [15:0] a13,
  input  [15:0] a14,
  input  [15:0] a15,
  input  [15:0] a16,
  input  [15:0] b1,
  input  [15:0] b5,
  input  [15:0] b9,
  input  [15:0] b13,
  input  [15:0] b2,
  input  [15:0] b6,
  input  [15:0] b10,
  input  [15:0] b14,
  input  [15:0] b3,
  input  [15:0] b7,
  input  [15:0] b11,
  input  [15:0] b15,
  input  [15:0] b4,
  input  [15:0] b8,
  input  [15:0] b12,
  input  [15:0] b16,
  input  [15:0] s1,
  input  [15:0] s2,
  input  [15:0] s3,
  input  [15:0] s4,
  input  [15:0] s5,
  input  [15:0] s6,
  input  [15:0] s7,
  input  [15:0] s8,
  input  [15:0] s9,
  input  [15:0] s10,
  input  [15:0] s11,
  input  [15:0] s12,
  input  [15:0] s13,
  input  [15:0] s14,
  input  [15:0] s15,
  input  [15:0] s16,
  output [15:0] c1,
  output [15:0] c2,
  output [15:0] c3,
  output [15:0] c4,
  output [15:0] c5,
  output [15:0] c6,
  output [15:0] c7,
  output [15:0] c8,
  output [15:0] c9,
  output [15:0] c10,
  output [15:0] c11,
  output [15:0] c12,
  output [15:0] c13,
  output [15:0] c14,
  output [15:0] c15,
  output [15:0] c16
);

  wire [15:0] adder_1_out, adder_2_out, adder_3_out, adder_4_out, adder_5_out, adder_6_out, adder_7_out,
       adder_8_out, adder_9_out, adder_10_out, adder_11_out, adder_12_out, adder_13_out, adder_14_out,
       adder_15_out, adder_16_out, adder_17_out, adder_18_out, adder_19_out, adder_20_out, adder_21_out,
       adder_22_out, adder_23_out, adder_24_out, adder_25_out, adder_26_out, adder_27_out, adder_28_out,
       adder_29_out, adder_30_out, adder_31_out, adder_32_out, adder_33_out, adder_34_out, adder_35_out,
       adder_36_out, adder_37_out, adder_38_out, adder_39_out, adder_40_out, adder_41_out, adder_42_out,
       adder_43_out, adder_44_out, adder_45_out, adder_46_out, adder_47_out, adder_48_out, multiplier_1_out,
       multiplier_2_out, multiplier_3_out, multiplier_4_out, multiplier_5_out, multiplier_6_out,
       multiplier_7_out, multiplier_8_out, multiplier_9_out, multiplier_10_out, multiplier_11_out,
       multiplier_12_out, multiplier_13_out, multiplier_14_out, multiplier_15_out, multiplier_16_out,
       multiplier_17_out, multiplier_18_out, multiplier_19_out, multiplier_20_out, multiplier_21_out,
       multiplier_22_out, multiplier_23_out, multiplier_24_out, multiplier_25_out, multiplier_26_out,
       multiplier_27_out, multiplier_28_out, multiplier_29_out, multiplier_30_out, multiplier_31_out,
       multiplier_32_out, multiplier_33_out, multiplier_34_out, multiplier_35_out, multiplier_36_out,
       multiplier_37_out, multiplier_38_out, multiplier_39_out, multiplier_40_out, multiplier_41_out,
       multiplier_42_out, multiplier_43_out, multiplier_44_out, multiplier_45_out, multiplier_46_out,
       multiplier_47_out, multiplier_48_out, multiplier_49_out, multiplier_50_out, multiplier_51_out,
       multiplier_52_out, multiplier_53_out, multiplier_54_out, multiplier_55_out, multiplier_56_out,
       multiplier_57_out, multiplier_58_out, multiplier_59_out, multiplier_60_out, multiplier_61_out,
       multiplier_62_out, multiplier_63_out, multiplier_64_out;

  Multiplier #(.width(16)) multiplier_1 (.a(a1), .b(b1), .out(multiplier_1_out));  // open: cin, cout
  Multiplier #(.width(16)) multiplier_2 (.a(a2), .b(b5), .out(multiplier_2_out));  // open: cin, cout
  Multiplier #(.width(16)) multiplier_3 (.a(a3), .b(b9), .out(multiplier_3_out));  // open: cin, cout
  Multiplier #(.width(16)) multiplier_4 (.a(a4), .b(b13), .out(multiplier_4_out));  // open: cin, cout
  Multiplier #(.width(16)) multiplier_5 (.a(a1), .b(b2), .out(multiplier_5_out));  // open: cin, cout
  Multiplier #(.width(16)) multiplier_6 (.a(a2), .b(b6), .out(multiplier_6_out));  // open: cin, cout
  Multiplier #(.width(16)) multiplier_7 (.a(a3), .b(b10), .out(multiplier_7_out));  // open: cin, cout
  Multiplier #(.width(16)) multiplier_8 (.a(a4), .b(b14), .out(multiplier_8_out));  // open: cin, cout
  Multiplier #(.width(16)) multiplier_9 (.a(a1), .b(b3), .out(multiplier_9_out));  // open: cin, cout
  Multiplier #(.width(16)) multiplier_10 (.a(a2), .b(b7), .out(multiplier_10_out));  // open: cin, cout
  Multiplier #(.width(16)) multiplier_11 (.a(a3), .b(b11), .out(multiplier_11_out));  // open: cin, cout
  Multiplier #(.width(16)) multiplier_12 (.a(a4), .b(b15), .out(multiplier_12_out));  // open: cin, cout
  Multiplier #(.width(16)) multiplier_13 (.a(a1), .b(b4), .out(multiplier_13_out));  // open: cin, cout
  Multiplier #(.width(16)) multiplier_14 (.a(a2), .b(b8), .out(multiplier_14_out));  // open: cin, cout
  Multiplier #(.width(16)) multiplier_15 (.a(a3), .b(b12), .out(multiplier_15_out));  // open: cin, cout
  Multiplier #(.width(16)) multiplier_16 (.a(a4), .b(b16), .out(multiplier_16_out));  // open: cin, cout
  Adder #(.width(16)) adder_1 (.a(multiplier_1_out), .b(multiplier_2_out), .out(adder_1_out));  // open: cin, cout
  Adder #(.width(16)) adder_2 (.a(adder_1_out), .b(adder_3_out), .out(adder_2_out));  // open: cin, cout
  Adder #(.width(16)) adder_3 (.a(multiplier_3_out), .b(multiplier_4_out), .out(adder_3_out));  // open: cin, cout
  Adder #(.width(16)) adder_4 (.a(multiplier_5_out), .b(multiplier_6_out), .out(adder_4_out));  // open: cin, cout
  Adder #(.width(16)) adder_5 (.a(adder_4_out), .b(adder_6_out), .out(adder_5_out));  // open: cin, cout
  Adder #(.width(16)) adder_6 (.a(multiplier_7_out), .b(multiplier_8_out), .out(adder_6_out));  // open: cin, cout
  Adder #(.width(16)) adder_7 (.a(multiplier_9_out), .b(multiplier_10_out), .out(adder_7_out));  // open: cin, cout
  Adder #(.width(16)) adder_8 (.a(adder_7_out), .b(adder_9_out), .out(adder_8_out));  // open: cin, cout
  Adder #(.width(16)) adder_9 (.a(multiplier_11_out), .b(multiplier_12_out), .out(adder_9_out));  // open: cin, cout
  Adder #(.width(16)) adder_10 (.a(multiplier_13_out), .b(multiplier_14_out), .out(adder_10_out));  // open: cin, cout
  Adder #(.width(16)) adder_11 (.a(adder_10_out), .b(adder_12_out), .out(adder_11_out));  // open: cin, cout
  Adder #(.width(16)) adder_12 (.a(multiplier_15_out), .b(multiplier_16_out), .out(adder_12_out));  // open: cin, cout
  Multiplier #(.width(16)) multiplier_17 (.a(a5), .b(b1), .out(multiplier_17_out));  // open: cin, cout
  Adder #(.width(16)) adder_13 (.a(multiplier_17_out), .b(multiplier_18_out), .out(adder_13_out));  // open: cin, cout
  Multiplier #(.width(16)) multiplier_18 (.a(a6), .b(b5), .out(multiplier_18_out));  // open: cin, cout
  Multiplier #(.width(16)) multiplier_19 (.a(a7), .b(b9), .out(multiplier_19_out));  // open: cin, cout
  Adder #(.width(16)) adder_14 (.a(multiplier_19_out), .b(multiplier_20_out), .out(adder_14_out));  // open: cin, cout
  Multiplier #(.width(16)) multiplier_20 (.a(a8), .b(b13), .out(multiplier_20_out));  // open: cin, cout
  Multiplier #(.width(16)) multiplier_21 (.a(a5), .b(b2), .out(multiplier_21_out));  // open: cin, cout
  Adder #(.width(16)) adder_15 (.a(multiplier_21_out), .b(multiplier_22_out), .out(adder_15_out));  // open: cin, cout
  Multiplier #(.width(16)) multiplier_22 (.a(a6), .b(b6), .out(multiplier_22_out));  // open: cin, cout
  Multiplier #(.width(16)) multiplier_23 (.a(a7), .b(b10), .out(multiplier_23_out));  // open: cin, cout
  Adder #(.width(16)) adder_16 (.a(multiplier_23_out), .b(multiplier_24_out), .out(adder_16_out));  // open: cin, cout
  Multiplier #(.width(16)) multiplier_24 (.a(a8), .b(b14), .out(multiplier_24_out));  // open: cin, cout
  Multiplier #(.width(16)) multiplier_25 (.a(a5), .b(b3), .out(multiplier_25_out));  // open: cin, cout
  Adder #(.width(16)) adder_17 (.a(multiplier_25_out), .b(multiplier_26_out), .out(adder_17_out));  // open: cin, cout
  Multiplier #(.width(16)) multiplier_26 (.a(a6), .b(b7), .out(multiplier_26_out));  // open: cin, cout
  Multiplier #(.width(16)) multiplier_27 (.a(a7), .b(b11), .out(multiplier_27_out));  // open: cin, cout
  Adder #(.width(16)) adder_18 (.a(multiplier_27_out), .b(multiplier_28_out), .out(adder_18_out));  // open: cin, cout
  Multiplier #(.width(16)) multiplier_28 (.a(a8), .b(b15), .out(multiplier_28_out));  // open: cin, cout
  Multiplier #(.width(16)) multiplier_29 (.a(a5), .b(b4), .out(multiplier_29_out));  // open: cin, cout
  Adder #(.width(16)) adder_19 (.a(multiplier_29_out), .b(multiplier_30_out), .out(adder_19_out));  // open: cin, cout
  Multiplier #(.width(16)) multiplier_30 (.a(a6), .b(b8), .out(multiplier_30_out));  // open: cin, cout
  Multiplier #(.width(16)) multiplier_31 (.a(a7), .b(b12), .out(multiplier_31_out));  // open: cin, cout
  Adder #(.width(16)) adder_20 (.a(multiplier_31_out), .b(multiplier_32_out), .out(adder_20_out));  // open: cin, cout
  Multiplier #(.width(16)) multiplier_32 (.a(a8), .b(b16), .out(multiplier_32_out));  // open: cin, cout
  Adder #(.width(16)) adder_21 (.a(adder_13_out), .b(adder_14_out), .out(adder_21_out));  // open: cin, cout
  Adder #(.width(16)) adder_22 (.a(adder_15_out), .b(adder_16_out), .out(adder_22_out));  // open: cin, cout
  Adder #(.width(16)) adder_23 (.a(adder_17_out), .b(adder_18_out), .out(adder_23_out));  // open: cin, cout
  Adder #(.width(16)) adder_24 (.a(adder_19_out), .b(adder_20_out), .out(adder_24_out));  // open: cin, cout
  Multiplier #(.width(16)) multiplier_33 (.a(a9), .b(b1), .out(multiplier_33_out));  // open: cin, cout
  Multiplier #(.width(16)) multiplier_34 (.a(a10), .b(b5), .out(multiplier_34_out));  // open: cin, cout
  Multiplier #(.width(16)) multiplier_35 (.a(a11), .b(b9), .out(multiplier_35_out));  // open: cin, cout
  Multiplier #(.width(16)) multiplier_36 (.a(a12), .b(b13), .out(multiplier_36_out));  // open: cin, cout
  Multiplier #(.width(16)) multiplier_37 (.a(a9), .b(b2), .out(multiplier_37_out));  // open: cin, cout
  Multiplier #(.width(16)) multiplier_38 (.a(a10), .b(b6), .out(multiplier_38_out));  // open: cin, cout
  Multiplier #(.width(16)) multiplier_39 (.a(a11), .b(b10), .out(multiplier_39_out));  // open: cin, cout
  Multiplier #(.width(16)) multiplier_40 (.a(a12), .b(b14), .out(multiplier_40_out));  // open: cin, cout
  Multiplier #(.width(16)) multiplier_41 (.a(a9), .b(b3), .out(multiplier_41_out));  // open: cin, cout
  Multiplier #(.width(16)) multiplier_42 (.a(a10), .b(b7), .out(multiplier_42_out));  // open: cin, cout
  Multiplier #(.width(16)) multiplier_43 (.a(a11), .b(b11), .out(multiplier_43_out));  // open: cin, cout
  Multiplier #(.width(16)) multiplier_44 (.a(a12), .b(b15), .out(multiplier_44_out));  // open: cin, cout
  Multiplier #(.width(16)) multiplier_45 (.a(a9), .b(b4), .out(multiplier_45_out));  // open: cin, cout
  Multiplier #(.width(16)) multiplier_46 (.a(a10), .b(b8), .out(multiplier_46_out));  // open: cin, cout
  Multiplier #(.width(16)) multiplier_47 (.a(a11), .b(b12), .out(multiplier_47_out));  // open: cin, cout
  Multiplier #(.width(16)) multiplier_48 (.a(a12), .b(b16), .out(multiplier_48_out));  // open: cin, cout
  Adder #(.width(16)) adder_25 (.a(multiplier_33_out), .b(multiplier_34_out), .out(adder_25_out));  // open: cin, cout
  Adder #(.width(16)) adder_26 (.a(multiplier_35_out), .b(multiplier_36_out), .out(adder_26_out));  // open: cin, cout
  Adder #(.width(16)) adder_27 (.a(multiplier_37_out), .b(multiplier_38_out), .out(adder_27_out));  // open: cin, cout
  Adder #(.width(16)) adder_28 (.a(multiplier_39_out), .b(multiplier_40_out), .out(adder_28_out));  // open: cin, cout
  Adder #(.width(16)) adder_29 (.a(multiplier_41_out), .b(multiplier_42_out), .out(adder_29_out));  // open: cin, cout
  Adder #(.width(16)) adder_30 (.a(multiplier_43_out), .b(multiplier_44_out), .out(adder_30_out));  // open: cin, cout
  Adder #(.width(16)) adder_31 (.a(multiplier_45_out), .b(multiplier_46_out), .out(adder_31_out));  // open: cin, cout
  Adder #(.width(16)) adder_32 (.a(multiplier_47_out), .b(multiplier_48_out), .out(adder_32_out));  // open: cin, cout
  Adder #(.width(16)) adder_33 (.a(adder_25_out), .b(adder_26_out), .out(adder_33_out));  // open: cin, cout
  Adder #(.width(16)) adder_34 (.a(adder_27_out), .b(adder_28_out), .out(adder_34_out));  // open: cin, cout
  Adder #(.width(16)) adder_35 (.a(adder_29_out), .b(adder_30_out), .out(adder_35_out));  // open: cin, cout
  Adder #(.width(16)) adder_36 (.a(adder_31_out), .b(adder_32_out), .out(adder_36_out));  // open: cin, cout
  Multiplier #(.width(16)) multiplier_49 (.a(a13), .b(b1), .out(multiplier_49_out));  // open: cin, cout
  Multiplier #(.width(16)) multiplier_50 (.a(a14), .b(b5), .out(multiplier_50_out));  // open: cin, cout
  Multiplier #(.width(16)) multiplier_51 (.a(a15), .b(b9), .out(multiplier_51_out));  // open: cin, cout
  Multiplier #(.width(16)) multiplier_52 (.a(a16), .b(b13), .out(multiplier_52_out));  // open: cin, cout
  Multiplier #(.width(16)) multiplier_53 (.a(a13), .b(b2), .out(multiplier_53_out));  // open: cin, cout
  Multiplier #(.width(16)) multiplier_54 (.a(a14), .b(b6), .out(multiplier_54_out));  // open: cin, cout
  Multiplier #(.width(16)) multiplier_55 (.a(a15), .b(b10), .out(multiplier_55_out));  // open: cin, cout
  Multiplier #(.width(16)) multiplier_56 (.a(a16), .b(b14), .out(multiplier_56_out));  // open: cin, cout
  Multiplier #(.width(16)) multiplier_57 (.a(a13), .b(b3), .out(multiplier_57_out));  // open: cin, cout
  Multiplier #(.width(16)) multiplier_58 (.a(a14), .b(b7), .out(multiplier_58_out));  // open: cin, cout
  Multiplier #(.width(16)) multiplier_59 (.a(a15), .b(b11), .out(multiplier_59_out));  // open: cin, cout
  Multiplier #(.width(16)) multiplier_60 (.a(a16), .b(b15), .out(multiplier_60_out));  // open: cin, cout
  Multiplier #(.width(16)) multiplier_61 (.a(a13), .b(b4), .out(multiplier_61_out));  // open: cin, cout
  Multiplier #(.width(16)) multiplier_62 (.a(a14), .b(b8), .out(multiplier_62_out));  // open: cin, cout
  Multiplier #(.width(16)) multiplier_63 (.a(a15), .b(b12), .out(multiplier_63_out));  // open: cin, cout
  Multiplier #(.width(16)) multiplier_64 (.a(a16), .b(b16), .out(multiplier_64_out));  // open: cin, cout
  Adder #(.width(16)) adder_37 (.a(multiplier_49_out), .b(multiplier_50_out), .out(adder_37_out));  // open: cin, cout
  Adder #(.width(16)) adder_38 (.a(multiplier_51_out), .b(multiplier_52_out), .out(adder_38_out));  // open: cin, cout
  Adder #(.width(16)) adder_39 (.a(multiplier_53_out), .b(multiplier_54_out), .out(adder_39_out));  // open: cin, cout
  Adder #(.width(16)) adder_40 (.a(multiplier_55_out), .b(multiplier_56_out), .out(adder_40_out));  // open: cin, cout
  Adder #(.width(16)) adder_41 (.a(multiplier_57_out), .b(multiplier_58_out), .out(adder_41_out));  // open: cin, cout
  Adder #(.width(16)) adder_42 (.a(multiplier_59_out), .b(multiplier_60_out), .out(adder_42_out));  // open: cin, cout
  Adder #(.width(16)) adder_43 (.a(multiplier_61_out), .b(multiplier_62_out), .out(adder_43_out));  // open: cin, cout
  Adder #(.width(16)) adder_44 (.a(multiplier_63_out), .b(multiplier_64_out), .out(adder_44_out));  // open: cin, cout
  Adder #(.width(16)) adder_45 (.a(adder_37_out), .b(adder_38_out), .out(adder_45_out));  // open: cin, cout
  Adder #(.width(16)) adder_46 (.a(adder_39_out), .b(adder_40_out), .out(adder_46_out));  // open: cin, cout
  Adder #(.width(16)) adder_47 (.a(adder_41_out), .b(adder_42_out), .out(adder_47_out));  // open: cin, cout
  Adder #(.width(16)) adder_48 (.a(adder_43_out), .b(adder_44_out), .out(adder_48_out));  // open: cin, cout
  Adder #(.width(16)) adder_49 (.a(adder_2_out), .b(s1), .out(c1));  // open: cin, cout
  Adder #(.width(16)) adder_50 (.a(adder_21_out), .b(s5), .out(c5));  // open: cin, cout
  Adder #(.width(16)) adder_51 (.a(s9), .b(adder_33_out), .out(c9));  // open: cin, cout
  Adder #(.width(16)) adder_52 (.a(s13), .b(adder_45_out), .out(c13));  // open: cin, cout
  Adder #(.width(16)) adder_53 (.a(adder_5_out), .b(s2), .out(c2));  // open: cin, cout
  Adder #(.width(16)) adder_54 (.a(adder_22_out), .b(s6), .out(c6));  // open: cin, cout
  Adder #(.width(16)) adder_55 (.a(s10), .b(adder_34_out), .out(c10));  // open: cin, cout
  Adder #(.width(16)) adder_56 (.a(s14), .b(adder_46_out), .out(c14));  // open: cin, cout
  Adder #(.width(16)) adder_57 (.a(adder_8_out), .b(s3), .out(c3));  // open: cin, cout
  Adder #(.width(16)) adder_58 (.a(adder_23_out), .b(s7), .out(c7));  // open: cin, cout
  Adder #(.width(16)) adder_59 (.a(s11), .b(adder_35_out), .out(c11));  // open: cin, cout
  Adder #(.width(16)) adder_60 (.a(s15), .b(adder_47_out), .out(c15));  // open: cin, cout
  Adder #(.width(16)) adder_61 (.a(adder_11_out), .b(s4), .out(c4));  // open: cin, cout
  Adder #(.width(16)) adder_62 (.a(adder_24_out), .b(s8), .out(c8));  // open: cin, cout
  Adder #(.width(16)) adder_63 (.a(s12), .b(adder_36_out), .out(c12));  // open: cin, cout
  Adder #(.width(16)) adder_64 (.a(s16), .b(adder_48_out), .out(c16));  // open: cin, cout
endmodule

module RxC_iram (
);

  wire and_1_out, and_2_out, and_3_out, and_4_out, and_5_out, and_6_out, and_7_out, and_8_out, and_9_out,
       and_10_out, and_11_out, and_12_out, and_13_out, and_14_out, and_16_out, clock_1_out, not_1_out,
       or_1_out, or_2_out, or_3_out;
  wire [3:0] counter_3_q, counter_3_q_2;
  wire [7:0] counter_1_q, counter_2_q, counter_4_q, counter_5_q, counter_6_q, register_49_q;
  wire [15:0] controlled_buffer_1_out, controlled_buffer_3_out, controlled_buffer_4_out,
       controlled_buffer_5_out, controlled_buffer_6_out, controlled_buffer_9_out, controlled_buffer_17_out,
       controlled_buffer_25_out, controlled_buffer_33_out, matrix_multiplier_1_cl1, ram_1_dout, ram_2_dout,
       ram_3_dout, ram_4_dout, ram_5_dout, ram_6_dout, ram_7_dout, ram_8_dout, ram_10_dout, register_1_q,
       register_2_q, register_3_q, register_4_q, register_5_q, register_6_q, register_7_q, register_8_q,
       register_9_q, register_10_q, register_11_q, register_12_q, register_13_q, register_14_q,
       register_15_q, register_16_q, register_17_q, register_18_q, register_19_q, register_20_q,
       register_21_q, register_22_q, register_23_q, register_24_q, register_25_q, register_26_q,
       register_27_q, register_28_q, register_29_q, register_30_q, register_31_q, register_32_q,
       register_33_q, register_34_q, register_35_q, register_36_q, register_37_q, register_38_q,
       register_39_q, register_40_q, register_41_q, register_42_q, register_43_q, register_44_q,
       register_45_q, register_46_q, register_47_q, register_48_q;
  wire [15:8] register_49_q_2;
  wire [47:0] rom_1_data;

  or or_1 (or_1_out, rom_1_data[47], rom_1_data[46], rom_1_data[45], rom_1_data[44]);
  or or_2 (or_2_out, rom_1_data[43], rom_1_data[42], rom_1_data[41], rom_1_data[40]);
  Counter counter_1 (
    .count(or_1_out), .Q(counter_1_q), .up(1'b1), .clk(clock_1_out), .clr(rom_1_data[3]));  // open: load, D, carry
  Counter counter_2 (
    .count(or_2_out), .Q(counter_2_q), .up(1'b1), .clk(clock_1_out), .clr(rom_1_data[15]));  // open: load, D, carry
  RAM #(.addrWidth(12), .dataWidth(16), .\type ("nonvolatile")) ram_1 (
    .addr({register_49_q[7:4], counter_1_q}), .oe(or_1_out), .clk(clock_1_out), .dout(ram_1_dout));  // open: we, din
  RAM #(.addrWidth(12), .dataWidth(16), .\type ("nonvolatile")) ram_2 (
    .addr({register_49_q[7:4], counter_1_q}), .oe(or_1_out), .clk(clock_1_out), .dout(ram_2_dout));  // open: we, din
  RAM #(.addrWidth(12), .dataWidth(16), .\type ("nonvolatile")) ram_3 (
    .addr({register_49_q[7:4], counter_1_q}), .oe(or_1_out), .clk(clock_1_out), .dout(ram_3_dout));  // open: we, din
  RAM #(.addrWidth(12), .dataWidth(16), .\type ("nonvolatile")) ram_4 (
    .addr({register_49_q[7:4], counter_1_q}), .oe(or_1_out), .clk(clock_1_out), .dout(ram_4_dout));  // open: we, din
  RAM #(.addrWidth(12), .dataWidth(16), .\type ("nonvolatile")) ram_5 (
    .addr({register_49_q[3:0], counter_2_q}), .oe(or_2_out), .clk(clock_1_out), .dout(ram_5_dout));  // open: we, din
  RAM #(.addrWidth(12), .dataWidth(16), .\type ("nonvolatile")) ram_6 (
    .addr({register_49_q[3:0], counter_2_q}), .oe(or_2_out), .clk(clock_1_out), .dout(ram_6_dout));  // open: we, din
  RAM #(.addrWidth(12), .dataWidth(16), .\type ("nonvolatile")) ram_7 (
    .addr({register_49_q[3:0], counter_2_q}), .oe(or_2_out), .clk(clock_1_out), .dout(ram_7_dout));  // open: we, din
  RAM #(.addrWidth(12), .dataWidth(16), .\type ("nonvolatile")) ram_8 (
    .addr({register_49_q[3:0], counter_2_q}), .oe(or_2_out), .clk(clock_1_out), .dout(ram_8_dout));  // open: we, din
  Register #(.width(16)) register_1 (
    .D(ram_1_dout), .en(rom_1_data[47]), .clk(clock_1_out), .Q(register_1_q));  // open: clr
  Register #(.width(16)) register_2 (
    .D(ram_2_dout), .en(rom_1_data[47]), .clk(clock_1_out), .Q(register_2_q));  // open: clr
  Register #(.width(16)) register_3 (
    .D(ram_3_dout), .en(rom_1_data[47]), .clk(clock_1_out), .Q(register_3_q));  // open: clr
  Register #(.width(16)) register_4 (
    .D(ram_4_dout), .en(rom_1_data[47]), .clk(clock_1_out), .Q(register_4_q));  // open: clr
  Register #(.width(16)) register_5 (
    .D(ram_5_dout), .en(rom_1_data[43]), .clk(clock_1_out), .Q(register_5_q));  // open: clr
  Register #(.width(16)) register_6 (
    .D(ram_6_dout), .en(rom_1_data[43]), .clk(clock_1_out), .Q(register_6_q));  // open: clr
  Register #(.width(16)) register_7 (
    .D(ram_7_dout), .en(rom_1_data[43]), .clk(clock_1_out), .Q(register_7_q));  // open: clr
  Register #(.width(16)) register_8 (
    .D(ram_8_dout), .en(rom_1_data[43]), .clk(clock_1_out), .Q(register_8_q));  // open: clr
  assign controlled_buffer_1_out = rom_1_data[37] ? register_3_q : 16'bz;  // Controlled_Buffer controlled_buffer_1
  assign controlled_buffer_1_out = rom_1_data[36] ? register_4_q : 16'bz;  // Controlled_Buffer controlled_buffer_2
  assign controlled_buffer_3_out = rom_1_data[35] ? register_5_q : 16'bz;  // Controlled_Buffer controlled_buffer_3
  assign controlled_buffer_4_out = rom_1_data[35] ? register_6_q : 16'bz;  // Controlled_Buffer controlled_buffer_4
  assign controlled_buffer_5_out = rom_1_data[35] ? register_7_q : 16'bz;  // Controlled_Buffer controlled_buffer_5
  assign controlled_buffer_6_out = rom_1_data[35] ? register_8_q : 16'bz;  // Controlled_Buffer controlled_buffer_6
  assign controlled_buffer_1_out = rom_1_data[39] ? register_1_q : 16'bz;  // Controlled_Buffer controlled_buffer_7
  assign controlled_buffer_1_out = rom_1_data[38] ? register_2_q : 16'bz;  // Controlled_Buffer controlled_buffer_8
  Clock clock_1 (.out(clock_1_out));
  Register #(.width(16)) register_9 (
    .D(ram_1_dout), .en(rom_1_data[46]), .clk(clock_1_out), .Q(register_9_q));  // open: clr
  Register #(.width(16)) register_10 (
    .D(ram_2_dout), .en(rom_1_data[46]), .clk(clock_1_out), .Q(register_10_q));  // open: clr
  Register #(.width(16)) register_11 (
    .D(ram_3_dout), .en(rom_1_data[46]), .clk(clock_1_out), .Q(register_11_q));  // open: clr
  Register #(.width(16)) register_12 (
    .D(ram_4_dout), .en(rom_1_data[46]), .clk(clock_1_out), .Q(register_12_q));  // open: clr
  Register #(.width(16)) register_13 (
    .D(ram_5_dout), .en(rom_1_data[42]), .clk(clock_1_out), .Q(register_13_q));  // open: clr
  Register #(.width(16)) register_14 (
    .D(ram_6_dout), .en(rom_1_data[42]), .clk(clock_1_out), .Q(register_14_q));  // open: clr
  Register #(.width(16)) register_15 (
    .D(ram_7_dout), .en(rom_1_data[42]), .clk(clock_1_out), .Q(register_15_q));  // open: clr
  Register #(.width(16)) register_16 (
    .D(ram_8_dout), .en(rom_1_data[42]), .clk(clock_1_out), .Q(register_16_q));  // open: clr
  assign controlled_buffer_9_out = rom_1_data[39] ? register_9_q : 16'bz;  // Controlled_Buffer controlled_buffer_9
  assign controlled_buffer_9_out = rom_1_data[38] ? register_10_q : 16'bz;  // Controlled_Buffer controlled_buffer_10
  assign controlled_buffer_9_out = rom_1_data[37] ? register_11_q : 16'bz;  // Controlled_Buffer controlled_buffer_11
  assign controlled_buffer_9_out = rom_1_data[36] ? register_12_q : 16'bz;  // Controlled_Buffer controlled_buffer_12
  assign controlled_buffer_3_out = rom_1_data[34] ? register_13_q : 16'bz;  // Controlled_Buffer controlled_buffer_13
  assign controlled_buffer_4_out = rom_1_data[34] ? register_14_q : 16'bz;  // Controlled_Buffer controlled_buffer_14
  assign controlled_buffer_5_out = rom_1_data[34] ? register_15_q : 16'bz;  // Controlled_Buffer controlled_buffer_15
  assign controlled_buffer_6_out = rom_1_data[34] ? register_16_q : 16'bz;  // Controlled_Buffer controlled_buffer_16
  Register #(.width(16)) register_17 (
    .D(ram_1_dout), .en(rom_1_data[45]), .clk(clock_1_out), .Q(register_17_q));  // open: clr
  Register #(.width(16)) register_18 (
    .D(ram_2_dout), .en(rom_1_data[45]), .clk(clock_1_out), .Q(register_18_q));  // open: clr
  Register #(.width(16)) register_19 (
    .D(ram_3_dout), .en(rom_1_data[45]), .clk(clock_1_out), .Q(register_19_q));  // open: clr
  Register #(.width(16)) register_20 (
    .D(ram_4_dout), .en(rom_1_data[45]), .clk(clock_1_out), .Q(register_20_q));  // open: clr
  Register #(.width(16)) register_21 (
    .D(ram_5_dout), .en(rom_1_data[41]), .clk(clock_1_out), .Q(register_21_q));  // open: clr
  Register #(.width(16)) register_22 (
    .D(ram_6_dout), .en(rom_1_data[41]), .clk(clock_1_out), .Q(register_22_q));  // open: clr
  Register #(.width(16)) register_23 (
    .D(ram_7_dout), .en(rom_1_data[41]), .clk(clock_1_out), .Q(register_23_q));  // open: clr
  Register #(.width(16)) register_24 (
    .D(ram_8_dout), .en(rom_1_data[41]), .clk(clock_1_out), .Q(register_24_q));  // open: clr
  assign controlled_buffer_17_out = rom_1_data[36] ? register_20_q : 16'bz;  // Controlled_Buffer controlled_buffer_17
  assign controlled_buffer_3_out = rom_1_data[33] ? register_21_q : 16'bz;  // Controlled_Buffer controlled_buffer_18
  assign controlled_buffer_4_out = rom_1_data[33] ? register_22_q : 16'bz;  // Controlled_Buffer controlled_buffer_19
  assign controlled_buffer_5_out = rom_1_data[33] ? register_23_q : 16'bz;  // Controlled_Buffer controlled_buffer_20
  assign controlled_buffer_6_out = rom_1_data[33] ? register_24_q : 16'bz;  // Controlled_Buffer controlled_buffer_21
  assign controlled_buffer_17_out = rom_1_data[39] ? register_17_q : 16'bz;  // Controlled_Buffer controlled_buffer_22
  assign controlled_buffer_17_out = rom_1_data[38] ? register_18_q : 16'bz;  // Controlled_Buffer controlled_buffer_23
  assign controlled_buffer_17_out = rom_1_data[37] ? register_19_q : 16'bz;  // Controlled_Buffer controlled_buffer_24
  Register #(.width(16)) register_25 (
    .D(ram_1_dout), .en(rom_1_data[44]), .clk(clock_1_out), .Q(register_25_q));  // open: clr
  Register #(.width(16)) register_26 (
    .D(ram_2_dout), .en(rom_1_data[44]), .clk(clock_1_out), .Q(register_26_q));  // open: clr
  Register #(.width(16)) register_27 (
    .D(ram_3_dout), .en(rom_1_data[44]), .clk(clock_1_out), .Q(register_27_q));  // open: clr
  Register #(.width(16)) register_28 (
    .D(ram_4_dout), .en(rom_1_data[44]), .clk(clock_1_out), .Q(register_28_q));  // open: clr
  Register #(.width(16)) register_29 (
    .D(ram_5_dout), .en(rom_1_data[40]), .clk(clock_1_out), .Q(register_29_q));  // open: clr
  Register #(.width(16)) register_30 (
    .D(ram_6_dout), .en(rom_1_data[40]), .clk(clock_1_out), .Q(register_30_q));  // open: clr
  Register #(.width(16)) register_31 (
    .D(ram_7_dout), .en(rom_1_data[40]), .clk(clock_1_out), .Q(register_31_q));  // open: clr
  Register #(.width(16)) register_32 (
    .D(ram_8_dout), .en(rom_1_data[40]), .clk(clock_1_out), .Q(register_32_q));  // open: clr
  assign controlled_buffer_25_out = rom_1_data[38] ? register_26_q : 16'bz;  // Controlled_Buffer controlled_buffer_25
  assign controlled_buffer_25_out = rom_1_data[37] ? register_27_q : 16'bz;  // Controlled_Buffer controlled_buffer_26
  assign controlled_buffer_25_out = rom_1_data[36] ? register_28_q : 16'bz;  // Controlled_Buffer controlled_buffer_27
  assign controlled_buffer_3_out = rom_1_data[32] ? register_29_q : 16'bz;  // Controlled_Buffer controlled_buffer_28
  assign controlled_buffer_4_out = rom_1_data[32] ? register_30_q : 16'bz;  // Controlled_Buffer controlled_buffer_29
  assign controlled_buffer_5_out = rom_1_data[32] ? register_31_q : 16'bz;  // Controlled_Buffer controlled_buffer_30
  assign controlled_buffer_6_out = rom_1_data[32] ? register_32_q : 16'bz;  // Controlled_Buffer controlled_buffer_31
  assign controlled_buffer_25_out = rom_1_data[39] ? register_25_q : 16'bz;  // Controlled_Buffer controlled_buffer_32
  and and_1 (and_1_out, rom_1_data[39], rom_1_data[35]);
  and and_2 (and_2_out, rom_1_data[39], rom_1_data[34]);
  and and_3 (and_3_out, rom_1_data[39], rom_1_data[33]);
  and and_4 (and_4_out, rom_1_data[39], rom_1_data[32]);
  and and_5 (and_5_out, rom_1_data[38], rom_1_data[35]);
  and and_6 (and_6_out, rom_1_data[38], rom_1_data[34]);
  and and_7 (and_7_out, rom_1_data[38], rom_1_data[33]);
  and and_8 (and_8_out, rom_1_data[38], rom_1_data[32]);
  and and_9 (and_9_out, rom_1_data[37], rom_1_data[35]);
  and and_10 (and_10_out, rom_1_data[37], rom_1_data[34]);
  and and_11 (and_11_out, rom_1_data[37], rom_1_data[33]);
  and and_12 (and_12_out, rom_1_data[37], rom_1_data[32]);
  and and_13 (and_13_out, rom_1_data[35], rom_1_data[36]);
  and and_14 (and_14_out, rom_1_data[34], rom_1_data[36]);
  and and_15 (rom_1_data[15], rom_1_data[33], rom_1_data[36]);
  and and_16 (and_16_out, rom_1_data[32], rom_1_data[36]);
  matrix_multiplier matrix_multiplier_1 (
    .A1(controlled_buffer_1_out), .A2(controlled_buffer_9_out), .A3(controlled_buffer_17_out),
    .A4(controlled_buffer_25_out), .B1(controlled_buffer_3_out), .B2(controlled_buffer_4_out),
    .B3(controlled_buffer_5_out), .B4(controlled_buffer_6_out), .Cl1(matrix_multiplier_1_cl1));
  Register #(.width(16)) register_33 (
    .D(matrix_multiplier_1_cl1), .en(and_1_out), .clk(clock_1_out), .Q(register_33_q));  // open: clr
  Register #(.width(16)) register_34 (
    .D(matrix_multiplier_1_cl1), .en(and_5_out), .clk(clock_1_out), .Q(register_34_q));  // open: clr
  Register #(.width(16)) register_35 (
    .D(matrix_multiplier_1_cl1), .en(and_9_out), .clk(clock_1_out), .Q(register_35_q));  // open: clr
  Register #(.width(16)) register_36 (
    .D(matrix_multiplier_1_cl1), .en(and_13_out), .clk(clock_1_out), .Q(register_36_q));  // open: clr
  assign controlled_buffer_33_out = rom_1_data[31] ? register_33_q : 16'bz;  // Controlled_Buffer controlled_buffer_33
  assign controlled_buffer_33_out = rom_1_data[27] ? register_34_q : 16'bz;  // Controlled_Buffer controlled_buffer_34
  assign controlled_buffer_33_out = rom_1_data[23] ? register_35_q : 16'bz;  // Controlled_Buffer controlled_buffer_35
  assign controlled_buffer_33_out = rom_1_data[19] ? register_36_q : 16'bz;  // Controlled_Buffer controlled_buffer_36
  Register #(.width(16)) register_37 (
    .D(matrix_multiplier_1_cl1), .en(and_2_out), .clk(clock_1_out), .Q(register_37_q));  // open: clr
  Register #(.width(16)) register_38 (
    .D(matrix_multiplier_1_cl1), .en(and_6_out), .clk(clock_1_out), .Q(register_38_q));  // open: clr
  Register #(.width(16)) register_39 (
    .D(matrix_multiplier_1_cl1), .en(and_10_out), .clk(clock_1_out), .Q(register_39_q));  // open: clr
  Register #(.width(16)) register_40 (
    .D(matrix_multiplier_1_cl1), .en(and_14_out), .clk(clock_1_out), .Q(register_40_q));  // open: clr
  assign controlled_buffer_33_out = rom_1_data[30] ? register_37_q : 16'bz;  // Controlled_Buffer controlled_buffer_37
  assign controlled_buffer_33_out = rom_1_data[26] ? register_38_q : 16'bz;  // Controlled_Buffer controlled_buffer_38
  assign controlled_buffer_33_out = rom_1_data[22] ? register_39_q : 16'bz;  // Controlled_Buffer controlled_buffer_39
  assign controlled_buffer_33_out = rom_1_data[18] ? register_40_q : 16'bz;  // Controlled_Buffer controlled_buffer_40
  Register #(.width(16)) register_41 (
    .D(matrix_multiplier_1_cl1), .en(and_3_out), .clk(clock_1_out), .Q(register_41_q));  // open: clr
  Register #(.width(16)) register_42 (
    .D(matrix_multiplier_1_cl1), .en(and_7_out), .clk(clock_1_out), .Q(register_42_q));  // open: clr
  Register #(.width(16)) register_43 (
    .D(matrix_multiplier_1_cl1), .en(and_11_out), .clk(clock_1_out), .Q(register_43_q));  // open: clr
  Register #(.width(16)) register_44 (
    .D(matrix_multiplier_1_cl1), .en(rom_1_data[15]), .clk(clock_1_out), .Q(register_44_q));  // open: clr
  assign controlled_buffer_33_out = rom_1_data[29] ? register_41_q : 16'bz;  // Controlled_Buffer controlled_buffer_41
  assign controlled_buffer_33_out = rom_1_data[25] ? register_42_q : 16'bz;  // Controlled_Buffer controlled_buffer_42
  assign controlled_buffer_33_out = rom_1_data[21] ? register_43_q : 16'bz;  // Controlled_Buffer controlled_buffer_43
  assign controlled_buffer_33_out = rom_1_data[17] ? register_44_q : 16'bz;  // Controlled_Buffer controlled_buffer_44
  Register #(.width(16)) register_45 (
    .D(matrix_multiplier_1_cl1), .en(and_4_out), .clk(clock_1_out), .Q(register_45_q));  // open: clr
  Register #(.width(16)) register_46 (
    .D(matrix_multiplier_1_cl1), .en(and_8_out), .clk(clock_1_out), .Q(register_46_q));  // open: clr
  Register #(.width(16)) register_47 (
    .D(matrix_multiplier_1_cl1), .en(and_12_out), .clk(clock_1_out), .Q(register_47_q));  // open: clr
  Register #(.width(16)) register_48 (
    .D(matrix_multiplier_1_cl1), .en(and_16_out), .clk(clock_1_out), .Q(register_48_q));  // open: clr
  assign controlled_buffer_33_out = rom_1_data[28] ? register_45_q : 16'bz;  // Controlled_Buffer controlled_buffer_45
  assign controlled_buffer_33_out = rom_1_data[24] ? register_46_q : 16'bz;  // Controlled_Buffer controlled_buffer_46
  assign controlled_buffer_33_out = rom_1_data[20] ? register_47_q : 16'bz;  // Controlled_Buffer controlled_buffer_47
  assign controlled_buffer_33_out = rom_1_data[16] ? register_48_q : 16'bz;  // Controlled_Buffer controlled_buffer_48
  Hex_Digit_Display hex_digit_display_1 (.value(counter_3_q_2));  // open: dp
  or or_3 (or_3_out, rom_1_data[31], rom_1_data[27], rom_1_data[23], rom_1_data[19], rom_1_data[30], rom_1_data[26], rom_1_data[22], rom_1_data[18], rom_1_data[29], rom_1_data[25], rom_1_data[21], rom_1_data[17], rom_1_data[28], rom_1_data[24], rom_1_data[20], rom_1_data[16]);
  Counter counter_3 (.Q({counter_3_q_2, counter_3_q}), .clk(clock_1_out));  // open: load, D, count, carry, up, clr
  Hex_Digit_Display hex_digit_display_2 (.value(counter_3_q));  // open: dp
  // Probe on {counter_3_q_2, counter_3_q}
  Counter counter_4 (.Q(counter_4_q), .clk(clock_1_out), .clr(rom_1_data[7]));  // open: load, D, count, carry, up
  Counter counter_5 (.count(or_3_out), .Q(counter_5_q), .up(1'b1), .clk(clock_1_out));  // open: load, D, carry, clr
  ROM #(.addrWidth(16), .dataWidth(48)) rom_1 (.addr({register_49_q_2, counter_4_q}), .data(rom_1_data));
  RAM #(.dataWidth(16)) ram_9 (
    .addr(counter_5_q), .we(or_3_out), .clk(clock_1_out), .din(controlled_buffer_33_out));  // open: oe, dout
  Counter counter_6 (.count(rom_1_data[11]), .Q(counter_6_q), .clk(clock_1_out));  // open: load, D, carry, up, clr
  RAM #(.dataWidth(16), .\type ("nonvolatile")) ram_10 (
    .addr(counter_6_q), .oe(rom_1_data[11]), .clk(clock_1_out), .dout(ram_10_dout));  // open: we, din
  not not_1 (not_1_out, rom_1_data[11]);
  Register #(.width(16)) register_49 (
    .D(ram_10_dout), .en(not_1_out), .clk(clock_1_out),
    .Q({register_49_q_2[11:8], register_49_q_2[15:12], register_49_q}), .clr(rom_1_data[7]));

  // Notes on the sheet:
  //   contents of rom_1 (hex, n*v repeats v):
  //   800 0 80 8447*0 800000000000 800000000000 400000000000 80 252*0 80000000000 80000000000 40000000000
  //   80 252*0 8800000000 8400000000 4800000000 4400000000 80 251*0 80000000 40000000 8000000 4000000 80
  //   3323*0 800000000000 800000000000 400000000000 200000000000 80 251*0 80000000000 80000000000
  //   40000000000 20000000000 80 251*0 8800000000 8400000000 8200000000 4800000000 4400000000 4200000000
  //   2800000000 2400000000 2200000000 80 246*0 80000000 40000000 20000000 8000000 4000000 2000000 800000
  //   400000 200000 80 3318*0 800000000000 800000000000 400000000000 200000000000 100000000000 80 250*0
  //   80000000000 80000000000 40000000000 20000000000 10000000000 80 250*0 8800000000 8400000000
  //   8200000000 8100000000 4800000000 4400000000 4200000000 4100000000 2800000000 2400000000 2200000000
  //   2100000000 1800000000 1400000000 1200000000 1100000000 80 239*0 80000000 40000000 20000000 10000000
  //   8000000 4000000 2000000 1000000 800000 400000 200000 100000 80000 40000 20000 10000 80
endmodule
