// Logisim project The_End_Game.circ as structural Verilog
module RnC_Tiling_Core (
  input  [15:0] a1,
  input  [15:0] a2,
  input  [15:0] a3,
  input  [15:0] a4,
  input  [15:0] a5,
  input  [15:0] a6,
  input  [15:0] a7,
  input  [15:0] a8,
  input  [15:0] a9,
  input  [15:0] a10,
  input  [15:0] a11,
  input  [15:0] a12,
  input  [15:0] a13,
  input  [15:0] a14,
  input  [15:0] a15,
  input  [15:0] a16,
  input  [15:0] b1,
  input  [15:0] b5,
  input  [15:0] b9,
  input  [15:0] b13,
  input  [15:0] b2,
  input  [15:0] b6,
  input  [15:0] b10,
  input  [15:0] b14,
  input  [15:0] b3,
  input  [15:0] b7,
  input  [15:0] b11,
  input  [15:0] b15,
  input  [15:0] b4,
  input  [15:0] b8,
  input  [15:0] b12,
  input  [15:0] b16,
  input  [15:0] s1,
  input  [15:0] s2,
  input  [15:0] s3,
  input  [15:0] s4,
  input  [15:0] s5,
  input  [15:0] s6,
  input  [15:0] s7,
  input  [15:0] s8,
  input  [15:0] s9,
  input  [15:0] s10,
  input  [15:0] s11,
  input  [15:0] s12,
  input  [15:0] s13,
  input  [15:0] s14,
  input  [15:0] s15,
  input  [15:0] s16,
  output [15:0] c1,
  output [15:0] c2,
  output [15:0] c3,
  output [15:0] c4,
  output [15:0] c5,
  output [15:0] c6,
  output [15:0] c7,
  output [15:0] c8,
  output [15:0] c9,
  output [15:0] c10,
  output [15:0] c11,
  output [15:0] c12,
  output [15:0] c13,
  output [15:0] c14,
  output [15:0] c15,
  output [15:0] c16
);

  wire [15:0] adder_1_out, adder_2_out, adder_3_out, adder_4_out, adder_5_out, adder_6_out, adder_7_out,
       adder_8_out, adder_9_out, adder_10_out, adder_11_out, adder_12_out, adder_17_out, adder_18_out,
       adder_19_out, adder_20_out, adder_21_out, adder_22_out, adder_23_out, adder_24_out, adder_25_out,
       adder_27_out, adder_28_out, adder_29_out, adder_33_out, adder_34_out, adder_35_out, adder_36_out,
       adder_37_out, adder_38_out, adder_39_out, adder_40_out, adder_41_out, adder_42_out, adder_43_out,
       adder_44_out, adder_49_out, adder_50_out, adder_51_out, adder_52_out, adder_53_out, adder_54_out,
       adder_55_out, adder_56_out, adder_57_out, adder_58_out, adder_59_out, adder_60_out, multiplier_1_out,
       multiplier_2_out, multiplier_3_out, multiplier_4_out, multiplier_5_out, multiplier_6_out,
       multiplier_7_out, multiplier_8_out, multiplier_9_out, multiplier_10_out, multiplier_11_out,
       multiplier_12_out, multiplier_13_out, multiplier_14_out, multiplier_15_out, multiplier_16_out,
       multiplier_17_out, multiplier_18_out, multiplier_19_out, multiplier_20_out, multiplier_21_out,
       multiplier_22_out, multiplier_23_out, multiplier_24_out, multiplier_25_out, multiplier_26_out,
       multiplier_27_out, multiplier_28_out, multiplier_29_out, multiplier_30_out, multiplier_31_out,
       multiplier_32_out, multiplier_33_out, multiplier_34_out, multiplier_35_out, multiplier_36_out,
       multiplier_37_out, multiplier_38_out, multiplier_39_out, multiplier_40_out, multiplier_41_out,
       multiplier_42_out, multiplier_43_out, multiplier_44_out, multiplier_45_out, multiplier_46_out,
       multiplier_47_out, multiplier_48_out, multiplier_49_out, multiplier_50_out, multiplier_51_out,
       multiplier_52_out, multiplier_53_out, multiplier_54_out, multiplier_55_out, multiplier_56_out,
       multiplier_57_out, multiplier_58_out, multiplier_59_out, multiplier_60_out, multiplier_61_out,
       multiplier_62_out, multiplier_63_out, multiplier_64_out;

  Multiplier #(.width(16)) multiplier_1 (.a(a1), .b(b1), .out(multiplier_1_out));  // open: cin, cout
  Multiplier #(.width(16)) multiplier_2 (.a(a2), .b(b5), .out(multiplier_2_out));  // open: cin, cout
  Multiplier #(.width(16)) multiplier_3 (.a(a3), .b(b9), .out(multiplier_3_out));  // open: cin, cout
  Multiplier #(.width(16)) multiplier_4 (.a(a4), .b(b13), .out(multiplier_4_out));  // open: cin, cout
  Multiplier #(.width(16)) multiplier_5 (.a(a1), .b(b2), .out(multiplier_5_out));  // open: cin, cout
  Multiplier #(.width(16)) multiplier_6 (.a(a2), .b(b6), .out(multiplier_6_out));  // open: cin, cout
  Multiplier #(.width(16)) multiplier_7 (.a(a3), .b(b10), .out(multiplier_7_out));  // open: cin, cout
  Multiplier #(.width(16)) multiplier_8 (.a(a4), .b(b14), .out(multiplier_8_out));  // open: cin, cout
  Multiplier #(.width(16)) multiplier_9 (.a(a1), .b(b3), .out(multiplier_9_out));  // open: cin, cout
  Multiplier #(.width(16)) multiplier_10 (.a(a2), .b(b7), .out(multiplier_10_out));  // open: cin, cout
  Multiplier #(.width(16)) multiplier_11 (.a(a3), .b(b11), .out(multiplier_11_out));  // open: cin, cout
  Multiplier #(.width(16)) multiplier_12 (.a(a4), .b(b15), .out(multiplier_12_out));  // open: cin, cout
  Multiplier #(.width(16)) multiplier_13 (.a(a1), .b(b4), .out(multiplier_13_out));  // open: cin, cout
  Multiplier #(.width(16)) multiplier_14 (.a(a2), .b(b8), .out(multiplier_14_out));  // open: cin, cout
  Multiplier #(.width(16)) multiplier_15 (.a(a3), .b(b12), .out(multiplier_15_out));  // open: cin, cout
  Multiplier #(.width(16)) multiplier_16 (.a(a4), .b(b16), .out(multiplier_16_out));  // open: cin, cout
  Adder #(.width(16)) adder_1 (.a(multiplier_1_out), .b(multiplier_2_out), .out(adder_1_out));  // open: cin, cout
  Adder #(.width(16)) adder_2 (.a(multiplier_3_out), .b(multiplier_4_out), .out(adder_2_out));  // open: cin, cout
  Adder #(.width(16)) adder_3 (.a(multiplier_5_out), .b(multiplier_6_out), .out(adder_3_out));  // open: cin, cout
  Adder #(.width(16)) adder_4 (.a(multiplier_7_out), .b(multiplier_8_out), .out(adder_4_out));  // open: cin, cout
  Adder #(.width(16)) adder_5 (.a(multiplier_9_out), .b(multiplier_10_out), .out(adder_5_out));  // open: cin, cout
  Adder #(.width(16)) adder_6 (.a(multiplier_11_out), .b(multiplier_12_out), .out(adder_6_out));  // open: cin, cout
  Adder #(.width(16)) adder_7 (.a(multiplier_13_out), .b(multiplier_14_out), .out(adder_7_out));  // open: cin, cout
  Adder #(.width(16)) adder_8 (.a(multiplier_15_out), .b(multiplier_16_out), .out(adder_8_out));  // open: cin, cout
  Adder #(.width(16)) adder_9 (.a(adder_1_out), .b(adder_2_out), .out(adder_9_out));  // open: cin, cout
  Adder #(.width(16)) adder_10 (.a(adder_3_out), .b(adder_4_out), .out(adder_10_out));  // open: cin, cout
  Adder #(.width(16)) adder_11 (.a(adder_5_out), .b(adder_6_out), .out(adder_11_out));  // open: cin, cout
  Adder #(.width(16)) adder_12 (.a(adder_7_out), .b(adder_8_out), .out(adder_12_out));  // open: cin, cout
  Adder #(.width(16)) adder_13 (.a(adder_9_out), .b(s1), .out(c1));  // open: cin, cout
  Adder #(.width(16)) adder_14 (.a(adder_10_out), .b(s2), .out(c2));  // open: cin, cout
  Adder #(.width(16)) adder_15 (.a(adder_11_out), .b(s3), .out(c3));  // open: cin, cout
  Adder #(.width(16)) adder_16 (.a(adder_12_out), .b(s4), .out(c4));  // open: cin, cout
  Multiplier #(.width(16)) multiplier_17 (.a(a5), .b(b1), .out(multiplier_17_out));  // open: cin, cout
  Multiplier #(.width(16)) multiplier_18 (.a(a6), .b(b5), .out(multiplier_18_out));  // open: cin, cout
  Multiplier #(.width(16)) multiplier_19 (.a(a7), .b(b9), .out(multiplier_19_out));  // open: cin, cout
  Multiplier #(.width(16)) multiplier_20 (.a(a8), .b(b13), .out(multiplier_20_out));  // open: cin, cout
  Multiplier #(.width(16)) multiplier_21 (.a(a5), .b(b2), .out(multiplier_21_out));  // open: cin, cout
  Multiplier #(.width(16)) multiplier_22 (.a(a6), .b(b6), .out(multiplier_22_out));  // open: cin, cout
  Multiplier #(.width(16)) multiplier_23 (.a(a7), .b(b10), .out(multiplier_23_out));  // open: cin, cout
  Multiplier #(.width(16)) multiplier_24 (.a(a8), .b(b14), .out(multiplier_24_out));  // open: cin, cout
  Multiplier #(.width(16)) multiplier_25 (.a(a5), .b(b3), .out(multiplier_25_out));  // open: cin, cout
  Multiplier #(.width(16)) multiplier_26 (.a(a6), .b(b7), .out(multiplier_26_out));  // open: cin, cout
  Multiplier #(.width(16)) multiplier_27 (.a(a7), .b(b11), .out(multiplier_27_out));  // open: cin, cout
  Multiplier #(.width(16)) multiplier_28 (.a(a8), .b(b15), .out(multiplier_28_out));  // open: cin, cout
  Multiplier #(.width(16)) multiplier_29 (.a(a5), .b(b4), .out(multiplier_29_out));  // open: cin, cout
  Multiplier #(.width(16)) multiplier_30 (.a(a6), .b(b8), .out(multiplier_30_out));  // open: cin, cout
  Multiplier #(.width(16)) multiplier_31 (.a(a7), .b(b12), .out(multiplier_31_out));  // open: cin, cout
  Multiplier #(.width(16)) multiplier_32 (.a(a8), .b(b16), .out(multiplier_32_out));  // open: cin, cout
  Adder #(.width(16)) adder_17 (.a(multiplier_17_out), .b(multiplier_18_out), .out(adder_17_out));  // open: cin, cout
  Adder #(.width(16)) adder_18 (.a(multiplier_19_out), .b(multiplier_20_out), .out(adder_18_out));  // open: cin, cout
  Adder #(.width(16)) adder_19 (.a(multiplier_21_out), .b(multiplier_22_out), .out(adder_19_out));  // open: cin, cout
  Adder #(.width(16)) adder_20 (.a(multiplier_23_out), .b(multiplier_24_out), .out(adder_20_out));  // open: cin, cout
  Adder #(.width(16)) adder_21 (.a(multiplier_25_out), .b(multiplier_26_out), .out(adder_21_out));  // open: cin, cout
  Adder #(.width(16)) adder_22 (.a(multiplier_27_out), .b(multiplier_28_out), .out(adder_22_out));  // open: cin, cout
  Adder #(.width(16)) adder_23 (.a(multiplier_29_out), .b(multiplier_30_out), .out(adder_23_out));  // open: cin, cout
  Adder #(.width(16)) adder_24 (.a(multiplier_31_out), .b(multiplier_32_out), .out(adder_24_out));  // open: cin, cout
  Adder #(.width(16)) adder_25 (.a(adder_17_out), .b(adder_18_out), .out(adder_25_out));  // open: cin, cout
  Adder #(.width(16)) adder_26 (.a(adder_25_out), .b(s5), .out(c5));  // open: cin, cout
  Adder #(.width(16)) adder_27 (.a(adder_19_out), .b(adder_20_out), .out(adder_27_out));  // open: cin, cout
  Adder #(.width(16)) adder_28 (.a(adder_21_out), .b(adder_22_out), .out(adder_28_out));  // open: cin, cout
  Adder #(.width(16)) adder_29 (.a(adder_23_out), .b(adder_24_out), .out(adder_29_out));  // open: cin, cout
  Adder #(.width(16)) adder_30 (.a(adder_27_out), .b(s6), .out(c6));  // open: cin, cout
  Adder #(.width(16)) adder_31 (.a(adder_28_out), .b(s7), .out(c7));  // open: cin, cout
  Adder #(.width(16)) adder_32 (.a(adder_29_out), .b(s8), .out(c8));  // open: cin, cout
  Multiplier #(.width(16)) multiplier_33 (.a(a9), .b(b1), .out(multiplier_33_out));  // open: cin, cout
  Multiplier #(.width(16)) multiplier_34 (.a(a10), .b(b5), .out(multiplier_34_out));  // open: cin, cout
  Multiplier #(.width(16)) multiplier_35 (.a(a11), .b(b9), .out(multiplier_35_out));  // open: cin, cout
  Multiplier #(.width(16)) multiplier_36 (.a(a12), .b(b13), .out(multiplier_36_out));  // open: cin, cout
  Multiplier #(.width(16)) multiplier_37 (.a(a9), .b(b2), .out(multiplier_37_out));  // open: cin, cout
  Multiplier #(.width(16)) multiplier_38 (.a(a10), .b(b6), .out(multiplier_38_out));  // open: cin, cout
  Multiplier #(.width(16)) multiplier_39 (.a(a11), .b(b10), .out(multiplier_39_out));  // open: cin, cout
  Multiplier #(.width(16)) multiplier_40 (.a(a12), .b(b14), .out(multiplier_40_out));  // open: cin, cout
  Multiplier #(.width(16)) multiplier_41 (.a(a9), .b(b3), .out(multiplier_41_out));  // open: cin, cout
  Multiplier #(.width(16)) multiplier_42 (.a(a10), .b(b7), .out(multiplier_42_out));  // open: cin, cout
  Multiplier #(.width(16)) multiplier_43 (.a(a11), .b(b11), .out(multiplier_43_out));  // open: cin, cout
  Multiplier #(.width(16)) multiplier_44 (.a(a12), .b(b15), .out(multiplier_44_out));  // open: cin, cout
  Multiplier #(.width(16)) multiplier_45 (.a(a9), .b(b4), .out(multiplier_45_out));  // open: cin, cout
  Multiplier #(.width(16)) multiplier_46 (.a(a10), .b(b8), .out(multiplier_46_out));  // open: cin, cout
  Multiplier #(.width(16)) multiplier_47 (.a(a11), .b(b12), .out(multiplier_47_out));  // open: cin, cout
  Multiplier #(.width(16)) multiplier_48 (.a(a12), .b(b16), .out(multiplier_48_out));  // open: cin, cout
  Adder #(.width(16)) adder_33 (.a(multiplier_33_out), .b(multiplier_34_out), .out(adder_33_out));  // open: cin, cout
  Adder #(.width(16)) adder_34 (.a(multiplier_35_out), .b(multiplier_36_out), .out(adder_34_out));  // open: cin, cout
  Adder #(.width(16)) adder_35 (.a(multiplier_37_out), .b(multiplier_38_out), .out(adder_35_out));  // open: cin, cout
  Adder #(.width(16)) adder_36 (.a(multiplier_39_out), .b(multiplier_40_out), .out(adder_36_out));  // open: cin, cout
  Adder #(.width(16)) adder_37 (.a(multiplier_41_out), .b(multiplier_42_out), .out(adder_37_out));  // open: cin, cout
  Adder #(.width(16)) adder_38 (.a(multiplier_43_out), .b(multiplier_44_out), .out(adder_38_out));  // open: cin, cout
  Adder #(.width(16)) adder_39 (.a(multiplier_45_out), .b(multiplier_46_out), .out(adder_39_out));  // open: cin, cout
  Adder #(.width(16)) adder_40 (.a(multiplier_47_out), .b(multiplier_48_out), .out(adder_40_out));  // open: cin, cout
  Adder #(.width(16)) adder_41 (.a(adder_33_out), .b(adder_34_out), .out(adder_41_out));  // open: cin, cout
  Adder #(.width(16)) adder_42 (.a(adder_35_out), .b(adder_36_out), .out(adder_42_out));  // open: cin, cout
  Adder #(.width(16)) adder_43 (.a(adder_37_out), .b(adder_38_out), .out(adder_43_out));  // open: cin, cout
  Adder #(.width(16)) adder_44 (.a(adder_39_out), .b(adder_40_out), .out(adder_44_out));  // open: cin, cout
  Adder #(.width(16)) adder_45 (.a(adder_41_out), .b(s9), .out(c9));  // open: cin, cout
  Adder #(.width(16)) adder_46 (.a(adder_42_out), .b(s10), .out(c10));  // open: cin, cout
  Adder #(.width(16)) adder_47 (.a(adder_43_out), .b(s11), .out(c11));  // open: cin, cout
  Adder #(.width(16)) adder_48 (.a(adder_44_out), .b(s12), .out(c12));  // open: cin, cout
  Multiplier #(.width(16)) multiplier_49 (.a(a13), .b(b1), .out(multiplier_49_out));  // open: cin, cout
  Multiplier #(.width(16)) multiplier_50 (.a(a14), .b(b5), .out(multiplier_50_out));  // open: cin, cout
  Multiplier #(.width(16)) multiplier_51 (.a(a15), .b(b9), .out(multiplier_51_out));  // open: cin, cout
  Multiplier #(.width(16)) multiplier_52 (.a(a16), .b(b13), .out(multiplier_52_out));  // open: cin, cout
  Multiplier #(.width(16)) multiplier_53 (.a(a13), .b(b2), .out(multiplier_53_out));  // open: cin, cout
  Multiplier #(.width(16)) multiplier_54 (.a(a14), .b(b6), .out(multiplier_54_out));  // open: cin, cout
  Multiplier #(.width(16)) multiplier_55 (.a(a15), .b(b10), .out(multiplier_55_out));  // open: cin, cout
  Multiplier #(.width(16)) multiplier_56 (.a(a16), .b(b14), .out(multiplier_56_out));  // open: cin, cout
  Multiplier #(.width(16)) multiplier_57 (.a(a13), .b(b3), .out(multiplier_57_out));  // open: cin, cout
  Multiplier #(.width(16)) multiplier_58 (.a(a14), .b(b7), .out(multiplier_58_out));  // open: cin, cout
  Multiplier #(.width(16)) multiplier_59 (.a(a15), .b(b11), .out(multiplier_59_out));  // open: cin, cout
  Multiplier #(.width(16)) multiplier_60 (.a(a16), .b(b15), .out(multiplier_60_out));  // open: cin, cout
  Multiplier #(.width(16)) multiplier_61 (.a(a13), .b(b4), .out(multiplier_61_out));  // open: cin, cout
  Multiplier #(.width(16)) multiplier_62 (.a(a14), .b(b8), .out(multiplier_62_out));  // open: cin, cout
  Multiplier #(.width(16)) multiplier_63 (.a(a15), .b(b12), .out(multiplier_63_out));  // open: cin, cout
  Multiplier #(.width(16)) multiplier_64 (.a(a16), .b(b16), .out(multiplier_64_out));  // open: cin, cout
  Adder #(.width(16)) adder_49 (.a(multiplier_49_out), .b(multiplier_50_out), .out(adder_49_out));  // open: cin, cout
  Adder #(.width(16)) adder_50 (.a(multiplier_51_out), .b(multiplier_52_out), .out(adder_50_out));  // open: cin, cout
  Adder #(.width(16)) adder_51 (.a(multiplier_53_out), .b(multiplier_54_out), .out(adder_51_out));  // open: cin, cout
  Adder #(.width(16)) adder_52 (.a(multiplier_55_out), .b(multiplier_56_out), .out(adder_52_out));  // open: cin, cout
  Adder #(.width(16)) adder_53 (.a(multiplier_57_out), .b(multiplier_58_out), .out(adder_53_out));  // open: cin, cout
  Adder #(.width(16)) adder_54 (.a(multiplier_59_out), .b(multiplier_60_out), .out(adder_54_out));  // open: cin, cout
  Adder #(.width(16)) adder_55 (.a(multiplier_61_out), .b(multiplier_62_out), .out(adder_55_out));  // open: cin, cout
  Adder #(.width(16)) adder_56 (.a(multiplier_63_out), .b(multiplier_64_out), .out(adder_56_out));  // open: cin, cout
  Adder #(.width(16)) adder_57 (.a(adder_49_out), .b(adder_50_out), .out(adder_57_out));  // open: cin, cout
  Adder #(.width(16)) adder_58 (.a(adder_51_out), .b(adder_52_out), .out(adder_58_out));  // open: cin, cout
  Adder #(.width(16)) adder_59 (.a(adder_53_out), .b(adder_54_out), .out(adder_59_out));  // open: cin, cout
  Adder #(.width(16)) adder_60 (.a(adder_55_out), .b(adder_56_out), .out(adder_60_out));  // open: cin, cout
  Adder #(.width(16)) adder_61 (.a(adder_57_out), .b(s13), .out(c13));  // open: cin, cout
  Adder #(.width(16)) adder_62 (.a(adder_58_out), .b(s14), .out(c14));  // open: cin, cout
  Adder #(.width(16)) adder_63 (.a(adder_59_out), .b(s15), .out(c15));  // open: cin, cout
  Adder #(.width(16)) adder_64 (.a(adder_60_out), .b(s16), .out(c16));  // open: cin, cout
endmodule

module RnC (
  input  in_1,
  input  in_2
);

  wire and_1_out, and_2_out, and_3_out, and_4_out, and_5_out, and_6_out, and_7_out, clock_1_out,
       comparator_1_eq, comparator_1_gt, comparator_1_lt, comparator_2_eq, comparator_2_gt, comparator_2_lt,
       comparator_3_eq, comparator_3_gt, comparator_3_lt, comparator_4_eq, comparator_4_gt, comparator_4_lt,
       comparator_5_eq, comparator_5_gt, comparator_5_lt, comparator_6_eq, comparator_6_lt,
       control_circuit_1_1_oe, control_circuit_1_1_out_6, control_circuit_1_1_rr, control_circuit_1_1_we,
       control_circuit_1_dc, control_circuit_2_1_out_6, control_circuit_3_1_out_7, control_circuit_3_1_r,
       or_1_out, or_2_out, or_3_out, or_4_out, or_5_out, or_6_out, or_7_out, or_8_out, or_9_out, or_10_out,
       or_11_out, or_12_out, or_13_out, or_14_out, or_15_out, or_16_out, or_17_out, or_18_out, or_19_out,
       or_20_out, or_21_out, or_22_out, or_23_out, or_24_out, or_25_out, or_26_out, or_27_out, or_28_out,
       or_29_out, or_30_out, or_31_out, or_32_out, or_33_out, or_34_out, or_35_out, or_36_out, or_37_out,
       or_38_out, or_39_out, or_40_out, or_41_out, or_42_out, or_43_out, or_44_out, or_45_out, or_46_out,
       or_47_out, or_48_out, or_49_out, or_50_out, or_51_out, or_52_out, or_53_out, or_54_out, or_55_out,
       or_56_out, or_57_out, or_58_out, or_59_out, or_60_out, undriven, undriven_2, undriven_3, undriven_4,
       undriven_5;
  wire [3:0] counter_3_q, counter_3_q_2, counter_3_q_3, counter_3_q_4, counter_5_q, counter_5_q_2,
       counter_5_q_3, counter_5_q_4, counter_6_q, counter_6_q_2, counter_6_q_3, counter_6_q_4, counter_7_q,
       counter_7_q_2, counter_7_q_3, counter_7_q_4, counter_8_q, counter_8_q_2, counter_8_q_3, counter_8_q_4,
       counter_10_q, counter_10_q_2, counter_10_q_3, counter_10_q_4, counter_11_q, counter_11_q_2,
       counter_11_q_3, counter_11_q_4;
  wire [7:0] control_circuit_1_d, counter_4_q, counter_9_q;
  wire [11:0] control_circuit_1_1_d, control_circuit_2_1_d, control_circuit_3_1_d, counter_1_q, counter_2_q,
       counter_12_q, counter_13_q, counter_14_q, counter_15_q, counter_16_q, counter_17_q, counter_18_q,
       counter_19_q, counter_20_q, counter_21_q, counter_22_q, counter_23_q, counter_24_q, counter_25_q,
       counter_26_q, counter_27_q, counter_28_q, counter_29_q, counter_30_q, counter_31_q, counter_32_q,
       counter_33_q, counter_34_q, counter_35_q, counter_36_q, counter_37_q, counter_38_q, counter_39_q,
       counter_40_q, counter_41_q, counter_42_q, counter_43_q, counter_44_q, counter_45_q, counter_46_q,
       counter_47_q, counter_48_q, counter_49_q, counter_50_q, counter_51_q, counter_52_q, counter_53_q,
       counter_54_q, counter_55_q, counter_56_q, counter_57_q, counter_58_q, counter_59_q, counter_60_q;
  wire [15:0] controlled_buffer_1_out, ram_1_dout, ram_2_dout, ram_4_dout, ram_5_dout, ram_6_dout,
       ram_7_dout, ram_8_dout, ram_9_dout, ram_10_dout, ram_11_dout, ram_12_dout, ram_13_dout, ram_14_dout,
       ram_15_dout, ram_16_dout, ram_17_dout, ram_18_dout, ram_19_dout, ram_20_dout, ram_21_dout,
       ram_22_dout, ram_23_dout, ram_24_dout, ram_25_dout, ram_26_dout, ram_27_dout, ram_28_dout,
       ram_29_dout, ram_30_dout, ram_31_dout, ram_32_dout, ram_33_dout, ram_34_dout, ram_35_dout,
       ram_37_dout, ram_38_dout, ram_39_dout, ram_40_dout, ram_41_dout, ram_42_dout, ram_43_dout,
       ram_44_dout, ram_45_dout, ram_46_dout, ram_47_dout, ram_48_dout, ram_49_dout, ram_50_dout,
       ram_51_dout, ram_52_dout, register_2_q, register_3_q, register_4_q, register_5_q, register_6_q,
       register_7_q, register_8_q, register_9_q, register_10_q, register_11_q, register_12_q, register_13_q,
       register_14_q, register_15_q, register_16_q, register_17_q, register_18_q, register_19_q,
       register_20_q, register_21_q, register_22_q, register_23_q, register_24_q, register_25_q,
       register_26_q, register_27_q, register_28_q, register_29_q, register_30_q, register_31_q,
       register_32_q, register_33_q, register_34_q, register_35_q, register_36_q, register_37_q,
       register_38_q, register_39_q, register_40_q, register_41_q, register_42_q, register_43_q,
       register_44_q, register_45_q, register_46_q, register_47_q, register_48_q, register_49_q,
       rnc_tiling_core_1_c1, rnc_tiling_core_1_c2, rnc_tiling_core_1_c3, rnc_tiling_core_1_c4,
       rnc_tiling_core_1_c5, rnc_tiling_core_1_c6, rnc_tiling_core_1_c7, rnc_tiling_core_1_c8,
       rnc_tiling_core_1_c9, rnc_tiling_core_1_c10, rnc_tiling_core_1_c11, rnc_tiling_core_1_c12,
       rnc_tiling_core_1_c13, rnc_tiling_core_1_c14, rnc_tiling_core_1_c15, rnc_tiling_core_1_c16;
  wire [23:0] ram_3_dout, register_1_q;
  wire [63:0] rom_1_data;

  Comparator comparator_1 (.a(counter_4_q), .b(8'h4), .gt(comparator_1_gt), .eq(comparator_1_eq), .lt(comparator_1_lt));
  Hex_Digit_Display hex_digit_display_1 (.value(counter_3_q_4));  // open: dp
  Hex_Digit_Display hex_digit_display_2 (.value(counter_3_q_3));  // open: dp
  or or_1 (or_1_out, comparator_1_eq, comparator_1_lt);
  Counter #(.max('hfff), .width(12)) counter_1 (
    .count(or_9_out), .Q(counter_1_q), .clk(clock_1_out));  // open: load, D, carry, up, clr
  Counter #(.max('hfff), .width(12)) counter_2 (
    .count(or_10_out), .Q(counter_2_q), .clk(clock_1_out));  // open: load, D, carry, up, clr
  Hex_Digit_Display hex_digit_display_3 (.value(counter_3_q_2));  // open: dp
  Hex_Digit_Display hex_digit_display_4 (.value(counter_3_q));  // open: dp
  // Probe on {counter_3_q_4, counter_3_q_3, counter_3_q_2, counter_3_q}
  Counter #(.max('hffff), .width(16)) counter_3 (
    .count(or_1_out), .Q({counter_3_q_4, counter_3_q_3, counter_3_q_2, counter_3_q}), .clk(clock_1_out));  // open: load, D, carry, up, clr
  Comparator comparator_2 (.a(counter_4_q), .b(8'h8), .gt(comparator_2_gt), .eq(comparator_2_eq), .lt(comparator_2_lt));
  RAM #(.addrWidth(12), .asyncread("true"), .dataWidth(16), .\type ("nonvolatile")) ram_1 (
    .addr(counter_1_q), .oe(or_9_out), .clk(clock_1_out), .dout(ram_1_dout));  // open: we, din
  RAM #(.addrWidth(12), .asyncread("true"), .dataWidth(16), .\type ("nonvolatile")) ram_2 (
    .addr(counter_2_q), .oe(or_10_out), .clk(clock_1_out), .dout(ram_2_dout));  // open: we, din
  and and_1 (and_1_out, or_4_out, rom_1_data[8]);
  Hex_Digit_Display hex_digit_display_5 (.value(counter_5_q_4));  // open: dp
  or or_2 (or_2_out, comparator_2_eq, comparator_2_lt);
  Counter counter_4 (.count(and_1_out), .Q(counter_4_q), .clk(clock_1_out));  // open: load, D, carry, up, clr
  Hex_Digit_Display hex_digit_display_6 (.value(counter_5_q_3));  // open: dp
  Hex_Digit_Display hex_digit_display_7 (.value(counter_5_q_2));  // open: dp
  and and_2 (and_2_out, comparator_1_gt, or_4_out, or_2_out);
  RAM #(.asyncread("true"), .dataWidth(24), .\type ("nonvolatile")) ram_3 (
    .addr(counter_4_q), .oe(rom_1_data[8]), .clk(clock_1_out), .dout(ram_3_dout));  // open: we, din
  Hex_Digit_Display hex_digit_display_8 (.value(counter_6_q_4));  // open: dp
  Hex_Digit_Display hex_digit_display_9 (.value(counter_5_q));  // open: dp
  // Probe on {counter_5_q_4, counter_5_q_3, counter_5_q_2, counter_5_q}
  Counter #(.max('hffff), .width(16)) counter_5 (
    .count(and_2_out), .Q({counter_5_q_4, counter_5_q_3, counter_5_q_2, counter_5_q}), .clk(clock_1_out));  // open: load, D, carry, up, clr
  Comparator comparator_3 (.a(counter_4_q), .b(8'hc), .gt(comparator_3_gt), .eq(comparator_3_eq), .lt(comparator_3_lt));
  Hex_Digit_Display hex_digit_display_10 (.value(counter_6_q_3));  // open: dp
  Hex_Digit_Display hex_digit_display_11 (.value(counter_6_q_2));  // open: dp
  Counter #(.max('hffff), .width(16)) counter_6 (
    .count(or_4_out), .Q({counter_6_q_4, counter_6_q_3, counter_6_q_2, counter_6_q}), .clk(clock_1_out));  // open: load, D, carry, up, clr
  Hex_Digit_Display hex_digit_display_12 (.value(counter_7_q_4));  // open: dp
  and and_3 (and_3_out, comparator_2_gt, or_4_out, or_3_out);
  or or_3 (or_3_out, comparator_3_eq, comparator_3_lt);
  Hex_Digit_Display hex_digit_display_13 (.value(counter_6_q));  // open: dp
  // Probe on {counter_6_q_4, counter_6_q_3, counter_6_q_2, counter_6_q}
  or or_4 (or_4_out, ram_3_dout[0], ram_3_dout[1], ram_3_dout[2], ram_3_dout[3], ram_3_dout[4], ram_3_dout[5], ram_3_dout[6], ram_3_dout[7], ram_3_dout[8], ram_3_dout[9], ram_3_dout[10], ram_3_dout[11], ram_3_dout[13], ram_3_dout[14], ram_3_dout[15], ram_3_dout[16], ram_3_dout[17], ram_3_dout[18], ram_3_dout[19], ram_3_dout[20], ram_3_dout[21], ram_3_dout[22], ram_3_dout[23], ram_3_dout[12]);
  Hex_Digit_Display hex_digit_display_14 (.value(counter_7_q_3));  // open: dp
  Hex_Digit_Display hex_digit_display_15 (.value(counter_7_q_2));  // open: dp
  Counter #(.max('hffff), .width(16)) counter_7 (
    .count(and_3_out), .Q({counter_7_q_4, counter_7_q_3, counter_7_q_2, counter_7_q}), .clk(clock_1_out));  // open: load, D, carry, up, clr
  Comparator comparator_4 (
    .a(counter_4_q), .b(8'h10), .gt(comparator_4_gt), .eq(comparator_4_eq), .lt(comparator_4_lt));
  Hex_Digit_Display hex_digit_display_16 (.value(counter_7_q));  // open: dp
  Hex_Digit_Display hex_digit_display_17 (.value(counter_8_q_4));  // open: dp
  // Probe on {counter_7_q_4, counter_7_q_3, counter_7_q_2, counter_7_q}
  and and_4 (and_4_out, comparator_3_gt, or_4_out, or_5_out);
  or or_5 (or_5_out, comparator_4_eq, comparator_4_lt);
  control_circuit control_circuit_1 (
    .a1(rom_1_data[63]), .a2(rom_1_data[62]), .a3(rom_1_data[61]), .a4(rom_1_data[60]), .a5(rom_1_data[59]),
    .a6(rom_1_data[58]), .a7(rom_1_data[57]), .a8(rom_1_data[56]), .a9(rom_1_data[55]), .a10(rom_1_data[54]),
    .a11(rom_1_data[53]), .a12(rom_1_data[52]), .a13(rom_1_data[51]), .a14(rom_1_data[50]),
    .a15(rom_1_data[49]), .a16(rom_1_data[48]), .b1(rom_1_data[47]), .b2(rom_1_data[46]),
    .b3(rom_1_data[45]), .b4(rom_1_data[44]), .b5(rom_1_data[43]), .b6(rom_1_data[42]), .b7(rom_1_data[41]),
    .b8(rom_1_data[40]), .b9(rom_1_data[39]), .b10(rom_1_data[38]), .b11(rom_1_data[37]),
    .b12(rom_1_data[36]), .b13(rom_1_data[35]), .b14(rom_1_data[34]), .b15(rom_1_data[33]),
    .b16(rom_1_data[32]), .aB1(rom_1_data[19]), .aB2(rom_1_data[18]), .aB3(rom_1_data[17]),
    .aB4(rom_1_data[16]), .bB1(rom_1_data[15]), .bB2(rom_1_data[14]), .bB3(rom_1_data[13]),
    .bB4(rom_1_data[12]), .ct(rom_1_data[10]), .Clock(clock_1_out), .R(rom_1_data[9]),
    .Dim(register_1_q[19:12]), .ct1(rom_1_data[20]), .R1(rom_1_data[8]), .ct2(rom_1_data[22]),
    .R2(rom_1_data[21]), .C1(rom_1_data[31]), .C2(rom_1_data[27]), .C3(rom_1_data[7]), .C4(rom_1_data[3]),
    .C5(rom_1_data[30]), .C6(rom_1_data[26]), .C7(rom_1_data[6]), .C8(rom_1_data[2]), .C9(rom_1_data[29]),
    .C10(rom_1_data[25]), .C11(rom_1_data[5]), .C12(rom_1_data[1]), .C13(rom_1_data[28]),
    .C14(rom_1_data[24]), .C15(rom_1_data[4]), .C16(rom_1_data[0]), .Opcode(register_1_q[23:20]),
    .DC(control_circuit_1_dc), .D(control_circuit_1_d));
  Register #(.width(24)) register_1 (
    .D(ram_3_dout), .en(rom_1_data[8]), .clk(clock_1_out), .Q(register_1_q), .clr(or_8_out));
  Hex_Digit_Display hex_digit_display_18 (.value(counter_8_q_3));  // open: dp
  Hex_Digit_Display hex_digit_display_19 (.value(counter_8_q_2));  // open: dp
  Hex_Digit_Display hex_digit_display_20 (.value(counter_8_q));  // open: dp
  // Probe on {counter_8_q_4, counter_8_q_3, counter_8_q_2, counter_8_q}
  Counter #(.max('hffff), .width(16)) counter_8 (
    .count(and_4_out), .Q({counter_8_q_4, counter_8_q_3, counter_8_q_2, counter_8_q}), .clk(clock_1_out));  // open: load, D, carry, up, clr
  Comparator comparator_5 (
    .a(counter_4_q), .b(8'h14), .gt(comparator_5_gt), .eq(comparator_5_eq), .lt(comparator_5_lt));
  Hex_Digit_Display hex_digit_display_21 (.value(counter_10_q_4));  // open: dp
  Hex_Digit_Display hex_digit_display_22 (.value(counter_10_q_3));  // open: dp
  and and_5 (and_5_out, comparator_4_gt, or_4_out, or_6_out);
  or or_6 (or_6_out, comparator_5_eq, comparator_5_lt);
  Counter counter_9 (
    .load(control_circuit_1_dc), .D(control_circuit_1_d), .Q(counter_9_q), .clk(clock_1_out), .clr(or_8_out));  // open: count, carry, up
  Hex_Digit_Display hex_digit_display_23 (.value(counter_10_q_2));  // open: dp
  Hex_Digit_Display hex_digit_display_24 (.value(counter_10_q));  // open: dp
  // Probe on {counter_10_q_4, counter_10_q_3, counter_10_q_2, counter_10_q}
  Counter #(.max('hffff), .width(16)) counter_10 (
    .count(and_5_out), .Q({counter_10_q_4, counter_10_q_3, counter_10_q_2, counter_10_q}), .clk(clock_1_out));  // open: load, D, carry, up, clr
  Comparator comparator_6 (.a(counter_4_q), .b(8'h18), .eq(comparator_6_eq), .lt(comparator_6_lt));  // open: gt
  and and_6 (and_6_out, comparator_5_gt, or_4_out, or_7_out);
  or or_7 (or_7_out, comparator_6_eq, comparator_6_lt);
  ROM #(.addrWidth(12), .dataWidth(64)) rom_1 (.addr({register_1_q[23:20], counter_9_q}), .data(rom_1_data));
  or or_8 (or_8_out, rom_1_data[11], control_circuit_3_1_r);
  Hex_Digit_Display hex_digit_display_25 (.value(counter_11_q_4));  // open: dp
  Hex_Digit_Display hex_digit_display_26 (.value(counter_11_q_3));  // open: dp
  Hex_Digit_Display hex_digit_display_27 (.value(counter_11_q_2));  // open: dp
  Hex_Digit_Display hex_digit_display_28 (.value(counter_11_q));  // open: dp
  // Probe on {counter_11_q_4, counter_11_q_3, counter_11_q_2, counter_11_q}
  Counter #(.max('hffff), .width(16)) counter_11 (
    .count(and_6_out), .Q({counter_11_q_4, counter_11_q_3, counter_11_q_2, counter_11_q}), .clk(clock_1_out));  // open: load, D, carry, up, clr
  or or_9 (or_9_out, rom_1_data[48], rom_1_data[52], rom_1_data[56], rom_1_data[60], rom_1_data[49], rom_1_data[53], rom_1_data[57], rom_1_data[50], rom_1_data[61], rom_1_data[54], rom_1_data[58], rom_1_data[62], rom_1_data[51], rom_1_data[55], rom_1_data[59], rom_1_data[63]);
  or or_10 (or_10_out, rom_1_data[32], rom_1_data[33], rom_1_data[34], rom_1_data[35], rom_1_data[36], rom_1_data[37], rom_1_data[38], rom_1_data[40], rom_1_data[39], rom_1_data[41], rom_1_data[42], rom_1_data[43], rom_1_data[44], rom_1_data[45], rom_1_data[46], rom_1_data[47]);
  control_circuit_1 control_circuit_1_1 (
    .add(register_1_q[11:0]), .dim(register_1_q[19:12]), .clock(clock_1_out), .R(rom_1_data[23]),
    .Opcode(register_1_q[23:20]), .out_6(control_circuit_1_1_out_6), .D(control_circuit_1_1_d),
    .OE(control_circuit_1_1_oe), .WE(control_circuit_1_1_we), .RR(control_circuit_1_1_rr));
  control_circuit_2 control_circuit_2_1 (
    .add(register_1_q[11:0]), .dim(register_1_q[19:12]), .clock(clock_1_out), .OE(control_circuit_1_1_oe),
    .R(rom_1_data[23]), .out_6(control_circuit_2_1_out_6), .D(control_circuit_2_1_d));
  or or_11 (or_11_out, rom_1_data[63], control_circuit_1_1_oe);
  or or_12 (or_12_out, rom_1_data[47], control_circuit_1_1_oe);
  RAM #(.addrWidth(12), .asyncread("true"), .dataWidth(16)) ram_4 (
    .addr(counter_12_q), .we(rom_1_data[63]), .oe(control_circuit_1_1_oe), .clk(clock_1_out),
    .din(ram_1_dout), .dout(ram_4_dout));
  Counter #(.max('hfff), .width(12)) counter_12 (
    .load(control_circuit_1_1_out_6), .D(control_circuit_1_1_d), .count(or_11_out), .Q(counter_12_q),
    .clk(clock_1_out), .clr(in_1));  // open: carry, up
  RAM #(.addrWidth(12), .asyncread("true"), .dataWidth(16)) ram_5 (
    .addr(counter_13_q), .we(rom_1_data[59]), .oe(control_circuit_1_1_oe), .clk(clock_1_out),
    .din(ram_1_dout), .dout(ram_5_dout));
  Counter #(.max('hfff), .width(12)) counter_13 (
    .load(control_circuit_1_1_out_6), .D(control_circuit_1_1_d), .count(or_13_out), .Q(counter_13_q),
    .clk(clock_1_out), .clr(in_1));  // open: carry, up
  or or_13 (or_13_out, rom_1_data[59], control_circuit_1_1_oe);
  RAM #(.addrWidth(12), .asyncread("true"), .dataWidth(16)) ram_6 (
    .addr(counter_14_q), .we(rom_1_data[55]), .oe(control_circuit_1_1_oe), .clk(clock_1_out),
    .din(ram_1_dout), .dout(ram_6_dout));
  Counter #(.max('hfff), .width(12)) counter_14 (
    .load(control_circuit_1_1_out_6), .D(control_circuit_1_1_d), .count(or_14_out), .Q(counter_14_q),
    .clk(clock_1_out), .clr(in_1));  // open: carry, up
  or or_14 (or_14_out, rom_1_data[55], control_circuit_1_1_oe);
  RAM #(.addrWidth(12), .asyncread("true"), .dataWidth(16)) ram_7 (
    .addr(counter_15_q), .we(rom_1_data[51]), .oe(control_circuit_1_1_oe), .clk(clock_1_out),
    .din(ram_1_dout), .dout(ram_7_dout));
  Counter #(.max('hfff), .width(12)) counter_15 (
    .load(control_circuit_1_1_out_6), .D(control_circuit_1_1_d), .count(or_15_out), .Q(counter_15_q),
    .clk(clock_1_out), .clr(in_1));  // open: carry, up
  or or_15 (or_15_out, rom_1_data[51], control_circuit_1_1_oe);
  RAM #(.addrWidth(12), .asyncread("true"), .dataWidth(16)) ram_8 (
    .addr(counter_16_q), .we(rom_1_data[47]), .oe(control_circuit_1_1_oe), .clk(clock_1_out),
    .din(ram_2_dout), .dout(ram_8_dout));
  Counter #(.max('hfff), .width(12)) counter_16 (
    .load(control_circuit_2_1_out_6), .D(control_circuit_2_1_d), .count(or_12_out), .Q(counter_16_q),
    .clk(clock_1_out), .clr(in_1));  // open: carry, up
  RAM #(.addrWidth(12), .asyncread("true"), .dataWidth(16)) ram_9 (
    .addr(counter_17_q), .we(rom_1_data[46]), .oe(control_circuit_1_1_oe), .clk(clock_1_out),
    .din(ram_2_dout), .dout(ram_9_dout));
  Counter #(.max('hfff), .width(12)) counter_17 (
    .load(control_circuit_2_1_out_6), .D(control_circuit_2_1_d), .count(or_16_out), .Q(counter_17_q),
    .clk(clock_1_out), .clr(in_1));  // open: carry, up
  or or_16 (or_16_out, rom_1_data[46], control_circuit_1_1_oe);
  RAM #(.addrWidth(12), .asyncread("true"), .dataWidth(16)) ram_10 (
    .addr(counter_18_q), .we(rom_1_data[45]), .oe(control_circuit_1_1_oe), .clk(clock_1_out),
    .din(ram_2_dout), .dout(ram_10_dout));
  Counter #(.max('hfff), .width(12)) counter_18 (
    .load(control_circuit_2_1_out_6), .D(control_circuit_2_1_d), .count(or_17_out), .Q(counter_18_q),
    .clk(clock_1_out), .clr(in_1));  // open: carry, up
  or or_17 (or_17_out, rom_1_data[45], control_circuit_1_1_oe);
  RAM #(.addrWidth(12), .asyncread("true"), .dataWidth(16)) ram_11 (
    .addr(counter_19_q), .we(rom_1_data[44]), .oe(control_circuit_1_1_oe), .clk(clock_1_out),
    .din(ram_2_dout), .dout(ram_11_dout));
  Counter #(.max('hfff), .width(12)) counter_19 (
    .load(control_circuit_2_1_out_6), .D(control_circuit_2_1_d), .count(or_18_out), .Q(counter_19_q),
    .clk(clock_1_out), .clr(in_1));  // open: carry, up
  or or_18 (or_18_out, rom_1_data[44], control_circuit_1_1_oe);
  or or_19 (or_19_out, rom_1_data[62], control_circuit_1_1_oe);
  or or_20 (or_20_out, rom_1_data[43], control_circuit_1_1_oe);
  Counter #(.max('hfff), .width(12)) counter_20 (
    .load(control_circuit_1_1_out_6), .D(control_circuit_1_1_d), .count(or_19_out), .Q(counter_20_q),
    .clk(clock_1_out), .clr(in_1));  // open: carry, up
  Counter #(.max('hfff), .width(12)) counter_21 (
    .load(control_circuit_1_1_out_6), .D(control_circuit_1_1_d), .count(or_21_out), .Q(counter_21_q),
    .clk(clock_1_out), .clr(in_1));  // open: carry, up
  or or_21 (or_21_out, rom_1_data[58], control_circuit_1_1_oe);
  Counter #(.max('hfff), .width(12)) counter_22 (
    .load(control_circuit_1_1_out_6), .D(control_circuit_1_1_d), .count(or_22_out), .Q(counter_22_q),
    .clk(clock_1_out), .clr(in_1));  // open: carry, up
  or or_22 (or_22_out, rom_1_data[54], control_circuit_1_1_oe);
  Counter #(.max('hfff), .width(12)) counter_23 (
    .load(control_circuit_1_1_out_6), .D(control_circuit_1_1_d), .count(or_23_out), .Q(counter_23_q),
    .clk(clock_1_out), .clr(in_1));  // open: carry, up
  or or_23 (or_23_out, rom_1_data[50], control_circuit_1_1_oe);
  RAM #(.addrWidth(12), .asyncread("true"), .dataWidth(16)) ram_12 (
    .addr(counter_24_q), .we(rom_1_data[43]), .oe(control_circuit_1_1_oe), .clk(clock_1_out),
    .din(ram_2_dout), .dout(ram_12_dout));
  Counter #(.max('hfff), .width(12)) counter_24 (
    .load(control_circuit_2_1_out_6), .D(control_circuit_2_1_d), .count(or_20_out), .Q(counter_24_q),
    .clk(clock_1_out), .clr(in_1));  // open: carry, up
  RAM #(.addrWidth(12), .asyncread("true"), .dataWidth(16)) ram_13 (
    .addr(counter_25_q), .we(rom_1_data[42]), .oe(control_circuit_1_1_oe), .clk(clock_1_out),
    .din(ram_2_dout), .dout(ram_13_dout));
  Counter #(.max('hfff), .width(12)) counter_25 (
    .load(control_circuit_2_1_out_6), .D(control_circuit_2_1_d), .count(or_24_out), .Q(counter_25_q),
    .clk(clock_1_out), .clr(in_1));  // open: carry, up
  or or_24 (or_24_out, rom_1_data[42], control_circuit_1_1_oe);
  RAM #(.addrWidth(12), .asyncread("true"), .dataWidth(16)) ram_14 (
    .addr(counter_26_q), .we(rom_1_data[41]), .oe(control_circuit_1_1_oe), .clk(clock_1_out),
    .din(ram_2_dout), .dout(ram_14_dout));
  Counter #(.max('hfff), .width(12)) counter_26 (
    .load(control_circuit_2_1_out_6), .D(control_circuit_2_1_d), .count(or_25_out), .Q(counter_26_q),
    .clk(clock_1_out), .clr(in_1));  // open: carry, up
  or or_25 (or_25_out, rom_1_data[41], control_circuit_1_1_oe);
  RAM #(.addrWidth(12), .asyncread("true"), .dataWidth(16)) ram_15 (
    .addr(counter_27_q), .we(rom_1_data[40]), .oe(control_circuit_1_1_oe), .clk(clock_1_out),
    .din(ram_2_dout), .dout(ram_15_dout));
  Counter #(.max('hfff), .width(12)) counter_27 (
    .load(control_circuit_2_1_out_6), .D(control_circuit_2_1_d), .count(or_26_out), .Q(counter_27_q),
    .clk(clock_1_out), .clr(in_1));  // open: carry, up
  or or_26 (or_26_out, rom_1_data[40], control_circuit_1_1_oe);
  RAM #(.addrWidth(12), .asyncread("true"), .dataWidth(16)) ram_16 (
    .addr(counter_20_q), .we(rom_1_data[62]), .oe(control_circuit_1_1_oe), .clk(clock_1_out),
    .din(ram_1_dout), .dout(ram_16_dout));
  RAM #(.addrWidth(12), .asyncread("true"), .dataWidth(16)) ram_17 (
    .addr(counter_21_q), .we(rom_1_data[58]), .oe(control_circuit_1_1_oe), .clk(clock_1_out),
    .din(ram_1_dout), .dout(ram_17_dout));
  RAM #(.addrWidth(12), .asyncread("true"), .dataWidth(16)) ram_18 (
    .addr(counter_22_q), .we(rom_1_data[54]), .oe(control_circuit_1_1_oe), .clk(clock_1_out),
    .din(ram_1_dout), .dout(ram_18_dout));
  RAM #(.addrWidth(12), .asyncread("true"), .dataWidth(16)) ram_19 (
    .addr(counter_23_q), .we(rom_1_data[50]), .oe(control_circuit_1_1_oe), .clk(clock_1_out),
    .din(ram_1_dout), .dout(ram_19_dout));
  or or_27 (or_27_out, rom_1_data[61], control_circuit_1_1_oe);
  or or_28 (or_28_out, rom_1_data[39], control_circuit_1_1_oe);
  Counter #(.max('hfff), .width(12)) counter_28 (
    .load(control_circuit_1_1_out_6), .D(control_circuit_1_1_d), .count(or_27_out), .Q(counter_28_q),
    .clk(clock_1_out), .clr(in_1));  // open: carry, up
  Counter #(.max('hfff), .width(12)) counter_29 (
    .load(control_circuit_1_1_out_6), .D(control_circuit_1_1_d), .count(or_29_out), .Q(counter_29_q),
    .clk(clock_1_out), .clr(in_1));  // open: carry, up
  or or_29 (or_29_out, rom_1_data[57], control_circuit_1_1_oe);
  Counter #(.max('hfff), .width(12)) counter_30 (
    .load(control_circuit_1_1_out_6), .D(control_circuit_1_1_d), .count(or_30_out), .Q(counter_30_q),
    .clk(clock_1_out), .clr(in_1));  // open: carry, up
  or or_30 (or_30_out, rom_1_data[53], control_circuit_1_1_oe);
  Counter #(.max('hfff), .width(12)) counter_31 (
    .load(control_circuit_1_1_out_6), .D(control_circuit_1_1_d), .count(or_31_out), .Q(counter_31_q),
    .clk(clock_1_out), .clr(in_1));  // open: carry, up
  or or_31 (or_31_out, rom_1_data[49], control_circuit_1_1_oe);
  Counter #(.max('hfff), .width(12)) counter_32 (
    .load(control_circuit_2_1_out_6), .D(control_circuit_2_1_d), .count(or_28_out), .Q(counter_32_q),
    .clk(clock_1_out), .clr(in_1));  // open: carry, up
  Counter #(.max('hfff), .width(12)) counter_33 (
    .load(control_circuit_2_1_out_6), .D(control_circuit_2_1_d), .count(or_32_out), .Q(counter_33_q),
    .clk(clock_1_out), .clr(in_1));  // open: carry, up
  or or_32 (or_32_out, rom_1_data[38], control_circuit_1_1_oe);
  Counter #(.max('hfff), .width(12)) counter_34 (
    .load(control_circuit_2_1_out_6), .D(control_circuit_2_1_d), .count(or_33_out), .Q(counter_34_q),
    .clk(clock_1_out), .clr(in_1));  // open: carry, up
  or or_33 (or_33_out, rom_1_data[37], control_circuit_1_1_oe);
  Counter #(.max('hfff), .width(12)) counter_35 (
    .load(control_circuit_2_1_out_6), .D(control_circuit_2_1_d), .count(or_34_out), .Q(counter_35_q),
    .clk(clock_1_out), .clr(in_1));  // open: carry, up
  or or_34 (or_34_out, rom_1_data[36], control_circuit_1_1_oe);
  RAM #(.addrWidth(12), .asyncread("true"), .dataWidth(16)) ram_20 (
    .addr(counter_28_q), .we(rom_1_data[61]), .oe(control_circuit_1_1_oe), .clk(clock_1_out),
    .din(ram_1_dout), .dout(ram_20_dout));
  RAM #(.addrWidth(12), .asyncread("true"), .dataWidth(16)) ram_21 (
    .addr(counter_29_q), .we(rom_1_data[57]), .oe(control_circuit_1_1_oe), .clk(clock_1_out),
    .din(ram_1_dout), .dout(ram_21_dout));
  RAM #(.addrWidth(12), .asyncread("true"), .dataWidth(16)) ram_22 (
    .addr(counter_30_q), .we(rom_1_data[53]), .oe(control_circuit_1_1_oe), .clk(clock_1_out),
    .din(ram_1_dout), .dout(ram_22_dout));
  RAM #(.addrWidth(12), .asyncread("true"), .dataWidth(16)) ram_23 (
    .addr(counter_31_q), .we(rom_1_data[49]), .oe(control_circuit_1_1_oe), .clk(clock_1_out),
    .din(ram_1_dout), .dout(ram_23_dout));
  RAM #(.addrWidth(12), .asyncread("true"), .dataWidth(16)) ram_24 (
    .addr(counter_32_q), .we(rom_1_data[39]), .oe(control_circuit_1_1_oe), .clk(clock_1_out),
    .din(ram_2_dout), .dout(ram_24_dout));
  RAM #(.addrWidth(12), .asyncread("true"), .dataWidth(16)) ram_25 (
    .addr(counter_33_q), .we(rom_1_data[38]), .oe(control_circuit_1_1_oe), .clk(clock_1_out),
    .din(ram_2_dout), .dout(ram_25_dout));
  RAM #(.addrWidth(12), .asyncread("true"), .dataWidth(16)) ram_26 (
    .addr(counter_34_q), .we(rom_1_data[37]), .oe(control_circuit_1_1_oe), .clk(clock_1_out),
    .din(ram_2_dout), .dout(ram_26_dout));
  RAM #(.addrWidth(12), .asyncread("true"), .dataWidth(16)) ram_27 (
    .addr(counter_35_q), .we(rom_1_data[36]), .oe(control_circuit_1_1_oe), .clk(clock_1_out),
    .din(ram_2_dout), .dout(ram_27_dout));
  or or_35 (or_35_out, rom_1_data[60], control_circuit_1_1_oe);
  or or_36 (or_36_out, rom_1_data[35], control_circuit_1_1_oe);
  Counter #(.max('hfff), .width(12)) counter_36 (
    .load(control_circuit_1_1_out_6), .D(control_circuit_1_1_d), .count(or_35_out), .Q(counter_36_q),
    .clk(clock_1_out), .clr(in_1));  // open: carry, up
  or or_37 (or_37_out, rom_1_data[56], control_circuit_1_1_oe);
  or or_38 (or_38_out, rom_1_data[52], control_circuit_1_1_oe);
  or or_39 (or_39_out, rom_1_data[48], control_circuit_1_1_oe);
  Counter #(.max('hfff), .width(12)) counter_37 (
    .load(control_circuit_2_1_out_6), .D(control_circuit_2_1_d), .count(or_36_out), .Q(counter_37_q),
    .clk(clock_1_out), .clr(in_1));  // open: carry, up
  Counter #(.max('hfff), .width(12)) counter_38 (
    .load(control_circuit_2_1_out_6), .D(control_circuit_2_1_d), .count(or_40_out), .Q(counter_38_q),
    .clk(clock_1_out), .clr(in_1));  // open: carry, up
  or or_40 (or_40_out, rom_1_data[34], control_circuit_1_1_oe);
  Counter #(.max('hfff), .width(12)) counter_39 (
    .load(control_circuit_2_1_out_6), .D(control_circuit_2_1_d), .count(or_41_out), .Q(counter_39_q),
    .clk(clock_1_out), .clr(in_1));  // open: carry, up
  or or_41 (or_41_out, rom_1_data[33], control_circuit_1_1_oe);
  Counter #(.max('hfff), .width(12)) counter_40 (
    .load(control_circuit_2_1_out_6), .D(control_circuit_2_1_d), .count(or_42_out), .Q(counter_40_q),
    .clk(clock_1_out), .clr(in_1));  // open: carry, up
  or or_42 (or_42_out, rom_1_data[32], control_circuit_1_1_oe);
  RAM #(.addrWidth(12), .asyncread("true"), .dataWidth(16)) ram_28 (
    .addr(counter_36_q), .we(rom_1_data[60]), .oe(control_circuit_1_1_oe), .clk(clock_1_out),
    .din(ram_1_dout), .dout(ram_28_dout));
  RAM #(.addrWidth(12), .asyncread("true"), .dataWidth(16)) ram_29 (
    .addr(counter_41_q), .we(rom_1_data[56]), .oe(control_circuit_1_1_oe), .clk(clock_1_out),
    .din(ram_1_dout), .dout(ram_29_dout));
  Counter #(.max('hfff), .width(12)) counter_41 (
    .load(control_circuit_1_1_out_6), .D(control_circuit_1_1_d), .count(or_37_out), .Q(counter_41_q),
    .clk(clock_1_out), .clr(in_1));  // open: carry, up
  RAM #(.addrWidth(12), .asyncread("true"), .dataWidth(16)) ram_30 (
    .addr(counter_42_q), .we(rom_1_data[52]), .oe(control_circuit_1_1_oe), .clk(clock_1_out),
    .din(ram_1_dout), .dout(ram_30_dout));
  Counter #(.max('hfff), .width(12)) counter_42 (
    .load(control_circuit_1_1_out_6), .D(control_circuit_1_1_d), .count(or_38_out), .Q(counter_42_q),
    .clk(clock_1_out), .clr(in_1));  // open: carry, up
  RAM #(.addrWidth(12), .asyncread("true"), .dataWidth(16)) ram_31 (
    .addr(counter_43_q), .we(rom_1_data[48]), .oe(control_circuit_1_1_oe), .clk(clock_1_out),
    .din(ram_1_dout), .dout(ram_31_dout));
  Counter #(.max('hfff), .width(12)) counter_43 (
    .load(control_circuit_1_1_out_6), .D(control_circuit_1_1_d), .count(or_39_out), .Q(counter_43_q),
    .clk(clock_1_out), .clr(in_1));  // open: carry, up
  RAM #(.addrWidth(12), .asyncread("true"), .dataWidth(16)) ram_32 (
    .addr(counter_37_q), .we(rom_1_data[35]), .oe(control_circuit_1_1_oe), .clk(clock_1_out),
    .din(ram_2_dout), .dout(ram_32_dout));
  RAM #(.addrWidth(12), .asyncread("true"), .dataWidth(16)) ram_33 (
    .addr(counter_38_q), .we(rom_1_data[34]), .oe(control_circuit_1_1_oe), .clk(clock_1_out),
    .din(ram_2_dout), .dout(ram_33_dout));
  RAM #(.addrWidth(12), .asyncread("true"), .dataWidth(16)) ram_34 (
    .addr(counter_39_q), .we(rom_1_data[33]), .oe(control_circuit_1_1_oe), .clk(clock_1_out),
    .din(ram_2_dout), .dout(ram_34_dout));
  RAM #(.addrWidth(12), .asyncread("true"), .dataWidth(16)) ram_35 (
    .addr(counter_40_q), .we(rom_1_data[32]), .oe(control_circuit_1_1_oe), .clk(clock_1_out),
    .din(ram_2_dout), .dout(ram_35_dout));
  Register #(.width(16)) register_2 (
    .D(ram_4_dout), .en(control_circuit_1_1_oe), .clk(clock_1_out), .Q(register_2_q));  // open: clr
  Register #(.width(16)) register_3 (
    .D(ram_5_dout), .en(control_circuit_1_1_oe), .clk(clock_1_out), .Q(register_3_q), .clr(undriven));
  Register #(.width(16)) register_4 (
    .D(ram_6_dout), .en(control_circuit_1_1_oe), .clk(clock_1_out), .Q(register_4_q));  // open: clr
  Register #(.width(16)) register_5 (
    .D(ram_7_dout), .en(control_circuit_1_1_oe), .clk(clock_1_out), .Q(register_5_q));  // open: clr
  Register #(.width(16)) register_6 (
    .D(ram_8_dout), .en(control_circuit_1_1_oe), .clk(clock_1_out), .Q(register_6_q));  // open: clr
  Register #(.width(16)) register_7 (
    .D(ram_9_dout), .en(control_circuit_1_1_oe), .clk(clock_1_out), .Q(register_7_q), .clr(undriven_2));
  Register #(.width(16)) register_8 (
    .D(ram_10_dout), .en(control_circuit_1_1_oe), .clk(clock_1_out), .Q(register_8_q));  // open: clr
  Register #(.width(16)) register_9 (
    .D(ram_11_dout), .en(control_circuit_1_1_oe), .clk(clock_1_out), .Q(register_9_q));  // open: clr
  Clock clock_1 (.out(clock_1_out));
  Register #(.width(16)) register_10 (
    .D(ram_16_dout), .en(control_circuit_1_1_oe), .clk(clock_1_out), .Q(register_10_q));  // open: clr
  Register #(.width(16)) register_11 (
    .D(ram_17_dout), .en(control_circuit_1_1_oe), .clk(clock_1_out), .Q(register_11_q));  // open: clr
  Register #(.width(16)) register_12 (
    .D(ram_18_dout), .en(control_circuit_1_1_oe), .clk(clock_1_out), .Q(register_12_q));  // open: clr
  Register #(.width(16)) register_13 (
    .D(ram_19_dout), .en(control_circuit_1_1_oe), .clk(clock_1_out), .Q(register_13_q));  // open: clr
  Register #(.width(16)) register_14 (
    .D(ram_12_dout), .en(control_circuit_1_1_oe), .clk(clock_1_out), .Q(register_14_q));  // open: clr
  Register #(.width(16)) register_15 (
    .D(ram_13_dout), .en(control_circuit_1_1_oe), .clk(clock_1_out), .Q(register_15_q), .clr(undriven_3));
  Register #(.width(16)) register_16 (
    .D(ram_14_dout), .en(control_circuit_1_1_oe), .clk(clock_1_out), .Q(register_16_q));  // open: clr
  Register #(.width(16)) register_17 (
    .D(ram_15_dout), .en(control_circuit_1_1_oe), .clk(clock_1_out), .Q(register_17_q));  // open: clr
  Register #(.width(16)) register_18 (
    .D(ram_20_dout), .en(control_circuit_1_1_oe), .clk(clock_1_out), .Q(register_18_q));  // open: clr
  Register #(.width(16)) register_19 (
    .D(ram_21_dout), .en(control_circuit_1_1_oe), .clk(clock_1_out), .Q(register_19_q));  // open: clr
  Register #(.width(16)) register_20 (
    .D(ram_22_dout), .en(control_circuit_1_1_oe), .clk(clock_1_out), .Q(register_20_q));  // open: clr
  Register #(.width(16)) register_21 (
    .D(ram_23_dout), .en(control_circuit_1_1_oe), .clk(clock_1_out), .Q(register_21_q));  // open: clr
  Register #(.width(16)) register_22 (
    .D(ram_24_dout), .en(control_circuit_1_1_oe), .clk(clock_1_out), .Q(register_22_q));  // open: clr
  Register #(.width(16)) register_23 (
    .D(ram_25_dout), .en(control_circuit_1_1_oe), .clk(clock_1_out), .Q(register_23_q), .clr(undriven_4));
  Register #(.width(16)) register_24 (
    .D(ram_26_dout), .en(control_circuit_1_1_oe), .clk(clock_1_out), .Q(register_24_q));  // open: clr
  Register #(.width(16)) register_25 (
    .D(ram_27_dout), .en(control_circuit_1_1_oe), .clk(clock_1_out), .Q(register_25_q));  // open: clr
  Register #(.width(16)) register_26 (
    .D(ram_28_dout), .en(control_circuit_1_1_oe), .clk(clock_1_out), .Q(register_26_q));  // open: clr
  Register #(.width(16)) register_27 (
    .D(ram_29_dout), .en(control_circuit_1_1_oe), .clk(clock_1_out), .Q(register_27_q));  // open: clr
  Register #(.width(16)) register_28 (
    .D(ram_30_dout), .en(control_circuit_1_1_oe), .clk(clock_1_out), .Q(register_28_q));  // open: clr
  Register #(.width(16)) register_29 (
    .D(ram_31_dout), .en(control_circuit_1_1_oe), .clk(clock_1_out), .Q(register_29_q));  // open: clr
  Register #(.width(16)) register_30 (
    .D(ram_32_dout), .en(control_circuit_1_1_oe), .clk(clock_1_out), .Q(register_30_q));  // open: clr
  Register #(.width(16)) register_31 (
    .D(ram_33_dout), .en(control_circuit_1_1_oe), .clk(clock_1_out), .Q(register_31_q), .clr(undriven_5));
  Register #(.width(16)) register_32 (
    .D(ram_34_dout), .en(control_circuit_1_1_oe), .clk(clock_1_out), .Q(register_32_q));  // open: clr
  Register #(.width(16)) register_33 (
    .D(ram_35_dout), .en(control_circuit_1_1_oe), .clk(clock_1_out), .Q(register_33_q));  // open: clr
  Counter #(.max('hfff), .width(12)) counter_44 (
    .count(and_7_out), .Q(counter_44_q), .clk(clock_1_out), .clr(in_2));  // open: load, D, carry, up
  and and_7 (and_7_out, or_43_out, or_44_out);
  RAM #(.addrWidth(12), .dataWidth(16)) ram_36 (
    .addr(counter_44_q), .we(and_7_out), .clk(clock_1_out), .din(controlled_buffer_1_out));  // open: oe, dout
  or or_43 (or_43_out, rom_1_data[31], rom_1_data[30], rom_1_data[29], rom_1_data[28], rom_1_data[27], rom_1_data[26], rom_1_data[25], rom_1_data[24], rom_1_data[7], rom_1_data[6], rom_1_data[5], rom_1_data[4], rom_1_data[3], rom_1_data[2], rom_1_data[1], rom_1_data[0]);
  RnC_Tiling_Core rnc_tiling_core_1 (
    .a1(register_2_q), .a2(register_10_q), .a3(register_18_q), .a4(register_26_q), .a5(register_3_q),
    .a6(register_11_q), .a7(register_19_q), .a8(register_27_q), .a9(register_4_q), .a10(register_12_q),
    .a11(register_20_q), .a12(register_28_q), .a13(register_5_q), .a14(register_13_q), .a15(register_21_q),
    .a16(register_29_q), .b1(register_6_q), .b5(register_7_q), .b9(register_8_q), .b13(register_9_q),
    .b2(register_14_q), .b6(register_15_q), .b10(register_16_q), .b14(register_17_q), .b3(register_22_q),
    .b7(register_23_q), .b11(register_24_q), .b15(register_25_q), .b4(register_30_q), .b8(register_31_q),
    .b12(register_32_q), .b16(register_33_q), .s1(register_34_q), .s2(register_38_q), .s3(register_42_q),
    .s4(register_46_q), .s5(register_35_q), .s6(register_39_q), .s7(register_43_q), .s8(register_47_q),
    .s9(register_36_q), .s10(register_40_q), .s11(register_44_q), .s12(register_48_q), .s13(register_37_q),
    .s14(register_41_q), .s15(register_45_q), .s16(register_49_q), .c1(rnc_tiling_core_1_c1),
    .c2(rnc_tiling_core_1_c2), .c3(rnc_tiling_core_1_c3), .c4(rnc_tiling_core_1_c4),
    .c5(rnc_tiling_core_1_c5), .c6(rnc_tiling_core_1_c6), .c7(rnc_tiling_core_1_c7),
    .c8(rnc_tiling_core_1_c8), .c9(rnc_tiling_core_1_c9), .c10(rnc_tiling_core_1_c10),
    .c11(rnc_tiling_core_1_c11), .c12(rnc_tiling_core_1_c12), .c13(rnc_tiling_core_1_c13),
    .c14(rnc_tiling_core_1_c14), .c15(rnc_tiling_core_1_c15), .c16(rnc_tiling_core_1_c16));
  control_circuit_3 control_circuit_3_1 (
    .Add(register_1_q[11:0]), .Dim(register_1_q[19:12]), .Opcode(register_1_q[23:20]),
    .CT(control_circuit_1_1_we), .Clock(clock_1_out), .RR(rom_1_data[23]), .out_7(control_circuit_3_1_out_7),
    .D(control_circuit_3_1_d), .R(control_circuit_3_1_r));
  or or_44 (or_44_out, controlled_buffer_1_out[7], controlled_buffer_1_out[0], controlled_buffer_1_out[1], controlled_buffer_1_out[2], controlled_buffer_1_out[3], controlled_buffer_1_out[4], controlled_buffer_1_out[5], controlled_buffer_1_out[6], controlled_buffer_1_out[8], controlled_buffer_1_out[9], controlled_buffer_1_out[10], controlled_buffer_1_out[11], controlled_buffer_1_out[12], controlled_buffer_1_out[13], controlled_buffer_1_out[14], controlled_buffer_1_out[15]);
  or or_45 (or_45_out, control_circuit_1_1_we, rom_1_data[30]);
  or or_46 (or_46_out, control_circuit_1_1_we, rom_1_data[29]);
  or or_47 (or_47_out, control_circuit_1_1_we, rom_1_data[28]);
  Counter #(.max('hfff), .width(12)) counter_45 (
    .load(control_circuit_3_1_out_7), .D(control_circuit_3_1_d), .count(or_48_out), .Q(counter_45_q),
    .clk(clock_1_out));  // open: carry, up, clr
  or or_48 (or_48_out, control_circuit_1_1_we, rom_1_data[31]);
  Counter #(.max('hfff), .width(12)) counter_46 (
    .load(control_circuit_3_1_out_7), .D(control_circuit_3_1_d), .count(or_45_out), .Q(counter_46_q),
    .clk(clock_1_out));  // open: carry, up, clr
  Counter #(.max('hfff), .width(12)) counter_47 (
    .load(control_circuit_3_1_out_7), .D(control_circuit_3_1_d), .count(or_46_out), .Q(counter_47_q),
    .clk(clock_1_out));  // open: carry, up, clr
  Counter #(.max('hfff), .width(12)) counter_48 (
    .load(control_circuit_3_1_out_7), .D(control_circuit_3_1_d), .count(or_47_out), .Q(counter_48_q),
    .clk(clock_1_out));  // open: carry, up, clr
  Register #(.width(16)) register_34 (
    .D(rnc_tiling_core_1_c1), .en(control_circuit_1_1_oe), .clk(clock_1_out), .Q(register_34_q),
    .clr(control_circuit_1_1_rr));
  Register #(.width(16)) register_35 (
    .D(rnc_tiling_core_1_c5), .en(control_circuit_1_1_oe), .clk(clock_1_out), .Q(register_35_q),
    .clr(control_circuit_1_1_rr));
  Register #(.width(16)) register_36 (
    .D(rnc_tiling_core_1_c9), .en(control_circuit_1_1_oe), .clk(clock_1_out), .Q(register_36_q),
    .clr(control_circuit_1_1_rr));
  Register #(.width(16)) register_37 (
    .D(rnc_tiling_core_1_c13), .en(control_circuit_1_1_oe), .clk(clock_1_out), .Q(register_37_q),
    .clr(control_circuit_1_1_rr));
  RAM #(.addrWidth(12), .asyncread("true"), .dataWidth(16)) ram_37 (
    .addr(counter_45_q), .we(control_circuit_1_1_we), .oe(rom_1_data[31]), .clk(clock_1_out),
    .din(register_34_q), .dout(ram_37_dout));
  RAM #(.addrWidth(12), .asyncread("true"), .dataWidth(16)) ram_38 (
    .addr(counter_46_q), .we(control_circuit_1_1_we), .oe(rom_1_data[30]), .clk(clock_1_out),
    .din(register_35_q), .dout(ram_38_dout));
  RAM #(.addrWidth(12), .asyncread("true"), .dataWidth(16)) ram_39 (
    .addr(counter_47_q), .we(control_circuit_1_1_we), .oe(rom_1_data[29]), .clk(clock_1_out),
    .din(register_36_q), .dout(ram_39_dout));
  RAM #(.addrWidth(12), .asyncread("true"), .dataWidth(16)) ram_40 (
    .addr(counter_48_q), .we(control_circuit_1_1_we), .oe(rom_1_data[28]), .clk(clock_1_out),
    .din(register_37_q), .dout(ram_40_dout));
  assign controlled_buffer_1_out = rom_1_data[31] ? ram_37_dout : 16'bz;  // Controlled_Buffer controlled_buffer_1
  assign controlled_buffer_1_out = rom_1_data[30] ? ram_38_dout : 16'bz;  // Controlled_Buffer controlled_buffer_2
  assign controlled_buffer_1_out = rom_1_data[29] ? ram_39_dout : 16'bz;  // Controlled_Buffer controlled_buffer_3
  assign controlled_buffer_1_out = rom_1_data[28] ? ram_40_dout : 16'bz;  // Controlled_Buffer controlled_buffer_4
  or or_49 (or_49_out, control_circuit_1_1_we, rom_1_data[27]);
  or or_50 (or_50_out, control_circuit_1_1_we, rom_1_data[26]);
  or or_51 (or_51_out, control_circuit_1_1_we, rom_1_data[25]);
  or or_52 (or_52_out, control_circuit_1_1_we, rom_1_data[24]);
  Register #(.width(16)) register_38 (
    .D(rnc_tiling_core_1_c2), .en(control_circuit_1_1_oe), .clk(clock_1_out), .Q(register_38_q),
    .clr(control_circuit_1_1_rr));
  Register #(.width(16)) register_39 (
    .D(rnc_tiling_core_1_c6), .en(control_circuit_1_1_oe), .clk(clock_1_out), .Q(register_39_q),
    .clr(control_circuit_1_1_rr));
  Register #(.width(16)) register_40 (
    .D(rnc_tiling_core_1_c10), .en(control_circuit_1_1_oe), .clk(clock_1_out), .Q(register_40_q),
    .clr(control_circuit_1_1_rr));
  Register #(.width(16)) register_41 (
    .D(rnc_tiling_core_1_c14), .en(control_circuit_1_1_oe), .clk(clock_1_out), .Q(register_41_q),
    .clr(control_circuit_1_1_rr));
  Counter #(.max('hfff), .width(12)) counter_49 (
    .load(control_circuit_3_1_out_7), .D(control_circuit_3_1_d), .count(or_49_out), .Q(counter_49_q),
    .clk(clock_1_out));  // open: carry, up, clr
  RAM #(.addrWidth(12), .asyncread("true"), .dataWidth(16)) ram_41 (
    .addr(counter_49_q), .we(control_circuit_1_1_we), .oe(rom_1_data[27]), .clk(clock_1_out),
    .din(register_38_q), .dout(ram_41_dout));
  Counter #(.max('hfff), .width(12)) counter_50 (
    .load(control_circuit_3_1_out_7), .D(control_circuit_3_1_d), .count(or_50_out), .Q(counter_50_q),
    .clk(clock_1_out));  // open: carry, up, clr
  RAM #(.addrWidth(12), .asyncread("true"), .dataWidth(16)) ram_42 (
    .addr(counter_50_q), .we(control_circuit_1_1_we), .oe(rom_1_data[26]), .clk(clock_1_out),
    .din(register_39_q), .dout(ram_42_dout));
  Counter #(.max('hfff), .width(12)) counter_51 (
    .load(control_circuit_3_1_out_7), .D(control_circuit_3_1_d), .count(or_51_out), .Q(counter_51_q),
    .clk(clock_1_out));  // open: carry, up, clr
  RAM #(.addrWidth(12), .asyncread("true"), .dataWidth(16)) ram_43 (
    .addr(counter_51_q), .we(control_circuit_1_1_we), .oe(rom_1_data[25]), .clk(clock_1_out),
    .din(register_40_q), .dout(ram_43_dout));
  Counter #(.max('hfff), .width(12)) counter_52 (
    .load(control_circuit_3_1_out_7), .D(control_circuit_3_1_d), .count(or_52_out), .Q(counter_52_q),
    .clk(clock_1_out));  // open: carry, up, clr
  RAM #(.addrWidth(12), .asyncread("true"), .dataWidth(16)) ram_44 (
    .addr(counter_52_q), .we(control_circuit_1_1_we), .oe(rom_1_data[24]), .clk(clock_1_out),
    .din(register_41_q), .dout(ram_44_dout));
  assign controlled_buffer_1_out = rom_1_data[27] ? ram_41_dout : 16'bz;  // Controlled_Buffer controlled_buffer_5
  assign controlled_buffer_1_out = rom_1_data[26] ? ram_42_dout : 16'bz;  // Controlled_Buffer controlled_buffer_6
  assign controlled_buffer_1_out = rom_1_data[25] ? ram_43_dout : 16'bz;  // Controlled_Buffer controlled_buffer_7
  assign controlled_buffer_1_out = rom_1_data[24] ? ram_44_dout : 16'bz;  // Controlled_Buffer controlled_buffer_8
  or or_53 (or_53_out, control_circuit_1_1_we, rom_1_data[7]);
  or or_54 (or_54_out, control_circuit_1_1_we, rom_1_data[6]);
  or or_55 (or_55_out, control_circuit_1_1_we, rom_1_data[5]);
  or or_56 (or_56_out, control_circuit_1_1_we, rom_1_data[4]);
  Register #(.width(16)) register_42 (
    .D(rnc_tiling_core_1_c3), .en(control_circuit_1_1_oe), .clk(clock_1_out), .Q(register_42_q),
    .clr(control_circuit_1_1_rr));
  Register #(.width(16)) register_43 (
    .D(rnc_tiling_core_1_c7), .en(control_circuit_1_1_oe), .clk(clock_1_out), .Q(register_43_q),
    .clr(control_circuit_1_1_rr));
  Register #(.width(16)) register_44 (
    .D(rnc_tiling_core_1_c11), .en(control_circuit_1_1_oe), .clk(clock_1_out), .Q(register_44_q),
    .clr(control_circuit_1_1_rr));
  Register #(.width(16)) register_45 (
    .D(rnc_tiling_core_1_c15), .en(control_circuit_1_1_oe), .clk(clock_1_out), .Q(register_45_q),
    .clr(control_circuit_1_1_rr));
  Counter #(.max('hfff), .width(12)) counter_53 (
    .load(control_circuit_3_1_out_7), .D(control_circuit_3_1_d), .count(or_53_out), .Q(counter_53_q),
    .clk(clock_1_out));  // open: carry, up, clr
  RAM #(.addrWidth(12), .asyncread("true"), .dataWidth(16)) ram_45 (
    .addr(counter_53_q), .we(control_circuit_1_1_we), .oe(rom_1_data[7]), .clk(clock_1_out),
    .din(register_42_q), .dout(ram_45_dout));
  Counter #(.max('hfff), .width(12)) counter_54 (
    .load(control_circuit_3_1_out_7), .D(control_circuit_3_1_d), .count(or_54_out), .Q(counter_54_q),
    .clk(clock_1_out));  // open: carry, up, clr
  RAM #(.addrWidth(12), .asyncread("true"), .dataWidth(16)) ram_46 (
    .addr(counter_54_q), .we(control_circuit_1_1_we), .oe(rom_1_data[6]), .clk(clock_1_out),
    .din(register_43_q), .dout(ram_46_dout));
  Counter #(.max('hfff), .width(12)) counter_55 (
    .load(control_circuit_3_1_out_7), .D(control_circuit_3_1_d), .count(or_55_out), .Q(counter_55_q),
    .clk(clock_1_out));  // open: carry, up, clr
  RAM #(.addrWidth(12), .asyncread("true"), .dataWidth(16)) ram_47 (
    .addr(counter_55_q), .we(control_circuit_1_1_we), .oe(rom_1_data[5]), .clk(clock_1_out),
    .din(register_44_q), .dout(ram_47_dout));
  Counter #(.max('hfff), .width(12)) counter_56 (
    .load(control_circuit_3_1_out_7), .D(control_circuit_3_1_d), .count(or_56_out), .Q(counter_56_q),
    .clk(clock_1_out));  // open: carry, up, clr
  RAM #(.addrWidth(12), .asyncread("true"), .dataWidth(16)) ram_48 (
    .addr(counter_56_q), .we(control_circuit_1_1_we), .oe(rom_1_data[4]), .clk(clock_1_out),
    .din(register_45_q), .dout(ram_48_dout));
  assign controlled_buffer_1_out = rom_1_data[7] ? ram_45_dout : 16'bz;  // Controlled_Buffer controlled_buffer_9
  assign controlled_buffer_1_out = rom_1_data[6] ? ram_46_dout : 16'bz;  // Controlled_Buffer controlled_buffer_10
  assign controlled_buffer_1_out = rom_1_data[5] ? ram_47_dout : 16'bz;  // Controlled_Buffer controlled_buffer_11
  assign controlled_buffer_1_out = rom_1_data[4] ? ram_48_dout : 16'bz;  // Controlled_Buffer controlled_buffer_12
  or or_57 (or_57_out, control_circuit_1_1_we, rom_1_data[3]);
  or or_58 (or_58_out, control_circuit_1_1_we, rom_1_data[2]);
  or or_59 (or_59_out, control_circuit_1_1_we, rom_1_data[1]);
  or or_60 (or_60_out, control_circuit_1_1_we, rom_1_data[0]);
  Register #(.width(16)) register_46 (
    .D(rnc_tiling_core_1_c4), .en(control_circuit_1_1_oe), .clk(clock_1_out), .Q(register_46_q),
    .clr(control_circuit_1_1_rr));
  Register #(.width(16)) register_47 (
    .D(rnc_tiling_core_1_c8), .en(control_circuit_1_1_oe), .clk(clock_1_out), .Q(register_47_q),
    .clr(control_circuit_1_1_rr));
  Register #(.width(16)) register_48 (
    .D(rnc_tiling_core_1_c12), .en(control_circuit_1_1_oe), .clk(clock_1_out), .Q(register_48_q),
    .clr(control_circuit_1_1_rr));
  Register #(.width(16)) register_49 (
    .D(rnc_tiling_core_1_c16), .en(control_circuit_1_1_oe), .clk(clock_1_out), .Q(register_49_q),
    .clr(control_circuit_1_1_rr));
  Counter #(.max('hfff), .width(12)) counter_57 (
    .load(control_circuit_3_1_out_7), .D(control_circuit_3_1_d), .count(or_57_out), .Q(counter_57_q),
    .clk(clock_1_out));  // open: carry, up, clr
  RAM #(.addrWidth(12), .asyncread("true"), .dataWidth(16)) ram_49 (
    .addr(counter_57_q), .we(control_circuit_1_1_we), .oe(rom_1_data[3]), .clk(clock_1_out),
    .din(register_46_q), .dout(ram_49_dout));
  Counter #(.max('hfff), .width(12)) counter_58 (
    .load(control_circuit_3_1_out_7), .D(control_circuit_3_1_d), .count(or_58_out), .Q(counter_58_q),
    .clk(clock_1_out));  // open: carry, up, clr
  RAM #(.addrWidth(12), .asyncread("true"), .dataWidth(16)) ram_50 (
    .addr(counter_58_q), .we(control_circuit_1_1_we), .oe(rom_1_data[2]), .clk(clock_1_out),
    .din(register_47_q), .dout(ram_50_dout));
  Counter #(.max('hfff), .width(12)) counter_59 (
    .load(control_circuit_3_1_out_7), .D(control_circuit_3_1_d), .count(or_59_out), .Q(counter_59_q),
    .clk(clock_1_out));  // open: carry, up, clr
  RAM #(.addrWidth(12), .asyncread("true"), .dataWidth(16)) ram_51 (
    .addr(counter_59_q), .we(control_circuit_1_1_we), .oe(rom_1_data[1]), .clk(clock_1_out),
    .din(register_48_q), .dout(ram_51_dout));
  Counter #(.max('hfff), .width(12)) counter_60 (
    .load(control_circuit_3_1_out_7), .D(control_circuit_3_1_d), .count(or_60_out), .Q(counter_60_q),
    .clk(clock_1_out));  // open: carry, up, clr
  RAM #(.addrWidth(12), .asyncread("true"), .dataWidth(16)) ram_52 (
    .addr(counter_60_q), .we(control_circuit_1_1_we), .oe(rom_1_data[0]), .clk(clock_1_out),
    .din(register_49_q), .dout(ram_52_dout));
  assign controlled_buffer_1_out = rom_1_data[3] ? ram_49_dout : 16'bz;  // Controlled_Buffer controlled_buffer_13
  assign controlled_buffer_1_out = rom_1_data[2] ? ram_50_dout : 16'bz;  // Controlled_Buffer controlled_buffer_14
  assign controlled_buffer_1_out = rom_1_data[1] ? ram_51_dout : 16'bz;  // Controlled_Buffer controlled_buffer_15
  assign controlled_buffer_1_out = rom_1_data[0] ? ram_52_dout : 16'bz;  // Controlled_Buffer controlled_buffer_16

  // Notes on the sheet:
  //   Matric 1
  //   Matric 2
  //   Matric 3
  //   Matric 4
  //   Matric 5
  //   contents of rom_1 (hex, n*v repeats v):
  //   100 256*0 8000000000000000 4000000000000000 2000000000000400 1000000000000000 80000 200
  //   800000000000000 400000000000000 200000000000400 100000000000000 40000 200 80000000000000
  //   40000000000000 20000000000400 10000000000000 20000 200 8000000000000 4000000000000 2000000000400
  //   1000000000000 10000 200 100000 229*0 800 0 800000000000 400000000000 200000000400 100000000000 80000
  //   200 80000000000 40000000000 20000000400 10000000000 40000 200 8000000000 4000000000 2000000400
  //   1000000000 20000 200 800000000 400000000 200000400 100000000 10000 200 100000 229*0 800 0 800000
  //   80000000 8000000 400080 8 8000 200000 40000000 4000000 400040 4 4000 200000 20000000 2000000 400020
  //   2 2000 200000 10000000 1000000 400010 1 1000 200000 100000 228*0 800 0 800000
  //   Matric 6
endmodule

module control_circuit (
  input  a1,
  input  a2,
  input  a3,
  input  a4,
  input  a5,
  input  a6,
  input  a7,
  input  a8,
  input  a9,
  input  a10,
  input  a11,
  input  a12,
  input  a13,
  input  a14,
  input  a15,
  input  a16,
  input  b1,
  input  b2,
  input  b3,
  input  b4,
  input  b5,
  input  b6,
  input  b7,
  input  b8,
  input  b9,
  input  b10,
  input  b11,
  input  b12,
  input  b13,
  input  b14,
  input  b15,
  input  b16,
  input  aB1,
  input  aB2,
  input  aB3,
  input  aB4,
  input  bB1,
  input  bB2,
  input  bB3,
  input  bB4,
  input  ct,
  input  Clock,
  input  R,
  input  [7:0] Dim,
  input  ct1,
  input  R1,
  input  ct2,
  input  R2,
  input  C1,
  input  C2,
  input  C3,
  input  C4,
  input  C5,
  input  C6,
  input  C7,
  input  C8,
  input  C9,
  input  C10,
  input  C11,
  input  C12,
  input  C13,
  input  C14,
  input  C15,
  input  C16,
  input  [3:0] Opcode,
  output DC,
  output [7:0] D
);

  wire and_1_out, and_2_out, and_3_out, and_4_out, and_5_out, and_6_out, and_7_out, and_8_out, and_9_out,
       and_10_out, and_11_out, and_12_out, and_13_out, and_14_out, and_15_out, and_16_out, and_17_out,
       and_18_out, and_19_out, and_20_out, comparator_1_eq, comparator_2_eq, comparator_3_eq,
       comparator_4_eq, comparator_5_eq, comparator_6_eq, comparator_7_eq, or_1_out, or_2_out, or_3_out,
       or_4_out, or_5_out, or_6_out, or_7_out, or_8_out, or_9_out, or_10_out, or_11_out, or_12_out,
       or_13_out, or_14_out, or_15_out, or_16_out, or_17_out, or_18_out, or_19_out, or_20_out, or_21_out,
       or_22_out, or_23_out, or_24_out, or_25_out, or_26_out, or_27_out, or_28_out;
  wire [3:0] counter_1_q, counter_2_q, counter_3_q, counter_4_q, divider_1_out;

  Comparator #(.width(4)) comparator_1 (.a(Opcode), .b(4'b0001), .eq(comparator_1_eq));  // open: gt, lt
  Comparator #(.width(4)) comparator_2 (.a(Opcode), .b(4'b0010), .eq(comparator_2_eq));  // open: gt, lt
  Comparator #(.width(4)) comparator_3 (.a(Opcode), .b(4'b0011), .eq(comparator_3_eq));  // open: gt, lt
  or or_1 (or_1_out, C1, C2, C3, C4);
  or or_2 (or_2_out, C5, C6, C7, C8);
  or or_3 (or_3_out, C9, C10, C11, C12);
  or or_4 (or_4_out, C13, C14, C15, C16);
  or or_5 (or_5_out, a1, a2, a3, a4);
  or or_6 (or_6_out, a5, a6, a7, a8);
  or or_7 (or_7_out, a9, a10, a11, a12);
  or or_8 (or_8_out, a13, a14, a15, a16);
  or or_9 (or_9_out, b1, b2, b3, b4);
  or or_10 (or_10_out, b5, b6, b7, b8);
  or or_11 (or_11_out, b9, b10, b11, b12);
  or or_12 (or_12_out, b13, b14, b15, b16);
  and and_1 (and_1_out, or_14_out, or_13_out);
  or or_13 (or_13_out, Opcode[1], Opcode[0], Opcode[2], Opcode[3]);
  or or_14 (or_14_out, comparator_1_eq, comparator_2_eq);
  Counter #(.max('hf), .width(4)) counter_1 (
    .count(ct), .Q(counter_1_q), .clk(Clock), .clr(R));  // open: load, D, carry, up
  Divider #(.width(4)) divider_1 (.a(Dim[3:0]), .b(4'b0100), .out(divider_1_out));  // open: upper, rem
  and and_2 (and_2_out, or_13_out, comparator_3_eq);
  or or_15 (or_15_out, counter_1_q[1], counter_1_q[0], counter_1_q[2], counter_1_q[3]);
  Comparator #(.width(4)) comparator_4 (.a(counter_1_q), .b(divider_1_out), .eq(comparator_4_eq));  // open: gt, lt
  and and_3 (and_3_out, comparator_4_eq, or_15_out);
  and and_4 (and_4_out, or_5_out, and_3_out);
  and and_5 (and_5_out, or_6_out, and_3_out);
  and and_6 (and_6_out, or_7_out, and_3_out);
  and and_7 (and_7_out, or_8_out, and_3_out);
  and and_8 (and_8_out, or_9_out, and_3_out);
  and and_9 (and_9_out, or_10_out, and_3_out);
  and and_10 (and_10_out, or_11_out, and_3_out);
  and and_11 (and_11_out, or_12_out, and_3_out);
  and and_12 (and_12_out, and_1_out, ct1);
  Counter #(.max('hf), .width(4)) counter_2 (
    .count(R), .Q(counter_2_q), .clk(Clock), .clr(R1));  // open: load, D, carry, up
  or or_16 (or_16_out, and_4_out, and_8_out);
  or or_17 (or_17_out, and_9_out, and_5_out);
  and and_13 (and_13_out, ct1, and_2_out);
  Comparator #(.width(4)) comparator_5 (.a(counter_2_q), .b(Dim[7:4]), .eq(comparator_5_eq));  // open: gt, lt
  or or_18 (or_18_out, and_6_out, and_10_out);
  or or_19 (or_19_out, and_7_out, and_11_out);
  or or_20 (or_20_out, aB1, and_12_out);
  buf or_21 (or_21_out, aB2);  // OR_Gate
  buf or_22 (or_22_out, aB3);  // OR_Gate
  buf or_23 (or_23_out, aB4);  // OR_Gate
  and and_14 (and_14_out, or_24_out, comparator_5_eq);
  or or_24 (or_24_out, counter_2_q[1], counter_2_q[0], counter_2_q[2], counter_2_q[3]);
  or or_25 (or_25_out, and_14_out, and_16_out);
  assign D = or_16_out ? 8'h6 : 8'bz;  // Controlled_Buffer controlled_buffer_1
  assign D = or_17_out ? 8'hc : 8'bz;  // Controlled_Buffer controlled_buffer_2
  assign D = or_18_out ? 8'h12 : 8'bz;  // Controlled_Buffer controlled_buffer_3
  assign D = or_19_out ? 8'h18 : 8'bz;  // Controlled_Buffer controlled_buffer_4
  assign D = or_20_out ? 8'h1 : 8'bz;  // Controlled_Buffer controlled_buffer_5
  assign D = or_21_out ? 8'h7 : 8'bz;  // Controlled_Buffer controlled_buffer_6
  assign D = or_22_out ? 8'hd : 8'bz;  // Controlled_Buffer controlled_buffer_7
  assign D = or_23_out ? 8'h13 : 8'bz;  // Controlled_Buffer controlled_buffer_8
  assign D = or_25_out ? 8'h19 : 8'bz;  // Controlled_Buffer controlled_buffer_9
  Counter #(.max('hf), .width(4)) counter_3 (
    .count(ct2), .Q(counter_3_q), .clk(Clock), .clr(R2));  // open: load, D, carry, up
  or or_26 (or_26_out, counter_3_q[1], counter_3_q[0], counter_3_q[2], counter_3_q[3]);
  Comparator #(.width(4)) comparator_6 (.a(counter_3_q), .b(divider_1_out), .eq(comparator_6_eq));  // open: gt, lt
  and and_15 (and_15_out, comparator_6_eq, or_26_out);
  Counter #(.max('hf), .width(4)) counter_4 (
    .count(R2), .Q(counter_4_q), .clk(Clock), .clr(R1));  // open: load, D, carry, up
  or or_27 (or_27_out, and_13_out, bB1);
  or or_28 (or_28_out, counter_4_q[1], counter_4_q[0], counter_4_q[2], counter_4_q[3]);
  Comparator #(.width(4)) comparator_7 (.a(counter_4_q), .b(Dim[7:4]), .eq(comparator_7_eq));  // open: gt, lt
  and and_16 (and_16_out, or_28_out, comparator_7_eq);
  assign D = or_27_out ? 8'h2 : 8'bz;  // Controlled_Buffer controlled_buffer_10
  assign D = bB2 ? 8'h8 : 8'bz;  // Controlled_Buffer controlled_buffer_11
  assign D = bB3 ? 8'he : 8'bz;  // Controlled_Buffer controlled_buffer_12
  assign D = bB4 ? 8'h14 : 8'bz;  // Controlled_Buffer controlled_buffer_13
  and and_17 (and_17_out, and_15_out, or_1_out);
  and and_18 (and_18_out, and_15_out, or_2_out);
  and and_19 (and_19_out, and_15_out, or_3_out);
  and and_20 (and_20_out, and_15_out, or_4_out);
  assign D = and_17_out ? 8'h7 : 8'bz;  // Controlled_Buffer controlled_buffer_14
  assign D = and_18_out ? 8'hd : 8'bz;  // Controlled_Buffer controlled_buffer_15
  assign D = and_19_out ? 8'h13 : 8'bz;  // Controlled_Buffer controlled_buffer_16
  assign D = and_20_out ? 8'h19 : 8'bz;  // Controlled_Buffer controlled_buffer_17
  or or_29 (DC, or_27_out, bB2, bB3, or_16_out, or_17_out, or_18_out, or_19_out, or_25_out, bB4, or_20_out, or_21_out, or_22_out, or_23_out, and_17_out, and_18_out, and_19_out, and_20_out);
endmodule

module control_circuit_1 (
  input  [11:0] add,
  input  [7:0] dim,
  input  clock,
  input  R,
  input  [3:0] Opcode,
  output out_6,
  output [11:0] D,
  output OE,
  output WE,
  output RR
);

  wire and_2_out, and_3_out, and_5_out, comparator_1_eq, comparator_2_eq, comparator_3_eq, comparator_4_eq,
       comparator_5_eq, comparator_6_eq, nor_1_out, not_1_out, not_2_out, or_1_out, or_3_out, or_4_out,
       or_5_out, or_6_out, register_2_q;
  wire [3:0] divider_1_out, divider_2_out, register_1_q;
  wire [11:0] adder_1_out, bit_extender_1_out, bit_extender_2_out, counter_1_q, counter_2_q, counter_3_q,
       counter_4_q, multiplier_1_out, multiplier_2_out, subtractor_1_out;

  Register #(.width(4)) register_1 (.D(Opcode), .en(clock), .clk(clock), .Q(register_1_q));  // open: clr
  nor nor_1 (nor_1_out, Opcode[0], Opcode[1], Opcode[2], Opcode[3]);
  Comparator #(.width(4)) comparator_1 (.a(register_1_q), .b(4'b0100), .eq(comparator_1_eq));  // open: gt, lt
  Divider #(.width(4)) divider_1 (.a(dim[3:0]), .b(4'b0100), .out(divider_1_out));  // open: upper, rem
  Divider #(.width(4)) divider_2 (.a(dim[7:4]), .b(4'b0100), .out(divider_2_out));  // open: upper, rem
  Counter #(.max('hfff), .width(12)) counter_1 (
    .load(and_2_out), .D({12{1'b0}}), .count(OE), .Q(counter_1_q), .clk(clock), .clr(nor_1_out));  // open: carry, up
  and and_1 (OE, comparator_1_eq, not_2_out, not_1_out);
  Comparator #(.width(12)) comparator_2 (
    .a(counter_1_q), .b(bit_extender_1_out), .eq(comparator_2_eq));  // open: gt, lt
  not not_1 (not_1_out, or_4_out);
  not not_2 (not_2_out, out_6);
  and and_2 (and_2_out, comparator_2_eq, or_1_out);
  or or_1 (or_1_out, counter_1_q[5], counter_1_q[0], counter_1_q[1], counter_1_q[2], counter_1_q[3], counter_1_q[4], counter_1_q[6], counter_1_q[7], counter_1_q[8], counter_1_q[9], counter_1_q[10], counter_1_q[11]);
  Counter #(.max('hfff), .width(12)) counter_2 (
    .load(and_3_out), .D({12{1'b0}}), .count(OE), .Q(counter_2_q), .clk(clock), .clr(nor_1_out));  // open: carry, up
  assign bit_extender_1_out = {{8{divider_1_out[3]}}, divider_1_out};  // Bit_Extender bit_extender_1
  assign bit_extender_2_out = {{8{divider_2_out[3]}}, divider_2_out};  // Bit_Extender bit_extender_2
  or or_2 (out_6, R, and_2_out);
  Multiplier #(.width(12)) multiplier_1 (
    .a(bit_extender_1_out), .b(bit_extender_2_out), .out(multiplier_1_out));  // open: cin, cout
  Counter #(.max('hfff), .width(12)) counter_3 (
    .load(RR), .D({12{1'b0}}), .count(comparator_1_eq), .Q(counter_3_q), .clk(clock), .clr(nor_1_out));  // open: carry, up
  Subtractor #(.width(12)) subtractor_1 (.a(multiplier_1_out), .b(12'h1), .out(subtractor_1_out));  // open: bin, bout
  Comparator #(.width(12)) comparator_3 (.a(counter_2_q), .b(subtractor_1_out), .eq(comparator_3_eq));  // open: gt, lt
  Adder #(.width(12)) adder_1 (.a(bit_extender_1_out), .b(12'h2), .out(adder_1_out));  // open: cin, cout
  Counter #(.max('hfff), .width(12)) counter_4 (
    .load(and_5_out), .D({12{1'b0}}), .count(and_3_out), .Q(counter_4_q), .clk(clock), .clr(nor_1_out));  // open: carry, up
  and and_3 (and_3_out, comparator_3_eq, or_3_out);
  or or_3 (or_3_out, counter_2_q[5], counter_2_q[0], counter_2_q[1], counter_2_q[2], counter_2_q[3], counter_2_q[4], counter_2_q[6], counter_2_q[7], counter_2_q[8], counter_2_q[9], counter_2_q[10], counter_2_q[11]);
  or or_4 (or_4_out, register_2_q, WE, RR);
  and and_4 (WE, comparator_4_eq, or_5_out);
  Comparator #(.width(12)) comparator_4 (.a(counter_3_q), .b(adder_1_out), .gt(RR), .eq(comparator_4_eq));  // open: lt
  or or_5 (or_5_out, counter_3_q[5], counter_3_q[0], counter_3_q[1], counter_3_q[2], counter_3_q[3], counter_3_q[4], counter_3_q[6], counter_3_q[7], counter_3_q[8], counter_3_q[9], counter_3_q[10], counter_3_q[11]);
  Multiplier #(.width(12)) multiplier_2 (
    .a(bit_extender_1_out), .b(counter_4_q), .out(multiplier_2_out));  // open: cin, cout
  Comparator #(.width(12)) comparator_5 (
    .a(counter_4_q), .b(bit_extender_2_out), .eq(comparator_5_eq));  // open: gt, lt
  Comparator #(.width(12)) comparator_6 (
    .a(bit_extender_1_out), .b(counter_1_q), .eq(comparator_6_eq));  // open: gt, lt
  Register #(.width(1)) register_2 (.D(RR), .en(clock), .clk(clock), .Q(register_2_q));  // open: clr
  or or_6 (or_6_out, counter_4_q[5], counter_4_q[0], counter_4_q[1], counter_4_q[2], counter_4_q[3], counter_4_q[4], counter_4_q[6], counter_4_q[7], counter_4_q[8], counter_4_q[9], counter_4_q[10], counter_4_q[11]);
  Adder #(.width(12)) adder_2 (.a(add), .b(multiplier_2_out), .out(D));  // open: cin, cout
  and and_5 (and_5_out, comparator_5_eq, or_6_out, comparator_6_eq);
endmodule

module control_circuit_2 (
  input  [11:0] add,
  input  [7:0] dim,
  input  clock,
  input  OE,
  input  R,
  output out_6,
  output [11:0] D
);

  wire and_1_out, comparator_1_eq, nor_1_out, or_1_out;
  wire [3:0] counter_1_q, divider_1_out, divider_2_out, multiplier_1_out;

  nor nor_1 (nor_1_out, dim[3], dim[0], dim[1], dim[2], dim[4], dim[5], dim[6], dim[7]);
  Counter #(.max('hf), .width(4)) counter_1 (
    .load(and_1_out), .D(4'b0000), .count(OE), .Q(counter_1_q), .clk(clock), .clr(nor_1_out));  // open: carry, up
  Divider #(.width(4)) divider_1 (.a(dim[3:0]), .b(4'b0100), .out(divider_1_out));  // open: upper, rem
  Divider #(.width(4)) divider_2 (.a(dim[7:4]), .b(4'b0100), .out(divider_2_out));  // open: upper, rem
  Multiplier #(.width(4)) multiplier_1 (
    .a(divider_2_out), .b(divider_1_out), .out(multiplier_1_out));  // open: cin, cout
  Subtractor #(.width(4)) subtractor_1 (.b(4'b0001));  // open: a, out, bin, bout
  or or_1 (or_1_out, counter_1_q[0], counter_1_q[2], counter_1_q[3], counter_1_q[1]);
  Comparator #(.width(4)) comparator_1 (.a(counter_1_q), .b(multiplier_1_out), .eq(comparator_1_eq));  // open: gt, lt
  or or_2 (out_6, and_1_out, R);
  and and_1 (and_1_out, comparator_1_eq, or_1_out);

  assign D = add;
endmodule

module control_circuit_3 (
  input  [11:0] Add,
  input  [7:0] Dim,
  input  [3:0] Opcode,
  input  CT,
  input  Clock,
  input  RR,
  output out_7,
  output [11:0] D,
  output R
);

  wire and_1_out, comparator_1_eq, comparator_2_eq, comparator_3_eq, nor_1_out, or_1_out;
  wire [3:0] counter_2_q, divider_1_out, divider_2_out;
  wire [11:0] bit_extender_1_out, bit_extender_2_out, counter_1_q, multiplier_1_out;

  Comparator #(.width(4)) comparator_1 (.a(Opcode), .b(4'b0100), .eq(comparator_1_eq));  // open: gt, lt
  nor nor_1 (nor_1_out, Opcode[0], Opcode[1], Opcode[2], Opcode[3]);
  assign bit_extender_1_out = {{8{divider_1_out[3]}}, divider_1_out};  // Bit_Extender bit_extender_1
  Divider #(.width(4)) divider_1 (.a(Dim[3:0]), .b(4'b0100), .out(divider_1_out));  // open: upper, rem
  assign bit_extender_2_out = {{8{divider_2_out[3]}}, divider_2_out};  // Bit_Extender bit_extender_2
  Divider #(.width(4)) divider_2 (.a(Dim[7:4]), .b(4'b0100), .out(divider_2_out));  // open: upper, rem
  Multiplier #(.width(12)) multiplier_1 (
    .a(bit_extender_1_out), .b(bit_extender_2_out), .out(multiplier_1_out));  // open: cin, cout
  Counter #(.max('hfff), .width(12)) counter_1 (
    .count(CT), .Q(counter_1_q), .clk(Clock), .clr(R));  // open: load, D, carry, up
  Adder #(.width(4)) adder_1 (.b(4'b0001));  // open: a, out, cin, cout
  or or_1 (or_1_out, multiplier_1_out[0], multiplier_1_out[1], multiplier_1_out[2], multiplier_1_out[3], multiplier_1_out[4], multiplier_1_out[5], multiplier_1_out[7], multiplier_1_out[8], multiplier_1_out[9], multiplier_1_out[10], multiplier_1_out[11], multiplier_1_out[6]);
  and and_1 (and_1_out, or_1_out, comparator_2_eq);
  Comparator #(.width(12)) comparator_2 (.a(multiplier_1_out), .b(counter_1_q), .eq(comparator_2_eq));  // open: gt, lt
  Counter #(.max('hf), .width(4)) counter_2 (
    .count(and_1_out), .Q(counter_2_q), .clk(Clock), .clr(nor_1_out));  // open: load, D, carry, up
  Comparator #(.width(4)) comparator_3 (.a(counter_2_q), .b(4'b0001), .eq(comparator_3_eq));  // open: gt, lt
  and and_2 (R, comparator_1_eq, comparator_3_eq);

  assign D = Add;
  assign out_7 = RR;
endmodule
module Systrolic (
  input  in_1,
  input  in_2
);

  wire and_1_out, and_2_out, and_3_out, and_4_out, and_5_out, and_6_out, clock_1_out, comparator_1_eq,
       comparator_1_gt, comparator_1_lt, comparator_2_eq, comparator_2_gt, comparator_2_lt, comparator_3_eq,
       comparator_3_gt, comparator_3_lt, comparator_4_eq, comparator_4_gt, comparator_4_lt, comparator_5_eq,
       comparator_5_gt, comparator_5_lt, comparator_6_eq, comparator_6_gt, comparator_6_lt,
       control_circuit_1_1_oe, control_circuit_1_1_out_6, control_circuit_1_1_rr, control_circuit_1_1_we,
       control_circuit_1_dc, control_circuit_2_1_out_6, control_circuit_3_1_out_7, control_circuit_3_1_r,
       or_1_out, or_2_out, or_3_out, or_4_out, or_5_out, or_6_out, or_8_out, or_9_out, or_10_out, or_11_out,
       or_12_out, or_13_out, or_14_out, or_15_out, or_16_out, or_17_out, or_18_out, or_19_out, or_20_out,
       or_21_out, or_22_out, or_23_out, or_24_out, or_25_out, or_26_out, or_27_out, or_28_out, or_29_out,
       or_30_out, or_31_out, or_32_out, or_33_out, or_34_out, or_35_out, or_36_out, or_37_out, or_38_out,
       or_39_out, or_40_out, or_41_out, or_42_out, or_43_out, or_44_out, or_45_out, or_46_out, or_47_out,
       or_48_out, or_49_out, or_50_out, or_51_out, or_52_out, or_53_out, or_54_out, or_55_out, or_56_out,
       or_57_out, or_58_out, or_59_out, or_60_out, undriven, undriven_2, undriven_3, undriven_4, undriven_5,
       undriven_6;
  wire [3:0] counter_3_q, counter_3_q_2, counter_3_q_3, counter_3_q_4, counter_5_q, counter_5_q_2,
       counter_5_q_3, counter_5_q_4, counter_6_q, counter_6_q_2, counter_6_q_3, counter_6_q_4, counter_7_q,
       counter_7_q_2, counter_7_q_3, counter_7_q_4, counter_8_q, counter_8_q_2, counter_8_q_3, counter_8_q_4,
       counter_10_q, counter_10_q_2, counter_10_q_3, counter_10_q_4, counter_11_q, counter_11_q_2,
       counter_11_q_3, counter_11_q_4;
  wire [7:0] control_circuit_1_d, counter_4_q, counter_9_q;
  wire [11:0] control_circuit_1_1_d, control_circuit_2_1_d, control_circuit_3_1_d, counter_1_q, counter_2_q,
       counter_12_q, counter_13_q, counter_14_q, counter_15_q, counter_16_q, counter_17_q, counter_18_q,
       counter_19_q, counter_20_q, counter_21_q, counter_22_q, counter_23_q, counter_24_q, counter_25_q,
       counter_26_q, counter_27_q, counter_28_q, counter_29_q, counter_30_q, counter_31_q, counter_32_q,
       counter_33_q, counter_34_q, counter_35_q, counter_36_q, counter_37_q, counter_38_q, counter_39_q,
       counter_40_q, counter_41_q, counter_42_q, counter_43_q, counter_44_q, counter_45_q, counter_46_q,
       counter_47_q, counter_48_q, counter_49_q, counter_50_q, counter_51_q, counter_52_q, counter_53_q,
       counter_54_q, counter_55_q, counter_56_q, counter_57_q, counter_58_q, counter_59_q, counter_60_q;
  wire [15:0] controlled_buffer_1_out, ram_1_dout, ram_2_dout, ram_4_dout, ram_5_dout, ram_6_dout,
       ram_7_dout, ram_8_dout, ram_9_dout, ram_10_dout, ram_11_dout, ram_12_dout, ram_13_dout, ram_14_dout,
       ram_15_dout, ram_16_dout, ram_17_dout, ram_18_dout, ram_19_dout, ram_20_dout, ram_21_dout,
       ram_22_dout, ram_23_dout, ram_24_dout, ram_25_dout, ram_26_dout, ram_27_dout, ram_28_dout,
       ram_29_dout, ram_30_dout, ram_31_dout, ram_32_dout, ram_33_dout, ram_34_dout, ram_35_dout,
       ram_37_dout, ram_38_dout, ram_39_dout, ram_40_dout, ram_41_dout, ram_42_dout, ram_43_dout,
       ram_44_dout, ram_45_dout, ram_46_dout, ram_47_dout, ram_48_dout, ram_49_dout, ram_50_dout,
       ram_51_dout, ram_52_dout, register_2_q, register_3_q, register_4_q, register_5_q, register_6_q,
       register_7_q, register_8_q, register_9_q, register_10_q, register_11_q, register_12_q, register_13_q,
       register_14_q, register_15_q, register_16_q, register_17_q, register_18_q, register_19_q,
       register_20_q, register_21_q, register_22_q, register_23_q, register_24_q, register_25_q,
       register_26_q, register_27_q, register_28_q, register_29_q, register_30_q, register_31_q,
       register_32_q, register_33_q, register_34_q, register_35_q, register_36_q, register_37_q,
       register_39_q, register_40_q, register_41_q, register_42_q, register_44_q, register_45_q,
       register_46_q, register_47_q, register_48_q, register_49_q, register_50_q, register_51_q,
       rnc_tiling_core_1_c1, rnc_tiling_core_1_c2, rnc_tiling_core_1_c3, rnc_tiling_core_1_c4,
       rnc_tiling_core_1_c5, rnc_tiling_core_1_c6, rnc_tiling_core_1_c7, rnc_tiling_core_1_c8,
       rnc_tiling_core_1_c9, rnc_tiling_core_1_c10, rnc_tiling_core_1_c11, rnc_tiling_core_1_c12,
       rnc_tiling_core_1_c13, rnc_tiling_core_1_c14, rnc_tiling_core_1_c15, rnc_tiling_core_1_c16;
  wire [23:0] ram_3_dout, register_1_q;
  wire [63:0] rom_1_data;

  Comparator comparator_1 (.a(counter_4_q), .b(8'h4), .gt(comparator_1_gt), .eq(comparator_1_eq), .lt(comparator_1_lt));
  Hex_Digit_Display hex_digit_display_1 (.value(counter_3_q_4));  // open: dp
  Hex_Digit_Display hex_digit_display_2 (.value(counter_3_q_3));  // open: dp
  or or_1 (or_1_out, comparator_1_gt, comparator_1_eq);
  Counter #(.max('hfff), .width(12)) counter_1 (
    .count(or_9_out), .Q(counter_1_q), .clk(clock_1_out));  // open: load, D, carry, up, clr
  Counter #(.max('hfff), .width(12)) counter_2 (
    .count(or_10_out), .Q(counter_2_q), .clk(clock_1_out));  // open: load, D, carry, up, clr
  Hex_Digit_Display hex_digit_display_3 (.value(counter_3_q_2));  // open: dp
  Hex_Digit_Display hex_digit_display_4 (.value(counter_3_q));  // open: dp
  // Probe on {counter_3_q_4, counter_3_q_3, counter_3_q_2, counter_3_q}
  Counter #(.max('hffff), .width(16)) counter_3 (
    .count(comparator_1_lt), .Q({counter_3_q_4, counter_3_q_3, counter_3_q_2, counter_3_q}), .clk(clock_1_out));  // open: load, D, carry, up, clr
  Comparator comparator_2 (.a(counter_4_q), .b(8'h8), .gt(comparator_2_gt), .eq(comparator_2_eq), .lt(comparator_2_lt));
  RAM #(.addrWidth(12), .asyncread("true"), .dataWidth(16), .\type ("nonvolatile")) ram_1 (
    .addr(counter_1_q), .oe(or_9_out), .clk(clock_1_out), .dout(ram_1_dout));  // open: we, din
  RAM #(.addrWidth(12), .asyncread("true"), .dataWidth(16), .\type ("nonvolatile")) ram_2 (
    .addr(counter_2_q), .oe(or_10_out), .clk(clock_1_out), .dout(ram_2_dout));  // open: we, din
  Hex_Digit_Display hex_digit_display_5 (.value(counter_5_q_4));  // open: dp
  or or_2 (or_2_out, comparator_2_gt, comparator_2_eq);
  Counter counter_4 (.count(rom_1_data[8]), .Q(counter_4_q), .clk(clock_1_out));  // open: load, D, carry, up, clr
  Hex_Digit_Display hex_digit_display_6 (.value(counter_5_q_3));  // open: dp
  Hex_Digit_Display hex_digit_display_7 (.value(counter_5_q_2));  // open: dp
  and and_1 (and_1_out, or_1_out, comparator_2_lt);
  RAM #(.asyncread("true"), .dataWidth(24), .\type ("nonvolatile")) ram_3 (
    .addr(counter_4_q), .oe(rom_1_data[8]), .clk(clock_1_out), .dout(ram_3_dout));  // open: we, din
  Hex_Digit_Display hex_digit_display_8 (.value(counter_6_q_4));  // open: dp
  Hex_Digit_Display hex_digit_display_9 (.value(counter_5_q));  // open: dp
  // Probe on {counter_5_q_4, counter_5_q_3, counter_5_q_2, counter_5_q}
  Counter #(.max('hffff), .width(16)) counter_5 (
    .count(and_1_out), .Q({counter_5_q_4, counter_5_q_3, counter_5_q_2, counter_5_q}), .clk(clock_1_out));  // open: load, D, carry, up, clr
  Comparator comparator_3 (.a(counter_4_q), .b(8'hc), .gt(comparator_3_gt), .eq(comparator_3_eq), .lt(comparator_3_lt));
  Hex_Digit_Display hex_digit_display_10 (.value(counter_6_q_3));  // open: dp
  Hex_Digit_Display hex_digit_display_11 (.value(counter_6_q_2));  // open: dp
  Counter #(.max('hffff), .width(16)) counter_6 (
    .count(or_4_out), .Q({counter_6_q_4, counter_6_q_3, counter_6_q_2, counter_6_q}), .clk(clock_1_out));  // open: load, D, carry, up, clr
  Hex_Digit_Display hex_digit_display_12 (.value(counter_7_q_4));  // open: dp
  and and_2 (and_2_out, or_2_out, comparator_3_lt);
  or or_3 (or_3_out, comparator_3_gt, comparator_3_eq);
  Hex_Digit_Display hex_digit_display_13 (.value(counter_6_q));  // open: dp
  // Probe on {counter_6_q_4, counter_6_q_3, counter_6_q_2, counter_6_q}
  or or_4 (or_4_out, ram_3_dout[0], ram_3_dout[1], ram_3_dout[2], ram_3_dout[3], ram_3_dout[4], ram_3_dout[5], ram_3_dout[6], ram_3_dout[7], ram_3_dout[8], ram_3_dout[9], ram_3_dout[10], ram_3_dout[11], ram_3_dout[13], ram_3_dout[14], ram_3_dout[15], ram_3_dout[16], ram_3_dout[17], ram_3_dout[18], ram_3_dout[19], ram_3_dout[20], ram_3_dout[21], ram_3_dout[22], ram_3_dout[23], ram_3_dout[12]);
  Hex_Digit_Display hex_digit_display_14 (.value(counter_7_q_3));  // open: dp
  Hex_Digit_Display hex_digit_display_15 (.value(counter_7_q_2));  // open: dp
  Counter #(.max('hffff), .width(16)) counter_7 (
    .count(and_2_out), .Q({counter_7_q_4, counter_7_q_3, counter_7_q_2, counter_7_q}), .clk(clock_1_out));  // open: load, D, carry, up, clr
  Comparator comparator_4 (
    .a(counter_4_q), .b(8'h10), .gt(comparator_4_gt), .eq(comparator_4_eq), .lt(comparator_4_lt));
  Hex_Digit_Display hex_digit_display_16 (.value(counter_7_q));  // open: dp
  Hex_Digit_Display hex_digit_display_17 (.value(counter_8_q_4));  // open: dp
  // Probe on {counter_7_q_4, counter_7_q_3, counter_7_q_2, counter_7_q}
  or or_5 (or_5_out, comparator_4_gt, comparator_4_eq);
  control_circuit control_circuit_1 (
    .a1(rom_1_data[63]), .a2(rom_1_data[62]), .a3(rom_1_data[61]), .a4(rom_1_data[60]), .a5(rom_1_data[59]),
    .a6(rom_1_data[58]), .a7(rom_1_data[57]), .a8(rom_1_data[56]), .a9(rom_1_data[55]), .a10(rom_1_data[54]),
    .a11(rom_1_data[53]), .a12(rom_1_data[52]), .a13(rom_1_data[51]), .a14(rom_1_data[50]),
    .a15(rom_1_data[49]), .a16(rom_1_data[48]), .b1(rom_1_data[47]), .b2(rom_1_data[46]),
    .b3(rom_1_data[45]), .b4(rom_1_data[44]), .b5(rom_1_data[43]), .b6(rom_1_data[42]), .b7(rom_1_data[41]),
    .b8(rom_1_data[40]), .b9(rom_1_data[39]), .b10(rom_1_data[38]), .b11(rom_1_data[37]),
    .b12(rom_1_data[36]), .b13(rom_1_data[35]), .b14(rom_1_data[34]), .b15(rom_1_data[33]),
    .b16(rom_1_data[32]), .aB1(rom_1_data[19]), .aB2(rom_1_data[18]), .aB3(rom_1_data[17]),
    .aB4(rom_1_data[16]), .bB1(rom_1_data[15]), .bB2(rom_1_data[14]), .bB3(rom_1_data[13]),
    .bB4(rom_1_data[12]), .ct(rom_1_data[10]), .Clock(clock_1_out), .R(rom_1_data[9]),
    .Dim(register_1_q[19:12]), .ct1(rom_1_data[20]), .R1(rom_1_data[8]), .ct2(rom_1_data[22]),
    .R2(rom_1_data[21]), .C1(rom_1_data[31]), .C2(rom_1_data[27]), .C3(rom_1_data[7]), .C4(rom_1_data[3]),
    .C5(rom_1_data[30]), .C6(rom_1_data[26]), .C7(rom_1_data[6]), .C8(rom_1_data[2]), .C9(rom_1_data[29]),
    .C10(rom_1_data[25]), .C11(rom_1_data[5]), .C12(rom_1_data[1]), .C13(rom_1_data[28]),
    .C14(rom_1_data[24]), .C15(rom_1_data[4]), .C16(rom_1_data[0]), .Opcode(register_1_q[23:20]),
    .DC(control_circuit_1_dc), .D(control_circuit_1_d));
  Register #(.width(24)) register_1 (
    .D(ram_3_dout), .en(rom_1_data[8]), .clk(clock_1_out), .Q(register_1_q), .clr(or_8_out));
  Hex_Digit_Display hex_digit_display_18 (.value(counter_8_q_3));  // open: dp
  Hex_Digit_Display hex_digit_display_19 (.value(counter_8_q_2));  // open: dp
  and and_3 (and_3_out, or_3_out, comparator_4_lt);
  Hex_Digit_Display hex_digit_display_20 (.value(counter_8_q));  // open: dp
  // Probe on {counter_8_q_4, counter_8_q_3, counter_8_q_2, counter_8_q}
  Counter #(.max('hffff), .width(16)) counter_8 (
    .count(and_3_out), .Q({counter_8_q_4, counter_8_q_3, counter_8_q_2, counter_8_q}), .clk(clock_1_out));  // open: load, D, carry, up, clr
  Comparator comparator_5 (
    .a(counter_4_q), .b(8'h14), .gt(comparator_5_gt), .eq(comparator_5_eq), .lt(comparator_5_lt));
  Hex_Digit_Display hex_digit_display_21 (.value(counter_10_q_4));  // open: dp
  Hex_Digit_Display hex_digit_display_22 (.value(counter_10_q_3));  // open: dp
  and and_4 (and_4_out, or_5_out, comparator_5_lt);
  or or_6 (or_6_out, comparator_5_gt, comparator_5_eq);
  Counter counter_9 (
    .load(control_circuit_1_dc), .D(control_circuit_1_d), .Q(counter_9_q), .clk(clock_1_out), .clr(or_8_out));  // open: count, carry, up
  Hex_Digit_Display hex_digit_display_23 (.value(counter_10_q_2));  // open: dp
  Hex_Digit_Display hex_digit_display_24 (.value(counter_10_q));  // open: dp
  // Probe on {counter_10_q_4, counter_10_q_3, counter_10_q_2, counter_10_q}
  Counter #(.max('hffff), .width(16)) counter_10 (
    .count(and_4_out), .Q({counter_10_q_4, counter_10_q_3, counter_10_q_2, counter_10_q}), .clk(clock_1_out));  // open: load, D, carry, up, clr
  Comparator comparator_6 (
    .a(counter_4_q), .b(8'h18), .gt(comparator_6_gt), .eq(comparator_6_eq), .lt(comparator_6_lt));
  // OR_Gate or_7 has open pins: in0=comparator_6_gt, in1=comparator_6_eq, out=open
  ROM #(.addrWidth(12), .dataWidth(64)) rom_1 (.addr({register_1_q[23:20], counter_9_q}), .data(rom_1_data));
  or or_8 (or_8_out, rom_1_data[11], control_circuit_3_1_r);
  Hex_Digit_Display hex_digit_display_25 (.value(counter_11_q_4));  // open: dp
  Hex_Digit_Display hex_digit_display_26 (.value(counter_11_q_3));  // open: dp
  and and_5 (and_5_out, or_6_out, comparator_6_lt);
  Hex_Digit_Display hex_digit_display_27 (.value(counter_11_q_2));  // open: dp
  Hex_Digit_Display hex_digit_display_28 (.value(counter_11_q));  // open: dp
  // Probe on {counter_11_q_4, counter_11_q_3, counter_11_q_2, counter_11_q}
  Counter #(.max('hffff), .width(16)) counter_11 (
    .count(and_5_out), .Q({counter_11_q_4, counter_11_q_3, counter_11_q_2, counter_11_q}), .clk(clock_1_out));  // open: load, D, carry, up, clr
  or or_9 (or_9_out, rom_1_data[48], rom_1_data[52], rom_1_data[56], rom_1_data[60], rom_1_data[49], rom_1_data[53], rom_1_data[57], rom_1_data[50], rom_1_data[61], rom_1_data[54], rom_1_data[58], rom_1_data[62], rom_1_data[51], rom_1_data[55], rom_1_data[59], rom_1_data[63]);
  or or_10 (or_10_out, rom_1_data[32], rom_1_data[33], rom_1_data[34], rom_1_data[35], rom_1_data[36], rom_1_data[37], rom_1_data[38], rom_1_data[40], rom_1_data[39], rom_1_data[41], rom_1_data[42], rom_1_data[43], rom_1_data[44], rom_1_data[45], rom_1_data[46], rom_1_data[47]);
  control_circuit_1 control_circuit_1_1 (
    .add(register_1_q[11:0]), .dim(register_1_q[19:12]), .clock(clock_1_out), .R(rom_1_data[23]),
    .Opcode(register_1_q[23:20]), .out_6(control_circuit_1_1_out_6), .D(control_circuit_1_1_d),
    .OE(control_circuit_1_1_oe), .WE(control_circuit_1_1_we), .RR(control_circuit_1_1_rr));
  control_circuit_2 control_circuit_2_1 (
    .add(register_1_q[11:0]), .dim(register_1_q[19:12]), .clock(clock_1_out), .OE(control_circuit_1_1_oe),
    .R(rom_1_data[23]), .out_6(control_circuit_2_1_out_6), .D(control_circuit_2_1_d));
  or or_11 (or_11_out, rom_1_data[63], control_circuit_1_1_oe);
  or or_12 (or_12_out, rom_1_data[47], control_circuit_1_1_oe);
  RAM #(.addrWidth(12), .asyncread("true"), .dataWidth(16)) ram_4 (
    .addr(counter_12_q), .we(rom_1_data[63]), .oe(control_circuit_1_1_oe), .clk(clock_1_out),
    .din(ram_1_dout), .dout(ram_4_dout));
  Counter #(.max('hfff), .width(12)) counter_12 (
    .load(control_circuit_1_1_out_6), .D(control_circuit_1_1_d), .count(or_11_out), .Q(counter_12_q),
    .clk(clock_1_out), .clr(in_1));  // open: carry, up
  RAM #(.addrWidth(12), .asyncread("true"), .dataWidth(16)) ram_5 (
    .addr(counter_13_q), .we(rom_1_data[59]), .oe(control_circuit_1_1_oe), .clk(clock_1_out),
    .din(ram_1_dout), .dout(ram_5_dout));
  Counter #(.max('hfff), .width(12)) counter_13 (
    .load(control_circuit_1_1_out_6), .D(control_circuit_1_1_d), .count(or_13_out), .Q(counter_13_q),
    .clk(clock_1_out), .clr(in_1));  // open: carry, up
  or or_13 (or_13_out, rom_1_data[59], control_circuit_1_1_oe);
  RAM #(.addrWidth(12), .asyncread("true"), .dataWidth(16)) ram_6 (
    .addr(counter_14_q), .we(rom_1_data[55]), .oe(control_circuit_1_1_oe), .clk(clock_1_out),
    .din(ram_1_dout), .dout(ram_6_dout));
  Counter #(.max('hfff), .width(12)) counter_14 (
    .load(control_circuit_1_1_out_6), .D(control_circuit_1_1_d), .count(or_14_out), .Q(counter_14_q),
    .clk(clock_1_out), .clr(in_1));  // open: carry, up
  or or_14 (or_14_out, rom_1_data[55], control_circuit_1_1_oe);
  RAM #(.addrWidth(12), .asyncread("true"), .dataWidth(16)) ram_7 (
    .addr(counter_15_q), .we(rom_1_data[51]), .oe(control_circuit_1_1_oe), .clk(clock_1_out),
    .din(ram_1_dout), .dout(ram_7_dout));
  Counter #(.max('hfff), .width(12)) counter_15 (
    .load(control_circuit_1_1_out_6), .D(control_circuit_1_1_d), .count(or_15_out), .Q(counter_15_q),
    .clk(clock_1_out), .clr(in_1));  // open: carry, up
  or or_15 (or_15_out, rom_1_data[51], control_circuit_1_1_oe);
  RAM #(.addrWidth(12), .asyncread("true"), .dataWidth(16)) ram_8 (
    .addr(counter_16_q), .we(rom_1_data[47]), .oe(control_circuit_1_1_oe), .clk(clock_1_out),
    .din(ram_2_dout), .dout(ram_8_dout));
  Counter #(.max('hfff), .width(12)) counter_16 (
    .load(control_circuit_2_1_out_6), .D(control_circuit_2_1_d), .count(or_12_out), .Q(counter_16_q),
    .clk(clock_1_out), .clr(in_1));  // open: carry, up
  RAM #(.addrWidth(12), .asyncread("true"), .dataWidth(16)) ram_9 (
    .addr(counter_17_q), .we(rom_1_data[46]), .oe(control_circuit_1_1_oe), .clk(clock_1_out),
    .din(ram_2_dout), .dout(ram_9_dout));
  Counter #(.max('hfff), .width(12)) counter_17 (
    .load(control_circuit_2_1_out_6), .D(control_circuit_2_1_d), .count(or_16_out), .Q(counter_17_q),
    .clk(clock_1_out), .clr(in_1));  // open: carry, up
  or or_16 (or_16_out, rom_1_data[46], control_circuit_1_1_oe);
  RAM #(.addrWidth(12), .asyncread("true"), .dataWidth(16)) ram_10 (
    .addr(counter_18_q), .we(rom_1_data[45]), .oe(control_circuit_1_1_oe), .clk(clock_1_out),
    .din(ram_2_dout), .dout(ram_10_dout));
  Counter #(.max('hfff), .width(12)) counter_18 (
    .load(control_circuit_2_1_out_6), .D(control_circuit_2_1_d), .count(or_17_out), .Q(counter_18_q),
    .clk(clock_1_out), .clr(in_1));  // open: carry, up
  or or_17 (or_17_out, rom_1_data[45], control_circuit_1_1_oe);
  RAM #(.addrWidth(12), .asyncread("true"), .dataWidth(16)) ram_11 (
    .addr(counter_19_q), .we(rom_1_data[44]), .oe(control_circuit_1_1_oe), .clk(clock_1_out),
    .din(ram_2_dout), .dout(ram_11_dout));
  Counter #(.max('hfff), .width(12)) counter_19 (
    .load(control_circuit_2_1_out_6), .D(control_circuit_2_1_d), .count(or_18_out), .Q(counter_19_q),
    .clk(clock_1_out), .clr(in_1));  // open: carry, up
  or or_18 (or_18_out, rom_1_data[44], control_circuit_1_1_oe);
  or or_19 (or_19_out, rom_1_data[62], control_circuit_1_1_oe);
  or or_20 (or_20_out, rom_1_data[43], control_circuit_1_1_oe);
  Counter #(.max('hfff), .width(12)) counter_20 (
    .load(control_circuit_1_1_out_6), .D(control_circuit_1_1_d), .count(or_19_out), .Q(counter_20_q),
    .clk(clock_1_out), .clr(in_1));  // open: carry, up
  Counter #(.max('hfff), .width(12)) counter_21 (
    .load(control_circuit_1_1_out_6), .D(control_circuit_1_1_d), .count(or_21_out), .Q(counter_21_q),
    .clk(clock_1_out), .clr(in_1));  // open: carry, up
  or or_21 (or_21_out, rom_1_data[58], control_circuit_1_1_oe);
  Counter #(.max('hfff), .width(12)) counter_22 (
    .load(control_circuit_1_1_out_6), .D(control_circuit_1_1_d), .count(or_22_out), .Q(counter_22_q),
    .clk(clock_1_out), .clr(in_1));  // open: carry, up
  or or_22 (or_22_out, rom_1_data[54], control_circuit_1_1_oe);
  Counter #(.max('hfff), .width(12)) counter_23 (
    .load(control_circuit_1_1_out_6), .D(control_circuit_1_1_d), .count(or_23_out), .Q(counter_23_q),
    .clk(clock_1_out), .clr(in_1));  // open: carry, up
  or or_23 (or_23_out, rom_1_data[50], control_circuit_1_1_oe);
  RAM #(.addrWidth(12), .asyncread("true"), .dataWidth(16)) ram_12 (
    .addr(counter_24_q), .we(rom_1_data[43]), .oe(control_circuit_1_1_oe), .clk(clock_1_out),
    .din(ram_2_dout), .dout(ram_12_dout));
  Counter #(.max('hfff), .width(12)) counter_24 (
    .load(control_circuit_2_1_out_6), .D(control_circuit_2_1_d), .count(or_20_out), .Q(counter_24_q),
    .clk(clock_1_out), .clr(in_1));  // open: carry, up
  RAM #(.addrWidth(12), .asyncread("true"), .dataWidth(16)) ram_13 (
    .addr(counter_25_q), .we(rom_1_data[42]), .oe(control_circuit_1_1_oe), .clk(clock_1_out),
    .din(ram_2_dout), .dout(ram_13_dout));
  Counter #(.max('hfff), .width(12)) counter_25 (
    .load(control_circuit_2_1_out_6), .D(control_circuit_2_1_d), .count(or_24_out), .Q(counter_25_q),
    .clk(clock_1_out), .clr(in_1));  // open: carry, up
  or or_24 (or_24_out, rom_1_data[42], control_circuit_1_1_oe);
  RAM #(.addrWidth(12), .asyncread("true"), .dataWidth(16)) ram_14 (
    .addr(counter_26_q), .we(rom_1_data[41]), .oe(control_circuit_1_1_oe), .clk(clock_1_out),
    .din(ram_2_dout), .dout(ram_14_dout));
  Counter #(.max('hfff), .width(12)) counter_26 (
    .load(control_circuit_2_1_out_6), .D(control_circuit_2_1_d), .count(or_25_out), .Q(counter_26_q),
    .clk(clock_1_out), .clr(in_1));  // open: carry, up
  or or_25 (or_25_out, rom_1_data[41], control_circuit_1_1_oe);
  RAM #(.addrWidth(12), .asyncread("true"), .dataWidth(16)) ram_15 (
    .addr(counter_27_q), .we(rom_1_data[40]), .oe(control_circuit_1_1_oe), .clk(clock_1_out),
    .din(ram_2_dout), .dout(ram_15_dout));
  Counter #(.max('hfff), .width(12)) counter_27 (
    .load(control_circuit_2_1_out_6), .D(control_circuit_2_1_d), .count(or_26_out), .Q(counter_27_q),
    .clk(clock_1_out), .clr(in_1));  // open: carry, up
  or or_26 (or_26_out, rom_1_data[40], control_circuit_1_1_oe);
  RAM #(.addrWidth(12), .asyncread("true"), .dataWidth(16)) ram_16 (
    .addr(counter_20_q), .we(rom_1_data[62]), .oe(control_circuit_1_1_oe), .clk(clock_1_out),
    .din(ram_1_dout), .dout(ram_16_dout));
  RAM #(.addrWidth(12), .asyncread("true"), .dataWidth(16)) ram_17 (
    .addr(counter_21_q), .we(rom_1_data[58]), .oe(control_circuit_1_1_oe), .clk(clock_1_out),
    .din(ram_1_dout), .dout(ram_17_dout));
  RAM #(.addrWidth(12), .asyncread("true"), .dataWidth(16)) ram_18 (
    .addr(counter_22_q), .we(rom_1_data[54]), .oe(control_circuit_1_1_oe), .clk(clock_1_out),
    .din(ram_1_dout), .dout(ram_18_dout));
  RAM #(.addrWidth(12), .asyncread("true"), .dataWidth(16)) ram_19 (
    .addr(counter_23_q), .we(rom_1_data[50]), .oe(control_circuit_1_1_oe), .clk(clock_1_out),
    .din(ram_1_dout), .dout(ram_19_dout));
  or or_27 (or_27_out, rom_1_data[61], control_circuit_1_1_oe);
  or or_28 (or_28_out, rom_1_data[39], control_circuit_1_1_oe);
  Counter #(.max('hfff), .width(12)) counter_28 (
    .load(control_circuit_1_1_out_6), .D(control_circuit_1_1_d), .count(or_27_out), .Q(counter_28_q),
    .clk(clock_1_out), .clr(in_1));  // open: carry, up
  Counter #(.max('hfff), .width(12)) counter_29 (
    .load(control_circuit_1_1_out_6), .D(control_circuit_1_1_d), .count(or_29_out), .Q(counter_29_q),
    .clk(clock_1_out), .clr(in_1));  // open: carry, up
  or or_29 (or_29_out, rom_1_data[57], control_circuit_1_1_oe);
  Counter #(.max('hfff), .width(12)) counter_30 (
    .load(control_circuit_1_1_out_6), .D(control_circuit_1_1_d), .count(or_30_out), .Q(counter_30_q),
    .clk(clock_1_out), .clr(in_1));  // open: carry, up
  or or_30 (or_30_out, rom_1_data[53], control_circuit_1_1_oe);
  Counter #(.max('hfff), .width(12)) counter_31 (
    .load(control_circuit_1_1_out_6), .D(control_circuit_1_1_d), .count(or_31_out), .Q(counter_31_q),
    .clk(clock_1_out), .clr(in_1));  // open: carry, up
  or or_31 (or_31_out, rom_1_data[49], control_circuit_1_1_oe);
  Counter #(.max('hfff), .width(12)) counter_32 (
    .load(control_circuit_2_1_out_6), .D(control_circuit_2_1_d), .count(or_28_out), .Q(counter_32_q),
    .clk(clock_1_out), .clr(in_1));  // open: carry, up
  Counter #(.max('hfff), .width(12)) counter_33 (
    .load(control_circuit_2_1_out_6), .D(control_circuit_2_1_d), .count(or_32_out), .Q(counter_33_q),
    .clk(clock_1_out), .clr(in_1));  // open: carry, up
  or or_32 (or_32_out, rom_1_data[38], control_circuit_1_1_oe);
  Counter #(.max('hfff), .width(12)) counter_34 (
    .load(control_circuit_2_1_out_6), .D(control_circuit_2_1_d), .count(or_33_out), .Q(counter_34_q),
    .clk(clock_1_out), .clr(in_1));  // open: carry, up
  or or_33 (or_33_out, rom_1_data[37], control_circuit_1_1_oe);
  Counter #(.max('hfff), .width(12)) counter_35 (
    .load(control_circuit_2_1_out_6), .D(control_circuit_2_1_d), .count(or_34_out), .Q(counter_35_q),
    .clk(clock_1_out), .clr(in_1));  // open: carry, up
  or or_34 (or_34_out, rom_1_data[36], control_circuit_1_1_oe);
  RAM #(.addrWidth(12), .asyncread("true"), .dataWidth(16)) ram_20 (
    .addr(counter_28_q), .we(rom_1_data[61]), .oe(control_circuit_1_1_oe), .clk(clock_1_out),
    .din(ram_1_dout), .dout(ram_20_dout));
  RAM #(.addrWidth(12), .asyncread("true"), .dataWidth(16)) ram_21 (
    .addr(counter_29_q), .we(rom_1_data[57]), .oe(control_circuit_1_1_oe), .clk(clock_1_out),
    .din(ram_1_dout), .dout(ram_21_dout));
  RAM #(.addrWidth(12), .asyncread("true"), .dataWidth(16)) ram_22 (
    .addr(counter_30_q), .we(rom_1_data[53]), .oe(control_circuit_1_1_oe), .clk(clock_1_out),
    .din(ram_1_dout), .dout(ram_22_dout));
  RAM #(.addrWidth(12), .asyncread("true"), .dataWidth(16)) ram_23 (
    .addr(counter_31_q), .we(rom_1_data[49]), .oe(control_circuit_1_1_oe), .clk(clock_1_out),
    .din(ram_1_dout), .dout(ram_23_dout));
  RAM #(.addrWidth(12), .asyncread("true"), .dataWidth(16)) ram_24 (
    .addr(counter_32_q), .we(rom_1_data[39]), .oe(control_circuit_1_1_oe), .clk(clock_1_out),
    .din(ram_2_dout), .dout(ram_24_dout));
  RAM #(.addrWidth(12), .asyncread("true"), .dataWidth(16)) ram_25 (
    .addr(counter_33_q), .we(rom_1_data[38]), .oe(control_circuit_1_1_oe), .clk(clock_1_out),
    .din(ram_2_dout), .dout(ram_25_dout));
  RAM #(.addrWidth(12), .asyncread("true"), .dataWidth(16)) ram_26 (
    .addr(counter_34_q), .we(rom_1_data[37]), .oe(control_circuit_1_1_oe), .clk(clock_1_out),
    .din(ram_2_dout), .dout(ram_26_dout));
  RAM #(.addrWidth(12), .asyncread("true"), .dataWidth(16)) ram_27 (
    .addr(counter_35_q), .we(rom_1_data[36]), .oe(control_circuit_1_1_oe), .clk(clock_1_out),
    .din(ram_2_dout), .dout(ram_27_dout));
  or or_35 (or_35_out, rom_1_data[60], control_circuit_1_1_oe);
  or or_36 (or_36_out, rom_1_data[35], control_circuit_1_1_oe);
  Counter #(.max('hfff), .width(12)) counter_36 (
    .load(control_circuit_1_1_out_6), .D(control_circuit_1_1_d), .count(or_35_out), .Q(counter_36_q),
    .clk(clock_1_out), .clr(in_1));  // open: carry, up
  or or_37 (or_37_out, rom_1_data[56], control_circuit_1_1_oe);
  or or_38 (or_38_out, rom_1_data[52], control_circuit_1_1_oe);
  or or_39 (or_39_out, rom_1_data[48], control_circuit_1_1_oe);
  Counter #(.max('hfff), .width(12)) counter_37 (
    .load(control_circuit_2_1_out_6), .D(control_circuit_2_1_d), .count(or_36_out), .Q(counter_37_q),
    .clk(clock_1_out), .clr(in_1));  // open: carry, up
  Counter #(.max('hfff), .width(12)) counter_38 (
    .load(control_circuit_2_1_out_6), .D(control_circuit_2_1_d), .count(or_40_out), .Q(counter_38_q),
    .clk(clock_1_out), .clr(in_1));  // open: carry, up
  or or_40 (or_40_out, rom_1_data[34], control_circuit_1_1_oe);
  Counter #(.max('hfff), .width(12)) counter_39 (
    .load(control_circuit_2_1_out_6), .D(control_circuit_2_1_d), .count(or_41_out), .Q(counter_39_q),
    .clk(clock_1_out), .clr(in_1));  // open: carry, up
  or or_41 (or_41_out, rom_1_data[33], control_circuit_1_1_oe);
  Counter #(.max('hfff), .width(12)) counter_40 (
    .load(control_circuit_2_1_out_6), .D(control_circuit_2_1_d), .count(or_42_out), .Q(counter_40_q),
    .clk(clock_1_out), .clr(in_1));  // open: carry, up
  or or_42 (or_42_out, rom_1_data[32], control_circuit_1_1_oe);
  RAM #(.addrWidth(12), .asyncread("true"), .dataWidth(16)) ram_28 (
    .addr(counter_36_q), .we(rom_1_data[60]), .oe(control_circuit_1_1_oe), .clk(clock_1_out),
    .din(ram_1_dout), .dout(ram_28_dout));
  RAM #(.addrWidth(12), .asyncread("true"), .dataWidth(16)) ram_29 (
    .addr(counter_41_q), .we(rom_1_data[56]), .oe(control_circuit_1_1_oe), .clk(clock_1_out),
    .din(ram_1_dout), .dout(ram_29_dout));
  Counter #(.max('hfff), .width(12)) counter_41 (
    .load(control_circuit_1_1_out_6), .D(control_circuit_1_1_d), .count(or_37_out), .Q(counter_41_q),
    .clk(clock_1_out), .clr(in_1));  // open: carry, up
  RAM #(.addrWidth(12), .asyncread("true"), .dataWidth(16)) ram_30 (
    .addr(counter_42_q), .we(rom_1_data[52]), .oe(control_circuit_1_1_oe), .clk(clock_1_out),
    .din(ram_1_dout), .dout(ram_30_dout));
  Counter #(.max('hfff), .width(12)) counter_42 (
    .load(control_circuit_1_1_out_6), .D(control_circuit_1_1_d), .count(or_38_out), .Q(counter_42_q),
    .clk(clock_1_out), .clr(in_1));  // open: carry, up
  RAM #(.addrWidth(12), .asyncread("true"), .dataWidth(16)) ram_31 (
    .addr(counter_43_q), .we(rom_1_data[48]), .oe(control_circuit_1_1_oe), .clk(clock_1_out),
    .din(ram_1_dout), .dout(ram_31_dout));
  Counter #(.max('hfff), .width(12)) counter_43 (
    .load(control_circuit_1_1_out_6), .D(control_circuit_1_1_d), .count(or_39_out), .Q(counter_43_q),
    .clk(clock_1_out), .clr(in_1));  // open: carry, up
  RAM #(.addrWidth(12), .asyncread("true"), .dataWidth(16)) ram_32 (
    .addr(counter_37_q), .we(rom_1_data[35]), .oe(control_circuit_1_1_oe), .clk(clock_1_out),
    .din(ram_2_dout), .dout(ram_32_dout));
  RAM #(.addrWidth(12), .asyncread("true"), .dataWidth(16)) ram_33 (
    .addr(counter_38_q), .we(rom_1_data[34]), .oe(control_circuit_1_1_oe), .clk(clock_1_out),
    .din(ram_2_dout), .dout(ram_33_dout));
  RAM #(.addrWidth(12), .asyncread("true"), .dataWidth(16)) ram_34 (
    .addr(counter_39_q), .we(rom_1_data[33]), .oe(control_circuit_1_1_oe), .clk(clock_1_out),
    .din(ram_2_dout), .dout(ram_34_dout));
  RAM #(.addrWidth(12), .asyncread("true"), .dataWidth(16)) ram_35 (
    .addr(counter_40_q), .we(rom_1_data[32]), .oe(control_circuit_1_1_oe), .clk(clock_1_out),
    .din(ram_2_dout), .dout(ram_35_dout));
  Register #(.width(16)) register_2 (
    .D(ram_4_dout), .en(control_circuit_1_1_oe), .clk(clock_1_out), .Q(register_2_q));  // open: clr
  Register #(.width(16)) register_3 (
    .D(ram_5_dout), .en(control_circuit_1_1_oe), .clk(clock_1_out), .Q(register_3_q), .clr(undriven));
  Register #(.width(16)) register_4 (
    .D(ram_6_dout), .en(control_circuit_1_1_oe), .clk(clock_1_out), .Q(register_4_q));  // open: clr
  Register #(.width(16)) register_5 (
    .D(ram_7_dout), .en(control_circuit_1_1_oe), .clk(clock_1_out), .Q(register_5_q));  // open: clr
  Register #(.width(16)) register_6 (
    .D(ram_8_dout), .en(control_circuit_1_1_oe), .clk(clock_1_out), .Q(register_6_q));  // open: clr
  Register #(.width(16)) register_7 (
    .D(ram_9_dout), .en(control_circuit_1_1_oe), .clk(clock_1_out), .Q(register_7_q), .clr(undriven_2));
  Register #(.width(16)) register_8 (
    .D(ram_10_dout), .en(control_circuit_1_1_oe), .clk(clock_1_out), .Q(register_8_q));  // open: clr
  Register #(.width(16)) register_9 (
    .D(ram_11_dout), .en(control_circuit_1_1_oe), .clk(clock_1_out), .Q(register_9_q));  // open: clr
  Clock clock_1 (.out(clock_1_out));
  Register #(.width(16)) register_10 (
    .D(ram_16_dout), .en(control_circuit_1_1_oe), .clk(clock_1_out), .Q(register_10_q));  // open: clr
  Register #(.width(16)) register_11 (
    .D(ram_17_dout), .en(control_circuit_1_1_oe), .clk(clock_1_out), .Q(register_11_q));  // open: clr
  Register #(.width(16)) register_12 (
    .D(ram_18_dout), .en(control_circuit_1_1_oe), .clk(clock_1_out), .Q(register_12_q));  // open: clr
  Register #(.width(16)) register_13 (
    .D(ram_19_dout), .en(control_circuit_1_1_oe), .clk(clock_1_out), .Q(register_13_q));  // open: clr
  Register #(.width(16)) register_14 (
    .D(ram_12_dout), .en(control_circuit_1_1_oe), .clk(clock_1_out), .Q(register_14_q));  // open: clr
  Register #(.width(16)) register_15 (
    .D(ram_13_dout), .en(control_circuit_1_1_oe), .clk(clock_1_out), .Q(register_15_q), .clr(undriven_3));
  Register #(.width(16)) register_16 (
    .D(ram_14_dout), .en(control_circuit_1_1_oe), .clk(clock_1_out), .Q(register_16_q));  // open: clr
  Register #(.width(16)) register_17 (
    .D(ram_15_dout), .en(control_circuit_1_1_oe), .clk(clock_1_out), .Q(register_17_q));  // open: clr
  Register #(.width(16)) register_18 (
    .D(ram_20_dout), .en(control_circuit_1_1_oe), .clk(clock_1_out), .Q(register_18_q));  // open: clr
  Register #(.width(16)) register_19 (
    .D(ram_21_dout), .en(control_circuit_1_1_oe), .clk(clock_1_out), .Q(register_19_q));  // open: clr
  Register #(.width(16)) register_20 (
    .D(ram_22_dout), .en(control_circuit_1_1_oe), .clk(clock_1_out), .Q(register_20_q));  // open: clr
  Register #(.width(16)) register_21 (
    .D(ram_23_dout), .en(control_circuit_1_1_oe), .clk(clock_1_out), .Q(register_21_q));  // open: clr
  Register #(.width(16)) register_22 (
    .D(ram_24_dout), .en(control_circuit_1_1_oe), .clk(clock_1_out), .Q(register_22_q));  // open: clr
  Register #(.width(16)) register_23 (
    .D(ram_25_dout), .en(control_circuit_1_1_oe), .clk(clock_1_out), .Q(register_23_q), .clr(undriven_4));
  Register #(.width(16)) register_24 (
    .D(ram_26_dout), .en(control_circuit_1_1_oe), .clk(clock_1_out), .Q(register_24_q));  // open: clr
  Register #(.width(16)) register_25 (
    .D(ram_27_dout), .en(control_circuit_1_1_oe), .clk(clock_1_out), .Q(register_25_q));  // open: clr
  Register #(.width(16)) register_26 (
    .D(ram_28_dout), .en(control_circuit_1_1_oe), .clk(clock_1_out), .Q(register_26_q));  // open: clr
  Register #(.width(16)) register_27 (
    .D(ram_29_dout), .en(control_circuit_1_1_oe), .clk(clock_1_out), .Q(register_27_q));  // open: clr
  Register #(.width(16)) register_28 (
    .D(ram_30_dout), .en(control_circuit_1_1_oe), .clk(clock_1_out), .Q(register_28_q));  // open: clr
  Register #(.width(16)) register_29 (
    .D(ram_31_dout), .en(control_circuit_1_1_oe), .clk(clock_1_out), .Q(register_29_q));  // open: clr
  Register #(.width(16)) register_30 (
    .D(ram_32_dout), .en(control_circuit_1_1_oe), .clk(clock_1_out), .Q(register_30_q));  // open: clr
  Register #(.width(16)) register_31 (
    .D(ram_33_dout), .en(control_circuit_1_1_oe), .clk(clock_1_out), .Q(register_31_q), .clr(undriven_5));
  Register #(.width(16)) register_32 (
    .D(ram_34_dout), .en(control_circuit_1_1_oe), .clk(clock_1_out), .Q(register_32_q));  // open: clr
  Register #(.width(16)) register_33 (
    .D(ram_35_dout), .en(control_circuit_1_1_oe), .clk(clock_1_out), .Q(register_33_q));  // open: clr
  Counter #(.max('hfff), .width(12)) counter_44 (
    .count(and_6_out), .Q(counter_44_q), .clk(clock_1_out), .clr(in_2));  // open: load, D, carry, up
  and and_6 (and_6_out, or_43_out, or_44_out);
  RAM #(.addrWidth(12), .dataWidth(16)) ram_36 (
    .addr(counter_44_q), .we(and_6_out), .clk(clock_1_out), .din(controlled_buffer_1_out));  // open: oe, dout
  or or_43 (or_43_out, rom_1_data[31], rom_1_data[30], rom_1_data[29], rom_1_data[28], rom_1_data[27], rom_1_data[26], rom_1_data[25], rom_1_data[24], rom_1_data[7], rom_1_data[6], rom_1_data[5], rom_1_data[4], rom_1_data[3], rom_1_data[2], rom_1_data[1], rom_1_data[0]);
  RnC_Tiling_Core rnc_tiling_core_1 (
    .a1(register_2_q), .a2(register_10_q), .a3(register_18_q), .a4(register_26_q), .a5(register_3_q),
    .a6(register_11_q), .a7(register_19_q), .a8(register_27_q), .a9(register_4_q), .a10(register_12_q),
    .a11(register_20_q), .a12(register_28_q), .a13(register_5_q), .a14(register_13_q), .a15(register_21_q),
    .a16(register_29_q), .b1(register_6_q), .b5(register_7_q), .b9(register_8_q), .b13(register_9_q),
    .b2(register_14_q), .b6(register_15_q), .b10(register_16_q), .b14(register_17_q), .b3(register_22_q),
    .b7(register_23_q), .b11(register_24_q), .b15(register_25_q), .b4(register_30_q), .b8(register_31_q),
    .b12(register_32_q), .b16(register_33_q), .s1(register_34_q), .s2(register_39_q), .s3(register_44_q),
    .s4(register_48_q), .s5(register_35_q), .s6(register_40_q), .s7(register_45_q), .s8(register_49_q),
    .s9(register_36_q), .s10(register_41_q), .s11(register_46_q), .s12(register_50_q), .s13(register_37_q),
    .s14(register_42_q), .s15(register_47_q), .s16(register_51_q), .c1(rnc_tiling_core_1_c1),
    .c2(rnc_tiling_core_1_c2), .c3(rnc_tiling_core_1_c3), .c4(rnc_tiling_core_1_c4),
    .c5(rnc_tiling_core_1_c5), .c6(rnc_tiling_core_1_c6), .c7(rnc_tiling_core_1_c7),
    .c8(rnc_tiling_core_1_c8), .c9(rnc_tiling_core_1_c9), .c10(rnc_tiling_core_1_c10),
    .c11(rnc_tiling_core_1_c11), .c12(rnc_tiling_core_1_c12), .c13(rnc_tiling_core_1_c13),
    .c14(rnc_tiling_core_1_c14), .c15(rnc_tiling_core_1_c15), .c16(rnc_tiling_core_1_c16));
  control_circuit_3 control_circuit_3_1 (
    .Add(register_1_q[11:0]), .Dim(register_1_q[19:12]), .Opcode(register_1_q[23:20]),
    .CT(control_circuit_1_1_we), .Clock(clock_1_out), .RR(rom_1_data[23]), .out_7(control_circuit_3_1_out_7),
    .D(control_circuit_3_1_d), .R(control_circuit_3_1_r));
  or or_44 (or_44_out, controlled_buffer_1_out[7], controlled_buffer_1_out[0], controlled_buffer_1_out[1], controlled_buffer_1_out[2], controlled_buffer_1_out[3], controlled_buffer_1_out[4], controlled_buffer_1_out[5], controlled_buffer_1_out[6], controlled_buffer_1_out[8], controlled_buffer_1_out[9], controlled_buffer_1_out[10], controlled_buffer_1_out[11], controlled_buffer_1_out[12], controlled_buffer_1_out[13], controlled_buffer_1_out[14], controlled_buffer_1_out[15]);
  or or_45 (or_45_out, control_circuit_1_1_we, rom_1_data[30]);
  or or_46 (or_46_out, control_circuit_1_1_we, rom_1_data[29]);
  or or_47 (or_47_out, control_circuit_1_1_we, rom_1_data[28]);
  Counter #(.max('hfff), .width(12)) counter_45 (
    .load(control_circuit_3_1_out_7), .D(control_circuit_3_1_d), .count(or_48_out), .Q(counter_45_q),
    .clk(clock_1_out));  // open: carry, up, clr
  or or_48 (or_48_out, control_circuit_1_1_we, rom_1_data[31]);
  Counter #(.max('hfff), .width(12)) counter_46 (
    .load(control_circuit_3_1_out_7), .D(control_circuit_3_1_d), .count(or_45_out), .Q(counter_46_q),
    .clk(clock_1_out));  // open: carry, up, clr
  Counter #(.max('hfff), .width(12)) counter_47 (
    .load(control_circuit_3_1_out_7), .D(control_circuit_3_1_d), .count(or_46_out), .Q(counter_47_q),
    .clk(clock_1_out));  // open: carry, up, clr
  Counter #(.max('hfff), .width(12)) counter_48 (
    .load(control_circuit_3_1_out_7), .D(control_circuit_3_1_d), .count(or_47_out), .Q(counter_48_q),
    .clk(clock_1_out));  // open: carry, up, clr
  Register #(.width(16)) register_34 (
    .D(rnc_tiling_core_1_c1), .en(control_circuit_1_1_oe), .clk(clock_1_out), .Q(register_34_q),
    .clr(control_circuit_1_1_rr));
  Register #(.width(16)) register_35 (
    .D(rnc_tiling_core_1_c5), .en(control_circuit_1_1_oe), .clk(clock_1_out), .Q(register_35_q),
    .clr(control_circuit_1_1_rr));
  Register #(.width(16)) register_36 (
    .D(rnc_tiling_core_1_c9), .en(control_circuit_1_1_oe), .clk(clock_1_out), .Q(register_36_q),
    .clr(control_circuit_1_1_rr));
  Register #(.width(16)) register_37 (
    .D(rnc_tiling_core_1_c13), .en(control_circuit_1_1_oe), .clk(clock_1_out), .Q(register_37_q),
    .clr(control_circuit_1_1_rr));
  RAM #(.addrWidth(12), .asyncread("true"), .dataWidth(16)) ram_37 (
    .addr(counter_45_q), .we(control_circuit_1_1_we), .oe(rom_1_data[31]), .clk(clock_1_out),
    .din(register_34_q), .dout(ram_37_dout));
  RAM #(.addrWidth(12), .asyncread("true"), .dataWidth(16)) ram_38 (
    .addr(counter_46_q), .we(control_circuit_1_1_we), .oe(rom_1_data[30]), .clk(clock_1_out),
    .din(register_35_q), .dout(ram_38_dout));
  RAM #(.addrWidth(12), .asyncread("true"), .dataWidth(16)) ram_39 (
    .addr(counter_47_q), .we(control_circuit_1_1_we), .oe(rom_1_data[29]), .clk(clock_1_out),
    .din(register_36_q), .dout(ram_39_dout));
  RAM #(.addrWidth(12), .asyncread("true"), .dataWidth(16)) ram_40 (
    .addr(counter_48_q), .we(control_circuit_1_1_we), .oe(rom_1_data[28]), .clk(clock_1_out),
    .din(register_37_q), .dout(ram_40_dout));
  assign controlled_buffer_1_out = rom_1_data[31] ? ram_37_dout : 16'bz;  // Controlled_Buffer controlled_buffer_1
  assign controlled_buffer_1_out = rom_1_data[30] ? ram_38_dout : 16'bz;  // Controlled_Buffer controlled_buffer_2
  assign controlled_buffer_1_out = rom_1_data[29] ? ram_39_dout : 16'bz;  // Controlled_Buffer controlled_buffer_3
  assign controlled_buffer_1_out = rom_1_data[28] ? ram_40_dout : 16'bz;  // Controlled_Buffer controlled_buffer_4
  or or_49 (or_49_out, control_circuit_1_1_we, rom_1_data[27]);
  or or_50 (or_50_out, control_circuit_1_1_we, rom_1_data[26]);
  or or_51 (or_51_out, control_circuit_1_1_we, rom_1_data[25]);
  or or_52 (or_52_out, control_circuit_1_1_we, rom_1_data[24]);
  Register #(.width(1)) register_38 (.en(undriven_6), .clk(undriven_6));  // open: D, Q, clr
  Register #(.width(16)) register_39 (
    .D(rnc_tiling_core_1_c2), .en(control_circuit_1_1_oe), .clk(clock_1_out), .Q(register_39_q),
    .clr(control_circuit_1_1_rr));
  Register #(.width(16)) register_40 (
    .D(rnc_tiling_core_1_c6), .en(control_circuit_1_1_oe), .clk(clock_1_out), .Q(register_40_q),
    .clr(control_circuit_1_1_rr));
  Register #(.width(16)) register_41 (
    .D(rnc_tiling_core_1_c10), .en(control_circuit_1_1_oe), .clk(clock_1_out), .Q(register_41_q),
    .clr(control_circuit_1_1_rr));
  Register #(.width(16)) register_42 (
    .D(rnc_tiling_core_1_c14), .en(control_circuit_1_1_oe), .clk(clock_1_out), .Q(register_42_q),
    .clr(control_circuit_1_1_rr));
  Counter #(.max('hfff), .width(12)) counter_49 (
    .load(control_circuit_3_1_out_7), .D(control_circuit_3_1_d), .count(or_49_out), .Q(counter_49_q),
    .clk(clock_1_out));  // open: carry, up, clr
  RAM #(.addrWidth(12), .asyncread("true"), .dataWidth(16)) ram_41 (
    .addr(counter_49_q), .we(control_circuit_1_1_we), .oe(rom_1_data[27]), .clk(clock_1_out),
    .din(register_39_q), .dout(ram_41_dout));
  Counter #(.max('hfff), .width(12)) counter_50 (
    .load(control_circuit_3_1_out_7), .D(control_circuit_3_1_d), .count(or_50_out), .Q(counter_50_q),
    .clk(clock_1_out));  // open: carry, up, clr
  RAM #(.addrWidth(12), .asyncread("true"), .dataWidth(16)) ram_42 (
    .addr(counter_50_q), .we(control_circuit_1_1_we), .oe(rom_1_data[26]), .clk(clock_1_out),
    .din(register_40_q), .dout(ram_42_dout));
  Counter #(.max('hfff), .width(12)) counter_51 (
    .load(control_circuit_3_1_out_7), .D(control_circuit_3_1_d), .count(or_51_out), .Q(counter_51_q),
    .clk(clock_1_out));  // open: carry, up, clr
  RAM #(.addrWidth(12), .asyncread("true"), .dataWidth(16)) ram_43 (
    .addr(counter_51_q), .we(control_circuit_1_1_we), .oe(rom_1_data[25]), .clk(clock_1_out),
    .din(register_41_q), .dout(ram_43_dout));
  Counter #(.max('hfff), .width(12)) counter_52 (
    .load(control_circuit_3_1_out_7), .D(control_circuit_3_1_d), .count(or_52_out), .Q(counter_52_q),
    .clk(clock_1_out));  // open: carry, up, clr
  RAM #(.addrWidth(12), .asyncread("true"), .dataWidth(16)) ram_44 (
    .addr(counter_52_q), .we(control_circuit_1_1_we), .oe(rom_1_data[24]), .clk(clock_1_out),
    .din(register_42_q), .dout(ram_44_dout));
  Register #(.width(1)) register_43 (.en(undriven_6), .clk(undriven_6));  // open: D, Q, clr
  assign controlled_buffer_1_out = rom_1_data[27] ? ram_41_dout : 16'bz;  // Controlled_Buffer controlled_buffer_5
  assign controlled_buffer_1_out = rom_1_data[26] ? ram_42_dout : 16'bz;  // Controlled_Buffer controlled_buffer_6
  assign controlled_buffer_1_out = rom_1_data[25] ? ram_43_dout : 16'bz;  // Controlled_Buffer controlled_buffer_7
  assign controlled_buffer_1_out = rom_1_data[24] ? ram_44_dout : 16'bz;  // Controlled_Buffer controlled_buffer_8
  or or_53 (or_53_out, control_circuit_1_1_we, rom_1_data[7]);
  or or_54 (or_54_out, control_circuit_1_1_we, rom_1_data[6]);
  or or_55 (or_55_out, control_circuit_1_1_we, rom_1_data[5]);
  or or_56 (or_56_out, control_circuit_1_1_we, rom_1_data[4]);
  Register #(.width(16)) register_44 (
    .D(rnc_tiling_core_1_c3), .en(control_circuit_1_1_oe), .clk(clock_1_out), .Q(register_44_q),
    .clr(control_circuit_1_1_rr));
  Register #(.width(16)) register_45 (
    .D(rnc_tiling_core_1_c7), .en(control_circuit_1_1_oe), .clk(clock_1_out), .Q(register_45_q),
    .clr(control_circuit_1_1_rr));
  Register #(.width(16)) register_46 (
    .D(rnc_tiling_core_1_c11), .en(control_circuit_1_1_oe), .clk(clock_1_out), .Q(register_46_q),
    .clr(control_circuit_1_1_rr));
  Register #(.width(16)) register_47 (
    .D(rnc_tiling_core_1_c15), .en(control_circuit_1_1_oe), .clk(clock_1_out), .Q(register_47_q),
    .clr(control_circuit_1_1_rr));
  Counter #(.max('hfff), .width(12)) counter_53 (
    .load(control_circuit_3_1_out_7), .D(control_circuit_3_1_d), .count(or_53_out), .Q(counter_53_q),
    .clk(clock_1_out));  // open: carry, up, clr
  RAM #(.addrWidth(12), .asyncread("true"), .dataWidth(16)) ram_45 (
    .addr(counter_53_q), .we(control_circuit_1_1_we), .oe(rom_1_data[7]), .clk(clock_1_out),
    .din(register_44_q), .dout(ram_45_dout));
  Counter #(.max('hfff), .width(12)) counter_54 (
    .load(control_circuit_3_1_out_7), .D(control_circuit_3_1_d), .count(or_54_out), .Q(counter_54_q),
    .clk(clock_1_out));  // open: carry, up, clr
  RAM #(.addrWidth(12), .asyncread("true"), .dataWidth(16)) ram_46 (
    .addr(counter_54_q), .we(control_circuit_1_1_we), .oe(rom_1_data[6]), .clk(clock_1_out),
    .din(register_45_q), .dout(ram_46_dout));
  Counter #(.max('hfff), .width(12)) counter_55 (
    .load(control_circuit_3_1_out_7), .D(control_circuit_3_1_d), .count(or_55_out), .Q(counter_55_q),
    .clk(clock_1_out));  // open: carry, up, clr
  RAM #(.addrWidth(12), .asyncread("true"), .dataWidth(16)) ram_47 (
    .addr(counter_55_q), .we(control_circuit_1_1_we), .oe(rom_1_data[5]), .clk(clock_1_out),
    .din(register_46_q), .dout(ram_47_dout));
  Counter #(.max('hfff), .width(12)) counter_56 (
    .load(control_circuit_3_1_out_7), .D(control_circuit_3_1_d), .count(or_56_out), .Q(counter_56_q),
    .clk(clock_1_out));  // open: carry, up, clr
  RAM #(.addrWidth(12), .asyncread("true"), .dataWidth(16)) ram_48 (
    .addr(counter_56_q), .we(control_circuit_1_1_we), .oe(rom_1_data[4]), .clk(clock_1_out),
    .din(register_47_q), .dout(ram_48_dout));
  assign controlled_buffer_1_out = rom_1_data[7] ? ram_45_dout : 16'bz;  // Controlled_Buffer controlled_buffer_9
  assign controlled_buffer_1_out = rom_1_data[6] ? ram_46_dout : 16'bz;  // Controlled_Buffer controlled_buffer_10
  assign controlled_buffer_1_out = rom_1_data[5] ? ram_47_dout : 16'bz;  // Controlled_Buffer controlled_buffer_11
  assign controlled_buffer_1_out = rom_1_data[4] ? ram_48_dout : 16'bz;  // Controlled_Buffer controlled_buffer_12
  or or_57 (or_57_out, control_circuit_1_1_we, rom_1_data[3]);
  or or_58 (or_58_out, control_circuit_1_1_we, rom_1_data[2]);
  or or_59 (or_59_out, control_circuit_1_1_we, rom_1_data[1]);
  or or_60 (or_60_out, control_circuit_1_1_we, rom_1_data[0]);
  Register #(.width(16)) register_48 (
    .D(rnc_tiling_core_1_c4), .en(control_circuit_1_1_oe), .clk(clock_1_out), .Q(register_48_q),
    .clr(control_circuit_1_1_rr));
  Register #(.width(16)) register_49 (
    .D(rnc_tiling_core_1_c8), .en(control_circuit_1_1_oe), .clk(clock_1_out), .Q(register_49_q),
    .clr(control_circuit_1_1_rr));
  Register #(.width(16)) register_50 (
    .D(rnc_tiling_core_1_c12), .en(control_circuit_1_1_oe), .clk(clock_1_out), .Q(register_50_q),
    .clr(control_circuit_1_1_rr));
  Register #(.width(16)) register_51 (
    .D(rnc_tiling_core_1_c16), .en(control_circuit_1_1_oe), .clk(clock_1_out), .Q(register_51_q),
    .clr(control_circuit_1_1_rr));
  Counter #(.max('hfff), .width(12)) counter_57 (
    .load(control_circuit_3_1_out_7), .D(control_circuit_3_1_d), .count(or_57_out), .Q(counter_57_q),
    .clk(clock_1_out));  // open: carry, up, clr
  RAM #(.addrWidth(12), .asyncread("true"), .dataWidth(16)) ram_49 (
    .addr(counter_57_q), .we(control_circuit_1_1_we), .oe(rom_1_data[3]), .clk(clock_1_out),
    .din(register_48_q), .dout(ram_49_dout));
  Counter #(.max('hfff), .width(12)) counter_58 (
    .load(control_circuit_3_1_out_7), .D(control_circuit_3_1_d), .count(or_58_out), .Q(counter_58_q),
    .clk(clock_1_out));  // open: carry, up, clr
  RAM #(.addrWidth(12), .asyncread("true"), .dataWidth(16)) ram_50 (
    .addr(counter_58_q), .we(control_circuit_1_1_we), .oe(rom_1_data[2]), .clk(clock_1_out),
    .din(register_49_q), .dout(ram_50_dout));
  Counter #(.max('hfff), .width(12)) counter_59 (
    .load(control_circuit_3_1_out_7), .D(control_circuit_3_1_d), .count(or_59_out), .Q(counter_59_q),
    .clk(clock_1_out));  // open: carry, up, clr
  RAM #(.addrWidth(12), .asyncread("true"), .dataWidth(16)) ram_51 (
    .addr(counter_59_q), .we(control_circuit_1_1_we), .oe(rom_1_data[1]), .clk(clock_1_out),
    .din(register_50_q), .dout(ram_51_dout));
  Counter #(.max('hfff), .width(12)) counter_60 (
    .load(control_circuit_3_1_out_7), .D(control_circuit_3_1_d), .count(or_60_out), .Q(counter_60_q),
    .clk(clock_1_out));  // open: carry, up, clr
  RAM #(.addrWidth(12), .asyncread("true"), .dataWidth(16)) ram_52 (
    .addr(counter_60_q), .we(control_circuit_1_1_we), .oe(rom_1_data[0]), .clk(clock_1_out),
    .din(register_51_q), .dout(ram_52_dout));
  assign controlled_buffer_1_out = rom_1_data[3] ? ram_49_dout : 16'bz;  // Controlled_Buffer controlled_buffer_13
  assign controlled_buffer_1_out = rom_1_data[2] ? ram_50_dout : 16'bz;  // Controlled_Buffer controlled_buffer_14
  assign controlled_buffer_1_out = rom_1_data[1] ? ram_51_dout : 16'bz;  // Controlled_Buffer controlled_buffer_15
  assign controlled_buffer_1_out = rom_1_data[0] ? ram_52_dout : 16'bz;  // Controlled_Buffer controlled_buffer_16

  // Notes on the sheet:
  //   Matric 1
  //   Matric 2
  //   Matric 3
  //   Matric 4
  //   Matric 5
  //   contents of rom_1 (hex, n*v repeats v):
  //   100 256*0 8000000000000000 4000000000000000 2000000000000400 1000000000000000 80000 200
  //   800000000000000 400000000000000 200000000000400 100000000000000 40000 200 80000000000000
  //   40000000000000 20000000000400 10000000000000 20000 200 8000000000000 4000000000000 2000000000400
  //   1000000000000 10000 200 100000 229*0 800 0 800000000000 400000000000 200000000400 100000000000 80000
  //   200 80000000000 40000000000 20000000400 10000000000 40000 200 8000000000 4000000000 2000000400
  //   1000000000 20000 200 800000000 400000000 200000400 100000000 10000 200 100000 229*0 800 0 800000
  //   255*0 800000 80000000 8000000 400080 8 8000 200000 40000000 4000000 400040 4 4000 200000 20000000
  //   2000000 400020 2 2000 200000 10000000 1000000 400010 1 1000 200000 100000 228*0 800
  //   Matric 6
endmodule
